// Logisim project cache2waylogisim.circ as structural Verilog
module main (
  input  [23:0] address,
  output hit,
  output miss,
  output [31:0] dataa
);

  wire clock_1_out;
  wire [5:0] cache_instrucciones_1_offset;
  wire [23:0] bit_extender_1_out;
  wire [29:24] undriven;
  wire [31:0] ROM_Memory_data;

  Clock clock_1 (.out(clock_1_out));
  Cache_instrucciones cache_instrucciones_1 (
    .clock(clock_1_out), .Address({undriven, address}), .Data_From_Mem(ROM_Memory_data), .hit(hit),
    .miss(miss), .data(dataa), .offset(cache_instrucciones_1_offset));
  assign bit_extender_1_out = {{18{1'b0}}, cache_instrucciones_1_offset};  // Bit_Extender bit_extender_1
  ROM #(.addrWidth(24), .dataWidth(32)) ROM_Memory (.addr(bit_extender_1_out), .data(ROM_Memory_data));
  // Pins of 24 and 30 bits meet at {undriven, address}

  // Notes on the sheet:
  //   contents of ROM_Memory (hex, n*v repeats v):
  //   32303130 30303030 d0a3230 30383030 30350d0a 32303039 30303033 d0a3230 30613030 30310d0a 32303062
  //   30303032 d0a3230 30633030 30330d0a 32303064 30303034 d0a3230 30653132 33340d0a 32303066 35363738
  //   d0a3031 30393530 32300d0a 32323130 30303031 d0a3031 30393538 32310d0a 32323130 30303031 d0a3031
  //   30393630 32320d0a 32323130 30303031 d0a3031 30393638 32330d0a 32323130 30303031 d0a3031 30393730
  //   32340d0a 32323130 30303031 d0a3031 30393738 32350d0a 32323130 30303031 d0a3031 30396330 32360d0a
  //   32323130 30303031 d0a3031 30396338 32370d0a 32323130 30303031 d0a3031 32383438 32610d0a 32323130
  //   30303031 d0a3031 30393530 32620d0a 32323130 30303031 d0a3030 30383538 38300d0a 32323130 30303031
  //   d0a3030 30383630 38320d0a 32323130 30303031 d0a3030 30383638 38330d0a 32323130 30303031 d0a3031
  //   32383730 30340d0a 32323130 30303031 d0a3031 32383738 30360d0a 32323130 30303031 d0a3031 32386330
  //   30370d0a 32323130 30303031 d0a3031 30393030 31380d0a 30303030 35303130 d0a3030 30303538 31320d0a
  //   32323130 30303031 d0a3031 30623030 31390d0a 30303030 35303130 d0a3030 30303538 31320d0a 32323130
  //   30303031 d0a3031 30393030 31610d0a 30303030 36303130 d0a3030 30303638 31320d0a 32323130 30303031
  //   d0a3031 30623030 31620d0a 30303030 36303130 d0a3030 30303638 31320d0a 32323130 30303031 d0a3232
  //   31303030 30310d0a 32313065 30303061 d0a3232 31303030 30310d0a 32353266 30303134 d0a3232 31303030
  //   30310d0a 32393138 30303038 d0a3232 31303030 30310d0a 32643339 30303034 d0a3232 31303030 30310d0a
  //   33313061 30303066 d0a3232 31303030 30310d0a 33353262 30303061 d0a3232 31303030 30310d0a 33393063
  //   30303037 d0a3232 31303030 30310d0a 33633064 31323334 d0a3232 31303030 30310d0a 30313039 30303138
  //   d0a3030 30303530 31300d0a 32323130 30303031 d0a3031 30303030 31310d0a 32323130 30303031 d0a3030
  //   30303538 31320d0a 32323130 30303031 d0a3031 32303030 31330d0a 32323130 30303031 d0a6133 61613030
  //   30300d0a 38336165 30303030 d0a3232 31303030 30310d0a 61336161 30303030 d0a3933 62393030 30300d0a
  //   32323130 30303031 d0a6137 61653030 30300d0a 38376166 30303030 d0a3232 31303030 30310d0a 61376165
  //   30303030 d0a3937 61383030 30300d0a 32323130 30303031 d0a6166 61383030 30300d0a 38666238 30303030
  //   d0a3232 31303030 30310d0a 61336139 30303030 d0a3232 31303030 30310d0a 61376161 30303030 d0a3232
  //   31303030 30310d0a 61666162 30303030 d0a3232 31303030 30310d0a 31313038 30303031 d0a3030 30303030
  //   30300d0a 32323130 30303031 d0a3135 30393030 30310d0a 30303030 30303030 d0a3232 31303030 30310d0a
  //   31393030 30303031 d0a3030 30303030 30300d0a 32323130 30303031 d0a3164 30303030 30310d0a 30303030
  //   30303030 d0a3232 31303030 30310d0a 32323130 30303031 d0a3038 31303030 37360d0a 32323130 30303031
  //   d0a3063 31303030 37620d0a 32323130 30303031 d0a3232 31303030 30310d0a 30383130 30303761 d0a3031
  //   30393130 32300d0a 32323130 30303031 d0a3033 65303030 30380d0a
endmodule

// VHDL entity cache, as the project stores it:
library IEEE;
use IEEE.STD_LOGIC_1164.ALL;
use IEEE.STD_LOGIC_ARITH.ALL;
use IEEE.STD_LOGIC_UNSIGNED.ALL;

entity cache is
    Port (
        clk : in std_logic;
        reset : in std_logic;
        address : in std_logic_vector(31 downto 0);
        write_data : in std_logic_vector(31 downto 0);
        write_enable : in std_logic;
        read_data : out std_logic_vector(31 downto 0);
        hit : out std_logic
    );
end cache;

architecture Behavioral of cache is
    -- Cache parameters
    constant CACHE_SIZE : integer := 256;  -- Number of sets
    constant ASSOCIATIVITY : integer := 2; -- 2-way associative

    -- Type declarations
    type cache_line is record
        valid : std_logic;
        tag : std_logic_vector(23 downto 0);
        data : std_logic_vector(31 downto 0);
    end record;

    type cache_set is array (0 to ASSOCIATIVITY-1) of cache_line;
    type cache_array is array (0 to CACHE_SIZE-1) of cache_set;

    -- Cache memory
    signal cache : cache_array := (others => (others => (valid => '0', tag => (others => '0'), data => (others => '0'))));

    -- Internal signals
    signal index : integer range 0 to CACHE_SIZE-1;
    signal tag : std_logic_vector(23 downto 0);
    signal offset : std_logic_vector(1 downto 0);
    signal hit_way : integer range 0 to ASSOCIATIVITY-1;
    signal found : std_logic;
    signal way : integer range 0 to ASSOCIATIVITY-1;

begin
    process(clk, reset)
    begin
        if reset = '1' then
            for i in 0 to CACHE_SIZE-1 loop
                for j in 0 to ASSOCIATIVITY-1 loop
                    cache(i)(j).valid <= '0';
                    cache(i)(j).tag <= (others => '0');
                    cache(i)(j).data <= (others => '0');
                end loop;
            end loop;
            read_data <= (others => '0');
            hit <= '0';

        elsif rising_edge(clk) then
            -- Extract index, tag, and offset from address
            index <= conv_integer(address(31 downto 24));   -- 8-bit index
            tag <= address(23 downto 0);			     -- 24-bit index
            offset <= address(1 downto 0);				-- 2-bit offset
            
            -- Check for cache hit
            found <= '0';
           if cache(index)(way).valid = '1' and cache(index)(way).tag = tag then
               found <= '1';
               hit_way <= way;
           end if;

            if found = '1' then
                -- Cache hit
                hit <= '1';
                read_data <= cache(index)(hit_way).data;
                if write_enable = '1' then
                    cache(index)(hit_way).data <= write_data;
                end if;
            else
                -- Cache miss
                hit <= '0';
                read_data <= (others => '0');
                -- Write operation (if enabled)
                if write_enable = '1' then
                    cache(index)(0).valid <= '1';  -- Simple policy: replace way 0
                    cache(index)(0).tag <= tag;
                    cache(index)(0).data <= write_data;
                end if;
            end if;
        end if;
    end process;
end Behavioral;

// VHDL entity classCache, as the project stores it:
--------------------------------------------------------------------------------
-- Description :
-- Cache for pipelined MIPS processor. 
-- 2 way associative.
-- 32 bit addresses and 32 bit data output. 
-- Address is divided this way: 
--  tag is of 10 bits, index is of 8 bits and offset is 5 bits. 
--------------------------------------------------------------------------------

LIBRARY ieee;
USE ieee.std_logic_1164.all;

USE ieee.numeric_std.all;  

ENTITY classCache IS
  PORT (
  ------------------------------------------------------------------------------
  --Insert input ports below
    clock      : IN  std_logic;           
    Address: IN std_logic_vector(31 DOWNTO 0);

  ------------------------------------------------------------------------------
	hit : OUT std_logic; 
	data_out: OUT std_logic_vector(31 DOWNTO 0);
		tag_out : OUT std_logic_vector (10 DOWNTO 0); 
		index_out : OUT std_logic_vector (8 DOWNTO 0); 
		offset_out :OUT std_logic_vector (5 DOWNTO 0);
	miss_out: OUT std_logic
    );
END classCache;

--------------------------------------------------------------------------------
--Complete your VHDL description below
--------------------------------------------------------------------------------

ARCHITECTURE TypeArchitecture OF classCache IS

type bloque is array(0 to 63) of std_logic_vector(10 downto 0);
type t_set is array(0 to 255) of bloque;
signal cache0 : t_set;
signal cache1 : t_set; 

type t_tag is array(0 to 255) of std_logic_vector(10 downto 0);

type t_valid is array(0 to 255) of std_logic;

type t_Dirty is array(0 to 255) of std_logic;



signal s_tag : std_logic_vector(10 downto 0);
signal s_index :std_logic_vector (8 DOWNTO 0); 
signal s_offset : std_logic_vector (5 DOWNTO 0); 

signal data: std_logic_vector(31 DOWNTO 0); 
signal hit_addr : std_logic;


type t_Memory is array (0 to 31) of std_logic_vector(31 downto 0);
signal mainmem : t_Memory:= ("00000000000000000000000000000001",others =>"00000000000000000000000000100000");

signal dirtys0 : t_Dirty;
signal valids0 : t_valid:= ('1', '0','0','0', others => '0');
signal tags0 : t_tag:=( others => "00000000000");

signal dirtys1 : t_Dirty;
signal valids1 : t_valid:= ('1', '0','0','0', others => '0');
signal tags1 : t_tag:=( others => "00000000000");

signal miss : std_logic; 

BEGIN

process (clock)
	begin
	if clock = '1' then
		s_tag <= Address(25 DOWNTO 15); 
		s_index <= Address(14  DOWNTO 6); 
		s_offset <= Address(5  DOWNTO 0); 
		hit_addr <= '0'; 
		if valids0(to_integer(unsigned(s_index))) = '1' or valids1(to_integer(unsigned(s_index))) = '1' then 
			if s_tag = tags0(to_integer(unsigned(s_index))) or s_tag = tags1(to_integer(unsigned(s_index))) then 
				data <= mainmem(to_integer(unsigned(s_offset))); 
				hit_addr <= '1'; 
				miss <= '0';
			end if; 
		else 
			hit_addr <= '0'; 
			if s_tag(0) = '0' then
				cache0(to_integer(unsigned(s_index)))(to_integer(unsigned(s_index))) <= s_tag;
				dirtys0(to_integer(unsigned(s_index))) <= '1'; 
				valids0(to_integer(unsigned(s_index))) <= '1';
				tags0(to_integer(unsigned(s_index))) <= s_tag;
			else
				cache1(to_integer(unsigned(s_index)))(to_integer(unsigned(s_index))) <= s_tag;
				dirtys1(to_integer(unsigned(s_index))) <= '1'; 
				valids1(to_integer(unsigned(s_index))) <= '1';
				tags1(to_integer(unsigned(s_index))) <= s_tag;
			end if; 
			miss <= '1'; 
			hit_addr <= '0'; 
			
		end if; 
		
	end if; 
end process;

	tag_out <= s_tag; 
	index_out <= s_index;
	offset_out <= s_offset;
	hit <= hit_addr; 
	data_out <= data;
	miss_out <= miss; 

END TypeArchitecture;

// VHDL entity cacheLRU, as the project stores it:
--------------------------------------------------------------------------------
-- Description :
-- Cache for pipelined MIPS processor. 
-- 2 way associative.
-- 32 bit addresses and 32 bit data output. 
-- Address is divided this way: 
--  tag is of 17 bits, index is of 8 bits and offset is 5 bits. 
--------------------------------------------------------------------------------

LIBRARY ieee;
USE ieee.std_logic_1164.all;

USE ieee.numeric_std.all;  

ENTITY cacheLRU IS
  PORT (
  ------------------------------------------------------------------------------
  -- Input ports
    clock      : IN  std_logic;           
    Address: IN std_logic_vector(31 DOWNTO 0);

  ------------------------------------------------------------------------------
  -- Output ports
	hit : OUT std_logic; 
	data_out: OUT std_logic_vector(31 DOWNTO 0);
		tag_out : OUT std_logic_vector (20 DOWNTO 0); 
		index_out : OUT std_logic_vector (4 DOWNTO 0); 
		offset_out :OUT std_logic_vector (5 DOWNTO 0);
	miss_out: OUT std_logic;
	set_0: OUT std_logic; 
	set_1: OUT std_logic
    );
END cacheLRU;

--------------------------------------------------------------------------------
-- Architecture of the cacheLRU entity
--------------------------------------------------------------------------------

ARCHITECTURE TypeArchitecture OF cacheLRU IS

-- Cache block definition: array of 64 blocks of 20-bit words
type bloque is array(0 to 63) of std_logic_vector(20 downto 0);

-- Cache set definition: array of 256 cache blocks
type t_set is array(0 to 255) of bloque;

-- Two sets for the 2-way associative cache
signal cache0 : t_set;
signal cache1 : t_set; 

-- Tag, valid, dirty, and LRU signal definitions
type t_tag is array(0 to 255) of std_logic_vector(20 downto 0);
type t_valid is array(0 to 255) of std_logic;
type t_Dirty is array(0 to 255) of std_logic;
type t_LRU is array(0 to 255) of std_logic; 

-- Internal signals for tag, index, offset, and data
signal s_tag : std_logic_vector(20 downto 0);
signal s_index :std_logic_vector (4 DOWNTO 0); 
signal s_offset : std_logic_vector (5 DOWNTO 0); 
signal data: std_logic_vector(31 DOWNTO 0); 
signal hit_addr : std_logic;

-- Main memory definition: array of 32 words of 32 bits
type t_Memory is array (0 to 31) of std_logic_vector(31 downto 0);
signal mainmem : t_Memory:= ("00000000000000000000000000000001",others =>"00000000000000000000000000100000");

-- Signals for dirty, valid, tag, and LRU bits for both cache sets
signal dirtys0 : t_Dirty:= ( others => '0');
signal valids0 : t_valid:= ( others => '0');
signal tags0 : t_tag:=( others => "000000000000000000000");
signal lru0: t_LRU:=(others => '0'); 

signal dirtys1 : t_Dirty:= ( others => '0');
signal valids1 : t_valid:= (others => '0');
signal tags1 : t_tag:=( others => "000000000000000000000");
signal lru1: t_LRU:=(others => '1'); 

-- Signal for miss logic
signal miss : std_logic; 

signal set_0_out: std_logic;
signal set_1_out : std_logic; 



BEGIN
-- Process that handles the cache behavior on clock edge
process (clock)
	begin
	if clock = '1' then
	-- Extracting tag, index, and offset from the address when clock is in its positive state 
		s_tag <= Address(31 DOWNTO 11); 
		s_index <= Address(10  DOWNTO 6); 
		s_offset <= Address(5  DOWNTO 0); 
		-- Default values for hit and miss signals 
		hit_addr <= '0'; 
		miss <= '1'; 

		-- Check if the address is in the cache (this is when valid bit and tag match) 
		if valids0(to_integer(unsigned(s_index))) = '1' or valids1(to_integer(unsigned(s_index))) = '1' then 
			if s_tag = tags0(to_integer(unsigned(s_index))) or s_tag = tags1(to_integer(unsigned(s_index))) then 
				-- If found, read data from main memory
				data <= mainmem(to_integer(unsigned(s_offset))); 
				hit_addr <= '1'; 
				miss <= '0';
			end if; 
		end if; 
		-- Determine which set to used based on LRU bit. Check if the tag is not stored already in the cache 
		if lru0(to_integer(unsigned(s_index))) = '0'and tags1(to_integer(unsigned(s_index))) /= s_tag  then 

				-- Use set 0 
				valids0(to_integer(unsigned(s_index))) <= '1';
				
				-- Actual lru_0 bit changes to '1' and the other lru_1 bit changes to '0' in the index from address.  
				lru0(to_integer(unsigned(s_index))) <= '1'; 
				lru1(to_integer(unsigned(s_index))) <= '0';
				
				-- Save tag in cache0
				cache0(to_integer(unsigned(s_index)))(to_integer(unsigned(s_offset))) <= s_tag;

				-- Add the tag to tags0 
				tags0(to_integer(unsigned(s_index))) <= s_tag;

		
				set_1_out <= '0'; 
				set_0_out <= '1';
		elsif lru1(to_integer(unsigned(s_index))) = '0' and tags0(to_integer(unsigned(s_index))) /= s_tag then 
				-- Use set 1 
				valids1(to_integer(unsigned(s_index))) <= '1';
				
				-- Actual lru_1 bit changes to '1' and the other lru_0 bit changes to '0' in the index from address.  
				lru1(to_integer(unsigned(s_index))) <= '1'; 
				lru0(to_integer(unsigned(s_index))) <= '0'; 
				-- Save tag in cache1
				cache1(to_integer(unsigned(s_index)))(to_integer(unsigned(s_offset))) <= s_tag;

				-- Add the tag to tags1
				tags1(to_integer(unsigned(s_index))) <= s_tag;


				set_1_out <= '1'; 
				set_0_out <= '0'; 
		end if;
	end if; 
end process;

	-- Assign internal signals to output ports 
	tag_out <= s_tag; 
	index_out <= s_index;
	offset_out <= s_offset;
	hit <= hit_addr; 
	data_out <= data;
	miss_out <= miss; 
	set_0 <= set_0_out; 
	set_1 <= set_1_out;

END TypeArchitecture;

// VHDL entity cacheMips, as the project stores it:
--------------------------------------------------------------------------------
-- Description :
-- Cache for pipelined MIPS processor. 
-- 2 way associative.
-- 32 bit addresses and 32 bit data output. 
-- Address is divided this way: 
--  tag is of 17 bits, index is of 8 bits and offset is 5 bits. 
--------------------------------------------------------------------------------

LIBRARY ieee;
USE ieee.std_logic_1164.all;

USE ieee.numeric_std.all;  

ENTITY cacheMips IS
  PORT (
  ------------------------------------------------------------------------------
  -- Input ports
    clock      : IN  std_logic;           
    Address: IN std_logic_vector(31 DOWNTO 0);
    Data_From_Mem: IN std_logic_vector(31 DOWNTO 0); 
    write_cache: IN std_logic; 
    entrada_dato: IN std_logic_vector(31 DOWNTO 0); 

  ------------------------------------------------------------------------------
  -- Output ports
	hit : OUT std_logic; 
	data: OUT std_logic_vector(31 DOWNTO 0);
	miss: OUT std_logic; 
	offset: OUT std_logic_vector(5 DOWNTO 0);
	dirty: OUT std_logic; 
	data_to_mem: OUT std_logic_vector(31 DOWNTO 0)
    );
END cacheMips;

--------------------------------------------------------------------------------
-- Architecture of the cacheLRU entity
--------------------------------------------------------------------------------

ARCHITECTURE TypeArchitecture OF cacheMips IS

-- Cache block definition: array of 64 blocks of 20-bit words
type bloque is array(0 to 63) of std_logic_vector(20 downto 0);

-- Cache set definition: array of 256 cache blocks
type t_set is array(0 to 255) of bloque;

-- Two sets for the 2-way associative cache
signal cache0 : t_set;
signal cache1 : t_set; 

-- Tag, valid, dirty, and LRU signal definitions
type t_tag is array(0 to 255) of std_logic_vector(20 downto 0);
type t_valid is array(0 to 255) of std_logic;
type t_Dirty is array(0 to 255) of std_logic;
type t_LRU is array(0 to 255) of std_logic; 

-- Internal signals for tag, index, offset, and data
signal s_tag : std_logic_vector(20 downto 0);
signal s_index :std_logic_vector (4 DOWNTO 0); 
signal s_offset : std_logic_vector (5 DOWNTO 0); 
signal data_out: std_logic_vector(31 DOWNTO 0); 
signal hit_addr : std_logic;

-- Main memory definition: array of 32 words of 32 bits
type t_Memory is array (0 to 31) of std_logic_vector(31 downto 0);
signal mainmem : t_Memory:= ("00000000000000000000000000000001",others =>"00000000000000000000000000100000");

-- Signals for dirty, valid, tag, and LRU bits for both cache sets
signal dirtys0 : t_Dirty:= ( others => '0');
signal valids0 : t_valid:= ( others => '0');
signal tags0 : t_tag:=( others => "000000000000000000000");
signal lru0: t_LRU:=(others => '0'); 

signal dirtys1 : t_Dirty:= ( others => '0');
signal valids1 : t_valid:= (others => '0');
signal tags1 : t_tag:=( others => "000000000000000000000");
signal lru1: t_LRU:=(others => '1'); 

-- Signal for miss logic
signal miss_out : std_logic; 

signal set_0_out: std_logic;
signal set_1_out : std_logic; 



BEGIN
-- Process that handles the cache behavior on clock edge
process (clock)
	begin
	if clock = '1' then
	-- Extracting tag, index, and offset from the address when clock is in its positive state 
		s_tag <= Address(31 DOWNTO 11); 
		s_index <= Address(10  DOWNTO 6); 
		s_offset <= Address(5  DOWNTO 0); 
		-- Default values for hit and miss signals 
		hit_addr <= '0'; 
		miss_out <= '1'; 

		-- Check if the address is in the cache (this is when valid bit and tag match) 
		if valids0(to_integer(unsigned(s_index))) = '1' or valids1(to_integer(unsigned(s_index))) = '1' then 
			if s_tag = tags0(to_integer(unsigned(s_index))) or s_tag = tags1(to_integer(unsigned(s_index))) then 
				-- If found, read data from main memory
				data_out <= Data_From_Mem;
				hit_addr <= '1'; 
				miss_out <= '0';
			end if; 
		end if; 
		-- Determine which set to used based on LRU bit. Check if the tag is not stored already in the cache 
		if lru0(to_integer(unsigned(s_index))) = '0'and tags1(to_integer(unsigned(s_index))) /= s_tag  then 

				-- Use set 0 
				valids0(to_integer(unsigned(s_index))) <= '1';
				
				-- Actual lru_0 bit changes to '1' and the other lru_1 bit changes to '0' in the index from address.  
				lru0(to_integer(unsigned(s_index))) <= '1'; 
				lru1(to_integer(unsigned(s_index))) <= '0';
				
				-- Save tag in cache0
				cache0(to_integer(unsigned(s_index)))(to_integer(unsigned(s_offset))) <= s_tag;

				-- Add the tag to tags0 
				tags0(to_integer(unsigned(s_index))) <= s_tag;

				if write_cache = '1' then 
					dirtys0(to_integer(unsigned(s_index))) <= '1';
				end if; 
				
		elsif lru1(to_integer(unsigned(s_index))) = '0' and tags0(to_integer(unsigned(s_index))) /= s_tag then 
				-- Use set 1 
				valids1(to_integer(unsigned(s_index))) <= '1';
				
				-- Actual lru_1 bit changes to '1' and the other lru_0 bit changes to '0' in the index from address.  
				lru1(to_integer(unsigned(s_index))) <= '1'; 
				lru0(to_integer(unsigned(s_index))) <= '0'; 
				-- Save tag in cache1
				cache1(to_integer(unsigned(s_index)))(to_integer(unsigned(s_offset))) <= s_tag;

				-- Add the tag to tags1
				tags1(to_integer(unsigned(s_index))) <= s_tag;
				if write_cache = '1' then 
					dirtys1(to_integer(unsigned(s_index))) <= '1';
				end if; 
		end if;
	end if; 
end process;

	-- Assign internal signals to output ports 

	hit <= hit_addr; 
	data <= data_out;
	miss <= miss_out; 
	offset <= s_offset;
	dirty <= write_cache;
	data_to_mem <= entrada_dato;
END TypeArchitecture;

// VHDL entity ROM_MIPS, as the project stores it:
--------------------------------------------------------------------------------
-- Project :
-- File    :
-- Autor   :
-- Date    :
--
--------------------------------------------------------------------------------
-- Description :
--
--------------------------------------------------------------------------------
LIBRARY ieee;
USE ieee.std_logic_1164.all;

USE ieee.numeric_std.all;  

ENTITY ROM_MIPS IS
  PORT (
  ------------------------------------------------------------------------------

    clock      : IN  std_logic;                    
    MIPS_Indice_Instruccion        : IN  std_logic_vector(31 DOWNTO 0); 
    Usar_Little_Endian: IN std_logic; 
    
  ------------------------------------------------------------------------------

    byte        : OUT std_logic_vector(31 DOWNTO 0);               
    nibble        : OUT std_logic_vector(30 DOWNTO 0);
    word: OUT  std_logic_vector(29 DOWNTO 0);
    ROM_WORD: OUT std_logic_vector(31 DOWNTO 0) 
    );
END ROM_MIPS;
--------------------------------------------------------------------

ARCHITECTURE TypeArchitecture OF ROM_MIPS IS

type t_Memory is array (0 to 64) of std_logic_vector(31 downto 0);

signal byte_out        :  std_logic_vector(31 DOWNTO 0);               
signal nibble_out        :  std_logic_vector(30 DOWNTO 0);
signal word_out:   std_logic_vector(29 DOWNTO 0);

signal ROM: t_Memory:=(x"a2d3a1e0",x"1ad3f349",others =>x"00000000") ; 
signal rom_word_out : std_logic_vector(31 DOWNTO 0);


BEGIN
-- Process that handles the cache behavior on clock edge
process (clock)
	begin
	if clock = '1' then
		byte_out <= MIPS_Indice_Instruccion; 
		nibble_out <= MIPS_Indice_Instruccion(31 DOWNTO 1); 
		word_out <= MIPS_Indice_Instruccion(31 DOWNTO 2);  

		rom_word_out <= ROM(to_integer(unsigned(word_out))); 
	end if; 
end process;

byte <= byte_out; 
nibble <= nibble_out; 
word <= word_out; 
ROM_WORD <= rom_word_out;

END TypeArchitecture;

// VHDL entity RAM_Module, as the project stores it:
--------------------------------------------------------------------------------
-- Project :
-- File    :
-- Autor   :
-- Date    :
--
--------------------------------------------------------------------------------
-- Description :
--
--------------------------------------------------------------------------------

LIBRARY ieee;
USE ieee.std_logic_1164.all;

USE ieee.numeric_std.all;

ENTITY RAM_Module IS
  PORT (
  ------------------------------------------------------------------------------
  --Insert input ports below
	clock: IN std_logic;
 
    read: IN std_logic; 
    offset: IN std_logic_vector(5 DOWNTO 0);
    write : IN std_logic;
    	data_to_write: IN std_logic_vector(31 DOWNTO 0); 
  ------------------------------------------------------------------------------
  --Insert output ports below
    data        : OUT std_logic_vector(31 DOWNTO 0);  
    data_show : OUT std_logic_vector(31 DOWNTO 0)-- output bit example
    );
END RAM_Module;

--------------------------------------------------------------------------------
--Complete your VHDL description below
--------------------------------------------------------------------------------

ARCHITECTURE TypeArchitecture OF RAM_Module IS

-- Main memory definition: array of 32 words of 32 bits
type t_Memory is array (0 to 63) of std_logic_vector(31 downto 0);
signal mainmem : t_Memory:= (x"12345678",x"1241a393",others=>x"aaaabbbb");


BEGIN
process (clock)
begin
	if clock = '1' then
		if read = '1' then
			data <= mainmem(to_integer(unsigned(offset))); 
		end if;
		if write = '1' then 
			mainmem(to_integer(unsigned(offset))) <= data_to_write; 
		end if;
	end if;  
end process; 
data_show <= mainmem(to_integer(unsigned(offset)));
END TypeArchitecture;

// VHDL entity Cache_instrucciones, as the project stores it:
--------------------------------------------------------------------------------
-- Project :
-- File    :
-- Autor   :
-- Date    :
--
--------------------------------------------------------------------------------
-- Description :
--
 --128KB 
-- Address are size 30
--------------------------------------------------------------------------------

LIBRARY ieee;
USE ieee.std_logic_1164.all;

USE ieee.numeric_std.all;  


ENTITY Cache_instrucciones IS
  PORT (
  ------------------------------------------------------------------------------
  --Insert input ports below
 	clock      : IN  std_logic;           
	Address: IN std_logic_vector(29 DOWNTO 0);
  	Data_From_Mem: IN std_logic_vector(31 DOWNTO 0); 
  ------------------------------------------------------------------------------
	hit : OUT std_logic; 
	miss: OUT std_logic; 
	data: OUT std_logic_vector(31 DOWNTO 0);
	offset: OUT std_logic_vector(5 DOWNTO 0)
    );
END Cache_instrucciones;


ARCHITECTURE TypeArchitecture OF Cache_instrucciones IS
-- Cache block definition: array of 2048 blocks of 32 bit words
type t_bloque is array(0 to 63) of std_logic_vector(31 downto 0);
type t_set is array(0 to 2048) of t_bloque;

signal cache0 : t_set;
type t_tag is array(0 to 2048) of std_logic_vector(12 downto 0);
type t_valid is array(0 to 2048) of std_logic;

signal valids0 : t_valid:= ( others => '0');
signal tags0 : t_tag:=( others => "00000000000");

signal s_tag : std_logic_vector(29 DOWNTO 17);
signal s_index :std_logic_vector (16 DOWNTO 6); 
signal s_offset : std_logic_vector (5 DOWNTO 0); 

-- Signal for miss and hit logic
signal miss_out : std_logic; 
signal hit_addr : std_logic;

signal data_out: std_logic_vector(31 DOWNTO 0); 

BEGIN
-- Process that handles the cache behavior on clock edge
process (clock)
	begin
	if clock = '1' then
		-- Extracting tag, index, and offset from the address when clock is in its positive state 
		s_tag    <= Address(29 DOWNTO 17); 
		s_index  <= Address(16 DOWNTO 6); 
		s_offset <= Address(5 DOWNTO 0); 
		-- Default values for hit and miss signals 
		hit_addr <= '0'; 
		miss_out <= '1'; 
		data_out <= x"00000000"; 
		if valids0(to_integer(unsigned(s_index))) = '1' then 
			if s_tag = tags0(to_integer(unsigned(s_index))) then 
				-- If found, read data from cache memory
				data_out <= cache0(to_integer(unsigned(s_index)))(to_integer(unsigned(s_offset)));
				hit_addr <= '1'; 
				miss_out <= '0';
			end if; 
		else
			
		 	hit_addr <= '0'; 
			miss_out <= '1';
			-- Miss, store data to cache 
			valids0(to_integer(unsigned(s_index))) <= '1';
			-- Save data in cache0
			cache0(to_integer(unsigned(s_index)))(to_integer(unsigned(s_offset))) <= Data_From_Mem;
			data_out <= x"aaaabbbb";
			-- Add the tag to tags0 
			tags0(to_integer(unsigned(s_index))) <= s_tag;	
		end if; 
	end if; 

end process;
hit <= hit_addr; 
miss <= miss_out; 
offset <= s_offset;
data <= data_out; 

END TypeArchitecture;

// VHDL entity Cache_datos, as the project stores it:
--------------------------------------------------------------------------------
-- Description :
-- Cache for pipelined MIPS processor. 
-- 2 way associative.
-- 32 bit addresses and 32 bit data output. 
-- Address is divided this way: 
--  tag is of 17 bits, index is of 8 bits and offset is 5 bits. 
--------------------------------------------------------------------------------

LIBRARY ieee;
USE ieee.std_logic_1164.all;

USE ieee.numeric_std.all;  

ENTITY Cache_datos IS
  PORT (
  ------------------------------------------------------------------------------
  -- Input ports
    clock      : IN  std_logic;           
    Address: IN std_logic_vector(31 DOWNTO 0);

  ------------------------------------------------------------------------------
  -- Output ports
	MIPS_Entrada
    );
END Cache_datos;

--------------------------------------------------------------------------------
-- Architecture of the cacheLRU entity
--------------------------------------------------------------------------------

ARCHITECTURE TypeArchitecture OF Cache_datos IS

-- Cache block definition: array of 64 blocks of 20-bit words
type bloque is array(0 to 63) of std_logic_vector(20 downto 0);

-- Cache set definition: array of 256 cache blocks
type t_set is array(0 to 255) of bloque;

-- Two sets for the 2-way associative cache
signal cache0 : t_set;
signal cache1 : t_set; 

-- Tag, valid, dirty, and LRU signal definitions
type t_tag is array(0 to 255) of std_logic_vector(20 downto 0);
type t_valid is array(0 to 255) of std_logic;
type t_Dirty is array(0 to 255) of std_logic;
type t_LRU is array(0 to 255) of std_logic; 

-- Internal signals for tag, index, offset, and data
signal s_tag : std_logic_vector(20 downto 0);
signal s_index :std_logic_vector (4 DOWNTO 0); 
signal s_offset : std_logic_vector (5 DOWNTO 0); 
signal data: std_logic_vector(31 DOWNTO 0); 
signal hit_addr : std_logic;

-- Main memory definition: array of 32 words of 32 bits
type t_Memory is array (0 to 31) of std_logic_vector(31 downto 0);
signal mainmem : t_Memory:= ("00000000000000000000000000000001",others =>"00000000000000000000000000100000");

-- Signals for dirty, valid, tag, and LRU bits for both cache sets
signal dirtys0 : t_Dirty:= ( others => '0');
signal valids0 : t_valid:= ( others => '0');
signal tags0 : t_tag:=( others => "000000000000000000000");
signal lru0: t_LRU:=(others => '0'); 

signal dirtys1 : t_Dirty:= ( others => '0');
signal valids1 : t_valid:= (others => '0');
signal tags1 : t_tag:=( others => "000000000000000000000");
signal lru1: t_LRU:=(others => '1'); 

-- Signal for miss logic
signal miss : std_logic; 

signal set_0_out: std_logic;
signal set_1_out : std_logic; 



BEGIN
-- Process that handles the cache behavior on clock edge
process (clock)
	begin
	if clock = '1' then
	-- Extracting tag, index, and offset from the address when clock is in its positive state 
		s_tag <= Address(31 DOWNTO 11); 
		s_index <= Address(10  DOWNTO 6); 
		s_offset <= Address(5  DOWNTO 0); 
		-- Default values for hit and miss signals 
		hit_addr <= '0'; 
		miss <= '1'; 

		-- Check if the address is in the cache (this is when valid bit and tag match) 
		if valids0(to_integer(unsigned(s_index))) = '1' or valids1(to_integer(unsigned(s_index))) = '1' then 
			if s_tag = tags0(to_integer(unsigned(s_index))) or s_tag = tags1(to_integer(unsigned(s_index))) then 
				-- If found, read data from main memory
				data <= mainmem(to_integer(unsigned(s_offset))); 
				hit_addr <= '1'; 
				miss <= '0';
			end if; 
		end if; 
		-- Determine which set to used based on LRU bit. Check if the tag is not stored already in the cache 
		if lru0(to_integer(unsigned(s_index))) = '0'and tags1(to_integer(unsigned(s_index))) /= s_tag  then 

				-- Use set 0 
				valids0(to_integer(unsigned(s_index))) <= '1';
				
				-- Actual lru_0 bit changes to '1' and the other lru_1 bit changes to '0' in the index from address.  
				lru0(to_integer(unsigned(s_index))) <= '1'; 
				lru1(to_integer(unsigned(s_index))) <= '0';
				
				-- Save tag in cache0
				cache0(to_integer(unsigned(s_index)))(to_integer(unsigned(s_offset))) <= s_tag;

				-- Add the tag to tags0 
				tags0(to_integer(unsigned(s_index))) <= s_tag;

		
				set_1_out <= '0'; 
				set_0_out <= '1';
		elsif lru1(to_integer(unsigned(s_index))) = '0' and tags0(to_integer(unsigned(s_index))) /= s_tag then 
				-- Use set 1 
				valids1(to_integer(unsigned(s_index))) <= '1';
				
				-- Actual lru_1 bit changes to '1' and the other lru_0 bit changes to '0' in the index from address.  
				lru1(to_integer(unsigned(s_index))) <= '1'; 
				lru0(to_integer(unsigned(s_index))) <= '0'; 
				-- Save tag in cache1
				cache1(to_integer(unsigned(s_index)))(to_integer(unsigned(s_offset))) <= s_tag;

				-- Add the tag to tags1
				tags1(to_integer(unsigned(s_index))) <= s_tag;


				set_1_out <= '1'; 
				set_0_out <= '0'; 
		end if;
	end if; 
end process;

	-- Assign internal signals to output ports 
	tag_out <= s_tag; 
	index_out <= s_index;
	offset_out <= s_offset;
	hit <= hit_addr; 
	data_out <= data;
	miss_out <= miss; 
	set_0 <= set_0_out; 
	set_1 <= set_1_out;

END TypeArchitecture;
