// Logisim project Modulos_MIPS.circ as structural Verilog
module main (
  input  Reloj,
  input  Poder,
  input  [7:0] in_3,
  input  in_4,
  input  in_5,
  input  in_6,
  output [7:0] out_7
);

  wire and_1_out, and_2_out, and_3_out, Dormir_EX, Dormir_ID, Dormir_IF, Dormir_MEM, Dormir_WB,
       EX_Alineamiento_Memoria, EX_Lectura_Pendiente, EX_Overflow, EX_Tomar_Salto, IF_Tomar_Salto,
       Interruptor_Encendido_out, Limpiar_RAM, MEM_Escribir, MEM_Solicitar_Memoria, not_1_out, not_2_out,
       not_3_out, not_4_out, not_5_out, not_6_out, not_7_out, not_8_out, not_9_out, not_10_out, not_11_out,
       not_12_out, not_13_out, not_14_out, not_15_out, not_16_out, not_17_out, not_18_out, not_19_out,
       not_20_out, not_21_out, not_22_out, not_23_out, not_24_out, not_25_out, not_26_out, not_27_out,
       not_28_out, not_29_out, not_30_out, not_31_out, not_32_out, not_33_out, not_34_out, Poder_t,
       Primer_Ciclo, Reiniciar_EX, Reiniciar_ID, Reiniciar_IF, Reiniciar_MEM, Reiniciar_WB, Reloj_Externo,
       Reloj_t, ULA_alineamiento_memoria, ULA_overflow, ULA_tomar_salto, Usar_Little_Endian, WB_Solo_Lectura;
  wire [1:0] Decodificador_Instrucciones_escribir_lohi, Decodificador_Instrucciones_leer_lohi,
       EX_Escribir_LOHI, ID_Escribir_LOHI, ID_Leer_LOHI, MEM_Escribir_LOHI;
  wire [4:0] Controlador_Memoria_Externa_registro_destino_efectivo,
       Decodificador_Instrucciones_cantidad_corrimiento, Decodificador_Instrucciones_registro_destino,
       Decodificador_Instrucciones_registro_fuente, Decodificador_Instrucciones_registro_objetivo,
       EX_Registro_Destino, EX_Registro_Objetivo, ID_Cantidad_Corrimiento, ID_Registro_Destino,
       ID_Registro_Fuente, ID_Registro_Objetivo, MEM_Indice_Registro;
  wire [7:0] Bitmap_Dependencias, Decodificador_Instrucciones_bitmap_acceso_memoria,
       EX_Bitmap_Acceso_Memoria, ID_Bitmap_Acceso_Memoria, RAM_Byte;
  wire [15:0] Decodificador_Instrucciones_valor_inmediato, ID_Valor_Inmediato, RAM_Nibble;
  wire [25:0] Decodificador_Instrucciones_direccion_inmediata, ID_Direccion_Inmediata;
  wire [31:0] Controlador_Memoria_Externa_salida, Controlador_PC_indice_siguiente,
       EX_Contenido_Registro_Fuente, EX_Contenido_Registro_Objetivo, EX_Direccion_Memoria, EX_Entrada_HI,
       EX_Entrada_LO, EX_Salida_Calculo, EX_Salida_HI, EX_Salida_LO, EX_Valor_Escritura_Memoria,
       ID_Indice_Instruccion, IF_Indice_Instruccion, IF_Indice_Salto, IF_Instruccion, MEM_Direccion_Salto,
       MEM_Salida_HI, MEM_Salida_LO, MEM_Salida_Registro, RAM_Word, ROM_Instrucciones_word,
       ULA_direccion_memoria, ULA_salida_calculo, ULA_salida_hi, ULA_salida_lo, WB_Salida_HI, WB_Salida_LO,
       WB_Salida_Registro_Fuente, WB_Salida_Registro_Objetivo;
  wire [49:0] Decodificador_Instrucciones_bitmap_instruccion, ID_Bitmap_Instruccion;

  Button Interruptor_Encendido (.out(Interruptor_Encendido_out));
  T_Flip_Flop Poder_Interno (.T(and_1_out), .clk(Reloj_Externo), .Q(Poder_t), .reset(not_1_out));  // open: Qn, preset
  and and_1 (and_1_out, Interruptor_Encendido_out, Poder);
  not not_1 (not_1_out, Poder);
  Boot_Controller Controlador_Arranque (
    .Reloj_Externo(Reloj_Externo), .Interruptor(Poder_t), .Primer_Ciclo(Primer_Ciclo), .Reloj(Reloj_t));
  MIPS_Instruction_Decoder Decodificador_Instrucciones (
    .Instruccion(IF_Instruccion), .Bitmap_Instruccion(Decodificador_Instrucciones_bitmap_instruccion),
    .Direccion_Inmediata(Decodificador_Instrucciones_direccion_inmediata),
    .Valor_Inmediato(Decodificador_Instrucciones_valor_inmediato),
    .Cantidad_Corrimiento(Decodificador_Instrucciones_cantidad_corrimiento),
    .Registro_Fuente(Decodificador_Instrucciones_registro_fuente),
    .Registro_Objetivo(Decodificador_Instrucciones_registro_objetivo),
    .Registro_Destino(Decodificador_Instrucciones_registro_destino),
    .Escribir_LOHI(Decodificador_Instrucciones_escribir_lohi),
    .Leer_LOHI(Decodificador_Instrucciones_leer_lohi),
    .Bitmap_Acceso_Memoria(Decodificador_Instrucciones_bitmap_acceso_memoria));
  not not_2 (not_2_out, MEM_Solicitar_Memoria);
  Four_GB_ROM_Controller ROM_Instrucciones (
    .Direccion_32_bits(IF_Indice_Instruccion), .Usar_Litte_Endian(Usar_Little_Endian),
    .Word(ROM_Instrucciones_word));  // open: Doubleword, Nibble, Byte
  and and_2 (and_2_out, MEM_Escribir_LOHI[1], ~Dormir_WB);  // AND_Gate
  and and_3 (and_3_out, MEM_Escribir_LOHI[0], ~Dormir_WB);  // AND_Gate
  // DipSwitch #(.number(2)) Opciones_Control: pin names not known; wires that end beside it: Usar_Little_Endian, Limpiar_RAM
  Clock clock_1 (.out(Reloj_Externo));
  PC_Controller Controlador_PC (
    .Indice_Anterior(IF_Indice_Instruccion), .Indice_Salto(IF_Indice_Salto), .Tomar_Salto(IF_Tomar_Salto),
    .Indice_Siguiente(Controlador_PC_indice_siguiente));
  Register #(.width(50)) u_ID_Bitmap_Instruccion (
    .D(Decodificador_Instrucciones_bitmap_instruccion), .en(not_3_out), .clk(Reloj_t),
    .Q(ID_Bitmap_Instruccion), .clr(Reiniciar_ID));
  not not_3 (not_3_out, Dormir_ID);
  Register #(.width(26)) u_ID_Direccion_Inmediata (
    .D(Decodificador_Instrucciones_direccion_inmediata), .en(not_4_out), .clk(Reloj_t),
    .Q(ID_Direccion_Inmediata), .clr(Reiniciar_ID));
  not not_4 (not_4_out, Dormir_ID);
  Register #(.width(16)) u_ID_Valor_Inmediato (
    .D(Decodificador_Instrucciones_valor_inmediato), .en(not_5_out), .clk(Reloj_t), .Q(ID_Valor_Inmediato),
    .clr(Reiniciar_ID));
  not not_5 (not_5_out, Dormir_ID);
  Register #(.width(5)) u_ID_Cantidad_Corrimiento (
    .D(Decodificador_Instrucciones_cantidad_corrimiento), .en(not_6_out), .clk(Reloj_t),
    .Q(ID_Cantidad_Corrimiento), .clr(Reiniciar_ID));
  not not_6 (not_6_out, Dormir_ID);
  Register #(.width(5)) u_ID_Registro_Fuente (
    .D(Decodificador_Instrucciones_registro_fuente), .en(not_7_out), .clk(Reloj_t), .Q(ID_Registro_Fuente),
    .clr(Reiniciar_ID));
  not not_7 (not_7_out, Dormir_ID);
  Register #(.width(5)) u_ID_Registro_Objetivo (
    .D(Decodificador_Instrucciones_registro_objetivo), .en(not_8_out), .clk(Reloj_t),
    .Q(ID_Registro_Objetivo), .clr(Reiniciar_ID));
  not not_8 (not_8_out, Dormir_ID);
  Register #(.width(5)) u_ID_Registro_Destino (
    .D(Decodificador_Instrucciones_registro_destino), .en(not_9_out), .clk(Reloj_t), .Q(ID_Registro_Destino),
    .clr(Reiniciar_ID));
  not not_9 (not_9_out, Dormir_ID);
  Register #(.width(2)) u_ID_Escribir_LOHI (
    .D(Decodificador_Instrucciones_escribir_lohi), .en(not_10_out), .clk(Reloj_t), .Q(ID_Escribir_LOHI),
    .clr(Reiniciar_ID));
  not not_10 (not_10_out, Dormir_ID);
  Register #(.width(2)) u_ID_Leer_LOHI (
    .D(Decodificador_Instrucciones_leer_lohi), .en(not_11_out), .clk(Reloj_t), .Q(ID_Leer_LOHI),
    .clr(Reiniciar_ID));
  not not_11 (not_11_out, Dormir_ID);
  Register u_ID_Bitmap_Acceso_Memoria (
    .D(Decodificador_Instrucciones_bitmap_acceso_memoria), .en(not_12_out), .clk(Reloj_t),
    .Q(ID_Bitmap_Acceso_Memoria), .clr(Reiniciar_ID));
  not not_12 (not_12_out, Dormir_ID);
  Four_GB_RAM_Controller RAM_Datos (
    .Reloj(Reloj_t), .Limpiar(Limpiar_RAM), .Bloquear(not_2_out), .Escribir(MEM_Escribir),
    .Direccion_32_bits(EX_Direccion_Memoria), .Usar_Litte_Endian(Usar_Little_Endian),
    .Entrada(EX_Valor_Escritura_Memoria), .Word(RAM_Word), .Nibble(RAM_Nibble), .Byte(RAM_Byte));  // open: Doubleword
  Register #(.width(32)) HI (.D(MEM_Salida_HI), .en(and_2_out), .clk(Reloj_t), .Q(WB_Salida_HI), .clr(Reiniciar_WB));
  Register #(.width(32)) LO (.D(MEM_Salida_LO), .en(and_3_out), .clk(Reloj_t), .Q(WB_Salida_LO), .clr(Reiniciar_WB));
  Register #(.width(32)) register_1 (
    .D(Controlador_PC_indice_siguiente), .en(not_13_out), .clk(Reloj_t), .Q(IF_Indice_Instruccion),
    .clr(Reiniciar_IF));
  not not_13 (not_13_out, Dormir_IF);
  Register #(.width(32)) u_IF_Instruccion (
    .D(ROM_Instrucciones_word), .en(not_14_out), .clk(Reloj_t), .Q(IF_Instruccion), .clr(Reiniciar_IF));
  not not_14 (not_14_out, Dormir_IF);
  MIPS_Memory_Controller Controlador_Memoria_Externa (
    .Entrada(EX_Salida_Calculo), .Registro_Destino(EX_Registro_Destino),
    .Registro_Objetivo(EX_Registro_Objetivo), .Bitmap_Acceso_Memoria(EX_Bitmap_Acceso_Memoria),
    .Word_Lectura(RAM_Word), .Nibble_Lectura(RAM_Nibble), .Byte_Lectura(RAM_Byte),
    .Salida(Controlador_Memoria_Externa_salida),
    .Registro_Destino_Efectivo(Controlador_Memoria_Externa_registro_destino_efectivo),
    .Solicitar_Memoria(MEM_Solicitar_Memoria), .Escribir_Memoria(MEM_Escribir));
  Register_File_Controller Controlador_Pagina_Registros (
    .Reloj(Reloj_t), .Limpiar(Reiniciar_WB), .Entrada(MEM_Salida_Registro),
    .Registro_Escritura(MEM_Indice_Registro), .Registro_Lectura_A(ID_Registro_Fuente),
    .Registro_Lectura_B(ID_Registro_Objetivo), .Solo_Lectura(WB_Solo_Lectura),
    .Salida_A(WB_Salida_Registro_Fuente), .Salida_B(WB_Salida_Registro_Objetivo));
  MIPS_ALU ULA (
    .Bitmap_Instruccion(ID_Bitmap_Instruccion), .Cantidad_Corrimiento(ID_Cantidad_Corrimiento),
    .Contenido_Registro_Fuente(EX_Contenido_Registro_Fuente),
    .Contenido_Registro_Objetivo(EX_Contenido_Registro_Objetivo), .Contenido_Previo_HI(EX_Entrada_HI),
    .Contenido_Previo_LO(EX_Entrada_LO), .Valor_Inmediato(ID_Valor_Inmediato),
    .Direccion_Inmediata(ID_Direccion_Inmediata), .Indice_PC(ID_Indice_Instruccion),
    .Salida_HI(ULA_salida_hi), .Salida_LO(ULA_salida_lo), .Salida_Calculo(ULA_salida_calculo),
    .Direccion_Memoria(ULA_direccion_memoria), .Overflow(ULA_overflow), .Tomar_Salto(ULA_tomar_salto),
    .Alineamiento_Memoria(ULA_alineamiento_memoria));
  Register register_2 (.D(in_3), .en(in_4), .clk(in_5), .Q(out_7), .clr(in_6));
  MIPS_Data_Hazard_Solver Corrector_Data_Hazards (
    .Bitmap_Dependencias(Bitmap_Dependencias), .EX_LO(EX_Salida_LO), .MEM_LO(MEM_Salida_LO),
    .WB_LO(WB_Salida_LO), .EX_HI(EX_Salida_HI), .MEM_HI(MEM_Salida_HI), .WB_HI(WB_Salida_HI),
    .EX_Salida(EX_Salida_Calculo), .MEM_Salida(MEM_Salida_Registro), .WB_Fuente(WB_Salida_Registro_Fuente),
    .WB_Objetivo(WB_Salida_Registro_Objetivo), .EX_Entrada_LO(EX_Entrada_LO), .EX_Entrada_HI(EX_Entrada_HI),
    .EX_Entrada_Fuente(EX_Contenido_Registro_Fuente), .EX_Entrada_Objetivo(EX_Contenido_Registro_Objetivo));
  // MIPS_Control_Hazard_Solver mips_control_hazard_solver_1: pin names not known; wires that end beside it: Reloj_t, EX_Lectura_Pendiente, EX_Tomar_Salto, IF_Tomar_Salto, Dormir_IF, Dormir_ID, Dormir_EX, Dormir_MEM, Dormir_WB, Reiniciar_IF, Reiniciar_ID, Reiniciar_EX, Reiniciar_MEM, Reiniciar_WB
  Register #(.width(32)) u_MEM_Salida_Registro (
    .D(Controlador_Memoria_Externa_salida), .en(not_15_out), .clk(Reloj_t), .Q(MEM_Salida_Registro),
    .clr(Reiniciar_MEM));
  not not_15 (not_15_out, Dormir_MEM);
  Register #(.width(5)) u_MEM_Indice_Registro (
    .D(Controlador_Memoria_Externa_registro_destino_efectivo), .en(not_16_out), .clk(Reloj_t),
    .Q(MEM_Indice_Registro), .clr(Reiniciar_MEM));
  not not_16 (not_16_out, Dormir_MEM);
  MIPS_Data_Hazard_Detector Detector_Data_Hazards (
    .ID_Registro_Fuente(ID_Registro_Fuente), .ID_Registro_Objetivo(ID_Registro_Objetivo),
    .EX_Registro_Destino(EX_Registro_Destino), .MEM_Indice_Registro(MEM_Indice_Registro),
    .ID_Leer_LOHI(ID_Leer_LOHI), .EX_Escribir_LOHI(EX_Escribir_LOHI), .MEM_Escribir_LOHI(MEM_Escribir_LOHI),
    .EX_Bitmap_Acceso_Memoria(EX_Bitmap_Acceso_Memoria), .Bitmap_Dependencias(Bitmap_Dependencias),
    .EX_Lectura_Memoria_Pendiente(EX_Lectura_Pendiente));
  Register #(.width(32)) u_ID_Indice_Instruccion (
    .D(IF_Indice_Instruccion), .en(not_17_out), .clk(Reloj_t), .Q(ID_Indice_Instruccion), .clr(Reiniciar_ID));
  not not_17 (not_17_out, Dormir_ID);
  Register #(.width(32)) EX_HI (
    .D(ULA_salida_hi), .en(not_18_out), .clk(Reloj_t), .Q(EX_Salida_HI), .clr(Reiniciar_EX));
  not not_18 (not_18_out, Dormir_EX);
  Register #(.width(32)) EX_LO (
    .D(ULA_salida_lo), .en(not_19_out), .clk(Reloj_t), .Q(EX_Salida_LO), .clr(Reiniciar_EX));
  not not_19 (not_19_out, Dormir_EX);
  Register #(.width(32)) u_EX_Salida_Calculo (
    .D(ULA_salida_calculo), .en(not_20_out), .clk(Reloj_t), .Q(EX_Salida_Calculo), .clr(Reiniciar_EX));
  not not_20 (not_20_out, Dormir_EX);
  Register #(.width(32)) u_EX_Direccion_Memoria (
    .D(ULA_direccion_memoria), .en(not_21_out), .clk(Reloj_t), .Q(EX_Direccion_Memoria), .clr(Reiniciar_EX));
  not not_21 (not_21_out, Dormir_EX);
  Register #(.width(1)) u_EX_Overflow (
    .D(ULA_overflow), .en(not_22_out), .clk(Reloj_t), .Q(EX_Overflow), .clr(Reiniciar_EX));
  not not_22 (not_22_out, Dormir_EX);
  Register #(.width(1)) u_EX_Tomar_Salto (
    .D(ULA_tomar_salto), .en(not_23_out), .clk(Reloj_t), .Q(EX_Tomar_Salto), .clr(Reiniciar_EX));
  not not_23 (not_23_out, Dormir_EX);
  Register #(.width(1)) u_EX_Alineamiento_Memoria (
    .D(ULA_alineamiento_memoria), .en(not_24_out), .clk(Reloj_t), .Q(EX_Alineamiento_Memoria),
    .clr(Reiniciar_EX));
  not not_24 (not_24_out, Dormir_EX);
  Register #(.width(32)) u_MEM_Salida_HI (
    .D(EX_Salida_HI), .en(not_25_out), .clk(Reloj_t), .Q(MEM_Salida_HI), .clr(Reiniciar_MEM));
  not not_25 (not_25_out, Dormir_MEM);
  Register #(.width(32)) u_MEM_Salida_LO (
    .D(EX_Salida_LO), .en(not_26_out), .clk(Reloj_t), .Q(MEM_Salida_LO), .clr(Reiniciar_MEM));
  not not_26 (not_26_out, Dormir_MEM);
  Register #(.width(2)) u_MEM_Escribir_LOHI (
    .D(EX_Escribir_LOHI), .en(not_27_out), .clk(Reloj_t), .Q(MEM_Escribir_LOHI), .clr(Reiniciar_MEM));
  not not_27 (not_27_out, Dormir_MEM);
  Register u_EX_Bitmap_Acceso_Memoria (
    .D(ID_Bitmap_Acceso_Memoria), .en(not_28_out), .clk(Reloj_t), .Q(EX_Bitmap_Acceso_Memoria),
    .clr(Reiniciar_EX));
  not not_28 (not_28_out, Dormir_EX);
  Register #(.width(32)) u_EX_Valor_Escritura_Memoria (
    .D(EX_Contenido_Registro_Objetivo), .en(not_29_out), .clk(Reloj_t), .Q(EX_Valor_Escritura_Memoria),
    .clr(Reiniciar_EX));
  not not_29 (not_29_out, Dormir_EX);
  Register #(.width(32)) u_MEM_Direccion_Salto (
    .D(EX_Direccion_Memoria), .en(not_30_out), .clk(Reloj_t), .Q(MEM_Direccion_Salto), .clr(Reiniciar_MEM));
  not not_30 (not_30_out, Dormir_MEM);
  Register #(.width(1)) MEM_Tomar_Salto (
    .D(EX_Tomar_Salto), .en(not_31_out), .clk(Reloj_t), .Q(IF_Tomar_Salto), .clr(Reiniciar_MEM));
  not not_31 (not_31_out, Dormir_MEM);
  Register #(.width(5)) u_EX_Registro_Destino (
    .D(ID_Registro_Destino), .en(not_32_out), .clk(Reloj_t), .Q(EX_Registro_Destino), .clr(Reiniciar_EX));
  not not_32 (not_32_out, Dormir_EX);
  Register #(.width(5)) u_EX_Registro_Objetivo (
    .D(ID_Registro_Objetivo), .en(not_33_out), .clk(Reloj_t), .Q(EX_Registro_Objetivo), .clr(Reiniciar_EX));
  not not_33 (not_33_out, Dormir_EX);
  Register #(.width(2)) u_EX_Escribir_LOHI (
    .D(ID_Escribir_LOHI), .en(not_34_out), .clk(Reloj_t), .Q(EX_Escribir_LOHI), .clr(Reiniciar_EX));
  not not_34 (not_34_out, Dormir_EX);

  // Other names for the same wires on the sheet: WB_Escribir_LO = MEM_Escribir_LOHI[0];
  //   WB_Escribir_HI = MEM_Escribir_LOHI[1]; MEM_Tomar_Salto = IF_Tomar_Salto; Poder_Externo = Poder

  // Notes on the sheet:
  //   Poder: initial=0x1
  //   Encender o apagar procesador
  //   Etapa I: Buscar instrucción
  //   Etapa III: Ejecutar cálculos
  //   Unidad de Control
  //   Etapa II: Decodificar instrucción
  //   Etapa IV: Accesar memoria externa
  //   Etapa V: Actualizar memoria interna
endmodule

module Boot_Controller (
  input  Reloj_Externo,
  input  Interruptor,
  output Primer_Ciclo,
  output Reloj
);

  wire and_1_out, d_ff_1_q, d_ff_1_qn, not_1_out, t_ff_1_q, t_ff_1_qn;

  T_Flip_Flop t_ff_1 (
    .T(t_ff_1_qn), .clk(Reloj_Externo), .Q(t_ff_1_q), .Qn(t_ff_1_qn), .reset(not_1_out), .preset(1'b0));
  not not_1 (not_1_out, Interruptor);
  and and_1 (and_1_out, Reloj_Externo, Interruptor);
  and and_2 (Reloj, t_ff_1_q, and_1_out);
  D_Flip_Flop d_ff_1 (
    .D(t_ff_1_qn), .clk(Reloj_Externo), .Q(d_ff_1_q), .Qn(d_ff_1_qn), .preset(1'b0), .reset(not_1_out));
  // NoConnect on d_ff_1_qn
  and and_3 (Primer_Ciclo, d_ff_1_q, Reloj);
endmodule

module PC_Controller (
  input  [31:0] Indice_Anterior,
  input  [31:0] Indice_Salto,
  input  Tomar_Salto,
  output [31:0] Indice_Siguiente
);

  wire [31:0] adder_1_out;

  Adder #(.width(32)) adder_1 (.a(Indice_Anterior), .b(32'h4), .out(adder_1_out), .cin(1'b0));  // open: cout
  Multiplexer #(.width(32)) multiplexer_1 (
    .in0(adder_1_out), .in1(Indice_Salto), .out(Indice_Siguiente), .sel(Tomar_Salto));

  // Notes on the sheet:
  //   Alienamiento de Instrucciones
endmodule

module Register_File_Controller (
  input  Reloj,
  input  Limpiar,
  input  [31:0] Entrada,
  input  [4:0] Registro_Escritura,
  input  [4:0] Registro_Lectura_A,
  input  [4:0] Registro_Lectura_B,
  output Solo_Lectura,
  output [31:0] Salida_A,
  output [31:0] Salida_B
);

  wire decoder_1_out1, decoder_1_out2, decoder_1_out3, decoder_1_out4, decoder_1_out5, decoder_1_out6,
       decoder_1_out7, decoder_1_out8, decoder_1_out9, decoder_1_out10, decoder_1_out11, decoder_1_out12,
       decoder_1_out13, decoder_1_out14, decoder_1_out15, decoder_1_out16, decoder_1_out17, decoder_1_out18,
       decoder_1_out19, decoder_1_out20, decoder_1_out21, decoder_1_out22, decoder_1_out23, decoder_1_out24,
       decoder_1_out25, decoder_1_out26, decoder_1_out27, decoder_1_out28, decoder_1_out29, decoder_1_out30,
       decoder_1_out31;
  wire [31:0] a0_q, a1_q, a2_q, a3_q, at_q, fp_q, gp_q, k0_q, k1_q, ra_q, s0_q, s1_q, s2_q, s3_q, s4_q, s5_q,
       s6_q, s7_q, sp_q, t0_q, t1_q, t2_q, t3_q, t4_q, t5_q, t6_q, t7_q, t8_q, t9_q, v0_q, v1_q;

  Decoder #(.enable("false"), .select(5)) decoder_1 (
    .out0(Solo_Lectura), .out1(decoder_1_out1), .out2(decoder_1_out2), .out3(decoder_1_out3),
    .out4(decoder_1_out4), .out5(decoder_1_out5), .out6(decoder_1_out6), .out7(decoder_1_out7),
    .out8(decoder_1_out8), .out9(decoder_1_out9), .out10(decoder_1_out10), .out11(decoder_1_out11),
    .out12(decoder_1_out12), .out13(decoder_1_out13), .out14(decoder_1_out14), .out15(decoder_1_out15),
    .out16(decoder_1_out16), .out17(decoder_1_out17), .out18(decoder_1_out18), .out19(decoder_1_out19),
    .out20(decoder_1_out20), .out21(decoder_1_out21), .out22(decoder_1_out22), .out23(decoder_1_out23),
    .out24(decoder_1_out24), .out25(decoder_1_out25), .out26(decoder_1_out26), .out27(decoder_1_out27),
    .out28(decoder_1_out28), .out29(decoder_1_out29), .out30(decoder_1_out30), .out31(decoder_1_out31),
    .sel(Registro_Escritura));
  Register #(.width(32)) at (.D(Entrada), .en(decoder_1_out1), .clk(Reloj), .Q(at_q), .clr(Limpiar));
  Register #(.width(32)) v0 (.D(Entrada), .en(decoder_1_out2), .clk(Reloj), .Q(v0_q), .clr(Limpiar));
  Register #(.width(32)) v1 (.D(Entrada), .en(decoder_1_out3), .clk(Reloj), .Q(v1_q), .clr(Limpiar));
  Register #(.width(32)) a0 (.D(Entrada), .en(decoder_1_out4), .clk(Reloj), .Q(a0_q), .clr(Limpiar));
  Register #(.width(32)) a1 (.D(Entrada), .en(decoder_1_out5), .clk(Reloj), .Q(a1_q), .clr(Limpiar));
  Register #(.width(32)) a2 (.D(Entrada), .en(decoder_1_out6), .clk(Reloj), .Q(a2_q), .clr(Limpiar));
  Register #(.width(32)) a3 (.D(Entrada), .en(decoder_1_out7), .clk(Reloj), .Q(a3_q), .clr(Limpiar));
  Register #(.width(32)) t0 (.D(Entrada), .en(decoder_1_out8), .clk(Reloj), .Q(t0_q), .clr(Limpiar));
  Register #(.width(32)) t1 (.D(Entrada), .en(decoder_1_out9), .clk(Reloj), .Q(t1_q), .clr(Limpiar));
  Register #(.width(32)) t2 (.D(Entrada), .en(decoder_1_out10), .clk(Reloj), .Q(t2_q), .clr(Limpiar));
  Register #(.width(32)) t3 (.D(Entrada), .en(decoder_1_out11), .clk(Reloj), .Q(t3_q), .clr(Limpiar));
  Register #(.width(32)) t4 (.D(Entrada), .en(decoder_1_out12), .clk(Reloj), .Q(t4_q), .clr(Limpiar));
  Register #(.width(32)) t5 (.D(Entrada), .en(decoder_1_out13), .clk(Reloj), .Q(t5_q), .clr(Limpiar));
  Register #(.width(32)) t6 (.D(Entrada), .en(decoder_1_out14), .clk(Reloj), .Q(t6_q), .clr(Limpiar));
  Register #(.width(32)) t7 (.D(Entrada), .en(decoder_1_out15), .clk(Reloj), .Q(t7_q), .clr(Limpiar));
  Register #(.width(32)) s0 (.D(Entrada), .en(decoder_1_out16), .clk(Reloj), .Q(s0_q), .clr(Limpiar));
  Register #(.width(32)) s1 (.D(Entrada), .en(decoder_1_out17), .clk(Reloj), .Q(s1_q), .clr(Limpiar));
  Register #(.width(32)) s2 (.D(Entrada), .en(decoder_1_out18), .clk(Reloj), .Q(s2_q), .clr(Limpiar));
  Register #(.width(32)) s3 (.D(Entrada), .en(decoder_1_out19), .clk(Reloj), .Q(s3_q), .clr(Limpiar));
  Register #(.width(32)) s4 (.D(Entrada), .en(decoder_1_out20), .clk(Reloj), .Q(s4_q), .clr(Limpiar));
  Register #(.width(32)) s5 (.D(Entrada), .en(decoder_1_out21), .clk(Reloj), .Q(s5_q), .clr(Limpiar));
  Register #(.width(32)) s6 (.D(Entrada), .en(decoder_1_out22), .clk(Reloj), .Q(s6_q), .clr(Limpiar));
  Register #(.width(32)) s7 (.D(Entrada), .en(decoder_1_out23), .clk(Reloj), .Q(s7_q), .clr(Limpiar));
  Register #(.width(32)) t8 (.D(Entrada), .en(decoder_1_out24), .clk(Reloj), .Q(t8_q), .clr(Limpiar));
  Register #(.width(32)) t9 (.D(Entrada), .en(decoder_1_out25), .clk(Reloj), .Q(t9_q), .clr(Limpiar));
  Register #(.width(32)) k0 (.D(Entrada), .en(decoder_1_out26), .clk(Reloj), .Q(k0_q), .clr(Limpiar));
  Register #(.width(32)) k1 (.D(Entrada), .en(decoder_1_out27), .clk(Reloj), .Q(k1_q), .clr(Limpiar));
  Register #(.width(32)) gp (.D(Entrada), .en(decoder_1_out28), .clk(Reloj), .Q(gp_q), .clr(Limpiar));
  Register #(.width(32)) sp (.D(Entrada), .en(decoder_1_out29), .clk(Reloj), .Q(sp_q), .clr(Limpiar));
  Register #(.width(32)) fp (.D(Entrada), .en(decoder_1_out30), .clk(Reloj), .Q(fp_q), .clr(Limpiar));
  Register #(.width(32)) ra (.D(Entrada), .en(decoder_1_out31), .clk(Reloj), .Q(ra_q), .clr(Limpiar));
  Multiplexer #(.select(5), .width(32)) multiplexer_1 (
    .in0({32{1'b0}}), .in1(at_q), .in2(v0_q), .in3(v1_q), .in4(a0_q), .in5(a1_q), .in6(a2_q), .in7(a3_q),
    .in8(t0_q), .in9(t1_q), .in10(t2_q), .in11(t3_q), .in12(t4_q), .in13(t5_q), .in14(t6_q), .in15(t7_q),
    .in16(s0_q), .in17(s1_q), .in18(s2_q), .in19(s3_q), .in20(s4_q), .in21(s5_q), .in22(s6_q), .in23(s7_q),
    .in24(t8_q), .in25(t9_q), .in26(k0_q), .in27(k1_q), .in28(gp_q), .in29(sp_q), .in30(fp_q), .in31(ra_q),
    .out(Salida_A), .sel(Registro_Lectura_A));
  Multiplexer #(.select(5), .width(32)) multiplexer_2 (
    .in0({32{1'b0}}), .in1(at_q), .in2(v0_q), .in3(v1_q), .in4(a0_q), .in5(a1_q), .in6(a2_q), .in7(a3_q),
    .in8(t0_q), .in9(t1_q), .in10(t2_q), .in11(t3_q), .in12(t4_q), .in13(t5_q), .in14(t6_q), .in15(t7_q),
    .in16(s0_q), .in17(s1_q), .in18(s2_q), .in19(s3_q), .in20(s4_q), .in21(s5_q), .in22(s6_q), .in23(s7_q),
    .in24(t8_q), .in25(t9_q), .in26(k0_q), .in27(k1_q), .in28(gp_q), .in29(sp_q), .in30(fp_q), .in31(ra_q),
    .out(Salida_B), .sel(Registro_Lectura_B));

  // Other names for the same wires on the sheet: Direccion_Escritura[4:0] = Registro_Escritura;
  //   Direccion_Lectura_A[4:0] = Registro_Lectura_A; Direccion_Lectura_B[4:0] = Registro_Lectura_B
endmodule

module MIPS_Instruction_Detector (
  input  [5:0] Tipo_Operacion,
  input  [6:0] Funcion_Aritmetica,
  output [49:0] Bitmap_Instruccion
);

  wire bit_extender_2_out, decoder_1_out0, decoder_1_out1, decoder_2_out1, decoder_2_out16, decoder_2_out17,
       decoder_2_out18, decoder_2_out19, decoder_2_out20, decoder_2_out21, decoder_2_out22, decoder_2_out23,
       decoder_2_out24, decoder_2_out25, decoder_2_out26, decoder_2_out27, decoder_2_out28, decoder_2_out29,
       decoder_2_out30, decoder_2_out31, decoder_3_out3, decoder_3_out6, decoder_3_out7, decoder_3_out10,
       decoder_3_out12, decoder_3_out13, decoder_3_out14, decoder_3_out15, decoder_3_out16, decoder_3_out17,
       decoder_3_out18, decoder_3_out19, decoder_3_out20, decoder_3_out21, decoder_3_out22, decoder_3_out23,
       decoder_3_out24, decoder_3_out25, decoder_3_out26, decoder_3_out27, decoder_3_out28, decoder_3_out29,
       decoder_3_out30, decoder_3_out31, decoder_4_out1, decoder_4_out5, decoder_4_out10, decoder_4_out11,
       decoder_4_out13, decoder_4_out14, decoder_4_out15, decoder_4_out20, decoder_4_out21, decoder_4_out22,
       decoder_4_out23, decoder_4_out28, decoder_4_out29, decoder_4_out30, decoder_4_out31, decoder_5_out8,
       decoder_5_out9, decoder_5_out12, decoder_5_out13, decoder_5_out14, decoder_5_out15, decoder_5_out16,
       decoder_5_out17, decoder_5_out18, decoder_5_out19, decoder_5_out20, decoder_5_out21, decoder_5_out22,
       decoder_5_out23, decoder_5_out24, decoder_5_out25, decoder_5_out26, decoder_5_out27, decoder_5_out28,
       decoder_5_out29, decoder_5_out30, decoder_5_out31, demultiplexer_1_out0, demultiplexer_1_out1,
       demultiplexer_1_out2, demultiplexer_1_out3, Instruccion_Desconocida_A, Instruccion_Desconocida_B,
       Instruccion_Desconocida_C, Instruccion_Desconocida_D, Instruccion_Desconocida_E, or_2_out, or_3_out,
       or_4_out, or_8_out, or_9_out, or_10_out, or_11_out, or_13_out, or_14_out, Tipo_R;
  wire [1:0] bit_extender_4_out;
  wire [4:0] bit_extender_1_out, bit_extender_3_out;
  wire [5:0] shifter_1_out;
  wire [6:0] shifter_2_out;

  Shifter #(.shift("lr"), .width(6)) shifter_1 (.in(Tipo_Operacion), .\dist (3'b101), .out(shifter_1_out));
  Bit_Extender #(.in_width(6), .out_width(5)) bit_extender_1 (.in(Tipo_Operacion), .out(bit_extender_1_out));
  or or_1 (Instruccion_Desconocida_A, decoder_2_out1, or_2_out);
  Bit_Extender #(.in_width(6), .out_width(1)) bit_extender_2 (.in(shifter_1_out), .out(bit_extender_2_out));
  Decoder #(.enable("false")) decoder_1 (.out0(decoder_1_out0), .out1(decoder_1_out1), .sel(bit_extender_2_out));
  Decoder #(.select(5)) decoder_2 (
    .out0(Tipo_R), .out1(decoder_2_out1), .out2(Bitmap_Instruccion[28]), .out3(Bitmap_Instruccion[29]),
    .out4(Bitmap_Instruccion[30]), .out5(Bitmap_Instruccion[31]), .out6(Bitmap_Instruccion[32]),
    .out7(Bitmap_Instruccion[33]), .out8(Bitmap_Instruccion[34]), .out9(Bitmap_Instruccion[35]),
    .out10(Bitmap_Instruccion[36]), .out11(Bitmap_Instruccion[37]), .out12(Bitmap_Instruccion[38]),
    .out13(Bitmap_Instruccion[39]), .out14(Bitmap_Instruccion[40]), .out15(Bitmap_Instruccion[41]),
    .out16(decoder_2_out16), .out17(decoder_2_out17), .out18(decoder_2_out18), .out19(decoder_2_out19),
    .out20(decoder_2_out20), .out21(decoder_2_out21), .out22(decoder_2_out22), .out23(decoder_2_out23),
    .out24(decoder_2_out24), .out25(decoder_2_out25), .out26(decoder_2_out26), .out27(decoder_2_out27),
    .out28(decoder_2_out28), .out29(decoder_2_out29), .out30(decoder_2_out30), .out31(decoder_2_out31),
    .sel(bit_extender_1_out), .en(decoder_1_out0));
  or or_2 (or_2_out, decoder_2_out16, decoder_2_out17, decoder_2_out18, decoder_2_out19, decoder_2_out20, decoder_2_out21, decoder_2_out22, decoder_2_out23, decoder_2_out24, decoder_2_out25, decoder_2_out26, decoder_2_out27, decoder_2_out28, decoder_2_out29, decoder_2_out30, decoder_2_out31);
  Decoder #(.select(5)) decoder_3 (
    .out0(Bitmap_Instruccion[42]), .out1(Bitmap_Instruccion[43]), .out2(Bitmap_Instruccion[44]),
    .out3(decoder_3_out3), .out4(Bitmap_Instruccion[45]), .out5(Bitmap_Instruccion[46]),
    .out6(decoder_3_out6), .out7(decoder_3_out7), .out8(Bitmap_Instruccion[47]),
    .out9(Bitmap_Instruccion[48]), .out10(decoder_3_out10), .out11(Bitmap_Instruccion[49]),
    .out12(decoder_3_out12), .out13(decoder_3_out13), .out14(decoder_3_out14), .out15(decoder_3_out15),
    .out16(decoder_3_out16), .out17(decoder_3_out17), .out18(decoder_3_out18), .out19(decoder_3_out19),
    .out20(decoder_3_out20), .out21(decoder_3_out21), .out22(decoder_3_out22), .out23(decoder_3_out23),
    .out24(decoder_3_out24), .out25(decoder_3_out25), .out26(decoder_3_out26), .out27(decoder_3_out27),
    .out28(decoder_3_out28), .out29(decoder_3_out29), .out30(decoder_3_out30), .out31(decoder_3_out31),
    .sel(bit_extender_1_out), .en(decoder_1_out1));
  or or_3 (or_3_out, decoder_3_out6, decoder_3_out7);
  or or_4 (or_4_out, decoder_3_out12, decoder_3_out13, decoder_3_out14, decoder_3_out15, decoder_3_out16, decoder_3_out17, decoder_3_out18, decoder_3_out19, decoder_3_out20, decoder_3_out21, decoder_3_out22, decoder_3_out23, decoder_3_out24, decoder_3_out25, decoder_3_out26, decoder_3_out27, decoder_3_out28, decoder_3_out29, decoder_3_out30, decoder_3_out31);
  or or_5 (Bitmap_Instruccion[0], Instruccion_Desconocida_C, Instruccion_Desconocida_D, Instruccion_Desconocida_B, Instruccion_Desconocida_A, Instruccion_Desconocida_E);
  or or_6 (Instruccion_Desconocida_B, or_4_out, decoder_3_out10, or_3_out, decoder_3_out3);
  Shifter #(.shift("lr"), .width(7)) shifter_2 (.in(Funcion_Aritmetica), .\dist (3'b101), .out(shifter_2_out));
  Bit_Extender #(.in_width(7), .out_width(5)) bit_extender_3 (.in(Funcion_Aritmetica), .out(bit_extender_3_out));
  or or_7 (Instruccion_Desconocida_C, decoder_4_out1, decoder_4_out5, or_8_out, or_9_out, or_10_out, or_11_out);
  Bit_Extender #(.in_width(7), .out_width(2)) bit_extender_4 (.in(shifter_2_out), .out(bit_extender_4_out));
  or or_8 (or_8_out, decoder_4_out10, decoder_4_out11);
  or or_9 (or_9_out, decoder_4_out13, decoder_4_out14, decoder_4_out15);
  or or_10 (or_10_out, decoder_4_out20, decoder_4_out21, decoder_4_out22, decoder_4_out23);
  or or_11 (or_11_out, decoder_4_out28, decoder_4_out29, decoder_4_out30, decoder_4_out31);
  Demultiplexer #(.select(2)) demultiplexer_1 (
    .out0(demultiplexer_1_out0), .out1(demultiplexer_1_out1), .out2(demultiplexer_1_out2),
    .out3(demultiplexer_1_out3), .in(Tipo_R), .sel(bit_extender_4_out));
  Decoder #(.select(5)) decoder_4 (
    .out0(Bitmap_Instruccion[1]), .out1(decoder_4_out1), .out2(Bitmap_Instruccion[2]),
    .out3(Bitmap_Instruccion[3]), .out4(Bitmap_Instruccion[4]), .out5(decoder_4_out5),
    .out6(Bitmap_Instruccion[5]), .out7(Bitmap_Instruccion[6]), .out8(Bitmap_Instruccion[7]),
    .out9(Bitmap_Instruccion[8]), .out10(decoder_4_out10), .out11(decoder_4_out11),
    .out12(Bitmap_Instruccion[9]), .out13(decoder_4_out13), .out14(decoder_4_out14), .out15(decoder_4_out15),
    .out16(Bitmap_Instruccion[10]), .out17(Bitmap_Instruccion[11]), .out18(Bitmap_Instruccion[12]),
    .out19(Bitmap_Instruccion[13]), .out20(decoder_4_out20), .out21(decoder_4_out21),
    .out22(decoder_4_out22), .out23(decoder_4_out23), .out24(Bitmap_Instruccion[14]),
    .out25(Bitmap_Instruccion[15]), .out26(Bitmap_Instruccion[16]), .out27(Bitmap_Instruccion[17]),
    .out28(decoder_4_out28), .out29(decoder_4_out29), .out30(decoder_4_out30), .out31(decoder_4_out31),
    .sel(bit_extender_3_out), .en(demultiplexer_1_out0));
  or or_12 (Instruccion_Desconocida_E, demultiplexer_1_out3, demultiplexer_1_out2);
  Decoder #(.select(5)) decoder_5 (
    .out0(Bitmap_Instruccion[18]), .out1(Bitmap_Instruccion[19]), .out2(Bitmap_Instruccion[20]),
    .out3(Bitmap_Instruccion[21]), .out4(Bitmap_Instruccion[22]), .out5(Bitmap_Instruccion[23]),
    .out6(Bitmap_Instruccion[24]), .out7(Bitmap_Instruccion[25]), .out8(decoder_5_out8),
    .out9(decoder_5_out9), .out10(Bitmap_Instruccion[26]), .out11(Bitmap_Instruccion[27]),
    .out12(decoder_5_out12), .out13(decoder_5_out13), .out14(decoder_5_out14), .out15(decoder_5_out15),
    .out16(decoder_5_out16), .out17(decoder_5_out17), .out18(decoder_5_out18), .out19(decoder_5_out19),
    .out20(decoder_5_out20), .out21(decoder_5_out21), .out22(decoder_5_out22), .out23(decoder_5_out23),
    .out24(decoder_5_out24), .out25(decoder_5_out25), .out26(decoder_5_out26), .out27(decoder_5_out27),
    .out28(decoder_5_out28), .out29(decoder_5_out29), .out30(decoder_5_out30), .out31(decoder_5_out31),
    .sel(bit_extender_3_out), .en(demultiplexer_1_out1));
  or or_13 (or_13_out, decoder_5_out8, decoder_5_out9);
  or or_14 (or_14_out, decoder_5_out12, decoder_5_out13, decoder_5_out14, decoder_5_out15, decoder_5_out16, decoder_5_out17, decoder_5_out18, decoder_5_out19, decoder_5_out20, decoder_5_out21, decoder_5_out22, decoder_5_out23, decoder_5_out24, decoder_5_out25, decoder_5_out26, decoder_5_out27, decoder_5_out28, decoder_5_out29, decoder_5_out30, decoder_5_out31);
  or or_15 (Instruccion_Desconocida_D, or_14_out, or_13_out);

  // Other names for the same wires on the sheet: Instruccion_Desconocida = Bitmap_Instruccion[0];
  //   R_SLL = Bitmap_Instruccion[1]; R_SRL = Bitmap_Instruccion[2]; R_SRA = Bitmap_Instruccion[3];
  //   R_SLLV = Bitmap_Instruccion[4]; R_SRLV = Bitmap_Instruccion[5]; R_SRAV = Bitmap_Instruccion[6];
  //   R_JR = Bitmap_Instruccion[7]; R_JALR = Bitmap_Instruccion[8]; R_SYS = Bitmap_Instruccion[9];
  //   R_MFHI = Bitmap_Instruccion[10]; R_MTHI = Bitmap_Instruccion[11]; R_MFLO = Bitmap_Instruccion[12];
  //   R_MTLO = Bitmap_Instruccion[13]; R_MULT = Bitmap_Instruccion[14]; R_MULT_U = Bitmap_Instruccion[15];
  //   R_DIV = Bitmap_Instruccion[16]; R_DIV_U = Bitmap_Instruccion[17]; R_ADD = Bitmap_Instruccion[18];
  //   R_ADD_U = Bitmap_Instruccion[19]; R_SUB = Bitmap_Instruccion[20]; R_SUB_U = Bitmap_Instruccion[21];
  //   R_AND = Bitmap_Instruccion[22]; R_OR = Bitmap_Instruccion[23]; R_XOR = Bitmap_Instruccion[24];
  //   R_NOR = Bitmap_Instruccion[25]; R_SLT = Bitmap_Instruccion[26]; R_SLT_U = Bitmap_Instruccion[27];
  //   J_J = Bitmap_Instruccion[28]; J_JAL = Bitmap_Instruccion[29]; I_BEQ = Bitmap_Instruccion[30];
  //   I_BNE = Bitmap_Instruccion[31]; I_BLEZ = Bitmap_Instruccion[32]; I_BGTZ = Bitmap_Instruccion[33];
  //   I_ADD = Bitmap_Instruccion[34]; I_ADD_U = Bitmap_Instruccion[35]; I_SLT = Bitmap_Instruccion[36];
  //   I_SLT_U = Bitmap_Instruccion[37]; I_AND = Bitmap_Instruccion[38]; I_OR = Bitmap_Instruccion[39];
  //   I_XOR = Bitmap_Instruccion[40]; I_LUI = Bitmap_Instruccion[41]; I_LB = Bitmap_Instruccion[42];
  //   I_LH = Bitmap_Instruccion[43]; I_LW = Bitmap_Instruccion[44]; I_LB_U = Bitmap_Instruccion[45];
  //   I_LH_U = Bitmap_Instruccion[46]; I_SB = Bitmap_Instruccion[47]; I_SH = Bitmap_Instruccion[48];
  //   I_SW = Bitmap_Instruccion[49]

  // Notes on the sheet:
  //   Respuestas
  //   Segmentos de identidad
  //   Detección por tipo general
  //   Detección por subtipo aritmético
endmodule

module MIPS_Instruction_Decoder (
  input  [31:0] Instruccion,
  output [49:0] Bitmap_Instruccion,
  output [25:0] Direccion_Inmediata,
  output [15:0] Valor_Inmediato,
  output [4:0] Cantidad_Corrimiento,
  output [4:0] Registro_Fuente,
  output [4:0] Registro_Objetivo,
  output [4:0] Registro_Destino,
  output [1:0] Escribir_LOHI,
  output [1:0] Leer_LOHI,
  output [7:0] Bitmap_Acceso_Memoria
);

  wire not_1_out, not_2_out, not_3_out, not_4_out, not_5_out, not_6_out, not_7_out, or_1_out, or_2_out,
       or_3_out, or_4_out, or_5_out, or_6_out, or_7_out, priority_encoder_1_en_out, priority_encoder_1_out,
       priority_encoder_2_en_out, priority_encoder_3_en_out, priority_encoder_3_out,
       priority_encoder_4_en_out, priority_encoder_4_out, priority_encoder_5_en_out, priority_encoder_5_out,
       priority_encoder_6_en_out, priority_encoder_6_out, priority_encoder_7_en_out, priority_encoder_7_out;
  wire [1:0] priority_encoder_2_out;

  // MIPS_Instruction_Detector Detector_Instrucciones: pin names not known; wires that end beside it: Instruccion[31:26], Instruccion[6:0], {Bitmap_Acceso_Memoria, Bitmap_Instruccion[41:0]}
  or or_1 (or_1_out, Bitmap_Instruccion[27], Bitmap_Instruccion[26], Bitmap_Instruccion[25], Bitmap_Instruccion[24], Bitmap_Instruccion[23], Bitmap_Instruccion[22], Bitmap_Instruccion[21], Bitmap_Instruccion[20], Bitmap_Instruccion[19], Bitmap_Instruccion[18], Bitmap_Instruccion[12], Bitmap_Instruccion[10], Bitmap_Instruccion[8], Bitmap_Instruccion[6], Bitmap_Instruccion[5], Bitmap_Instruccion[4], Bitmap_Instruccion[3], Bitmap_Instruccion[2], Bitmap_Instruccion[1]);
  or or_2 (or_2_out, Bitmap_Acceso_Memoria[7], Bitmap_Acceso_Memoria[6], Bitmap_Acceso_Memoria[5], Bitmap_Instruccion[31], Bitmap_Instruccion[30], Bitmap_Instruccion[27], Bitmap_Instruccion[26], Bitmap_Instruccion[25], Bitmap_Instruccion[24], Bitmap_Instruccion[23], Bitmap_Instruccion[22], Bitmap_Instruccion[21], Bitmap_Instruccion[20], Bitmap_Instruccion[19], Bitmap_Instruccion[18], Bitmap_Instruccion[17], Bitmap_Instruccion[16], Bitmap_Instruccion[15], Bitmap_Instruccion[14], Bitmap_Instruccion[6], Bitmap_Instruccion[5], Bitmap_Instruccion[4], Bitmap_Instruccion[3], Bitmap_Instruccion[2], Bitmap_Instruccion[1]);
  or or_3 (or_3_out, Bitmap_Acceso_Memoria[7], Bitmap_Acceso_Memoria[6], Bitmap_Acceso_Memoria[5], Bitmap_Instruccion[33], Bitmap_Instruccion[32], Bitmap_Instruccion[31], Bitmap_Instruccion[30], Bitmap_Instruccion[28], Bitmap_Instruccion[17], Bitmap_Instruccion[16], Bitmap_Instruccion[15], Bitmap_Instruccion[14], Bitmap_Instruccion[13], Bitmap_Instruccion[11], Bitmap_Instruccion[9], Bitmap_Instruccion[7], Bitmap_Instruccion[0]);
  Priority_Encoder #(.select(1)) priority_encoder_1 (
    .in0(Bitmap_Instruccion[0]), .in1(or_2_out), .out(priority_encoder_1_out),
    .en_out(priority_encoder_1_en_out), .en_in(1'b1));  // open: gs
  not not_1 (not_1_out, priority_encoder_1_en_out);
  Multiplexer #(.enable("true"), .width(5)) multiplexer_1 (
    .in0({5{1'b0}}), .in1(Instruccion[20:16]), .out(Registro_Objetivo), .sel(priority_encoder_1_out),
    .en(not_1_out));
  or or_4 (or_4_out, Bitmap_Acceso_Memoria[4], Bitmap_Acceso_Memoria[3], Bitmap_Acceso_Memoria[2], Bitmap_Acceso_Memoria[1], Bitmap_Acceso_Memoria[0], Bitmap_Instruccion[41], Bitmap_Instruccion[40], Bitmap_Instruccion[39], Bitmap_Instruccion[38], Bitmap_Instruccion[37], Bitmap_Instruccion[36], Bitmap_Instruccion[35], Bitmap_Instruccion[34]);
  Priority_Encoder #(.select(2)) priority_encoder_2 (
    .in0(Bitmap_Instruccion[29]), .in1(or_4_out), .in2(or_3_out), .in3(or_1_out),
    .out(priority_encoder_2_out), .en_out(priority_encoder_2_en_out), .en_in(1'b1));  // open: gs
  not not_2 (not_2_out, priority_encoder_2_en_out);
  Multiplexer #(.enable("true"), .select(2), .width(5)) multiplexer_2 (
    .in0({5{1'b1}}), .in1(Instruccion[20:16]), .in2({5{1'b0}}), .in3(Instruccion[16:12]),
    .out(Registro_Destino), .sel(priority_encoder_2_out), .en(not_2_out));
  or or_5 (or_5_out, Bitmap_Acceso_Memoria[7], Bitmap_Acceso_Memoria[6], Bitmap_Acceso_Memoria[5], Bitmap_Acceso_Memoria[4], Bitmap_Acceso_Memoria[3], Bitmap_Acceso_Memoria[2], Bitmap_Acceso_Memoria[1], Bitmap_Acceso_Memoria[0], Bitmap_Instruccion[40], Bitmap_Instruccion[39], Bitmap_Instruccion[38], Bitmap_Instruccion[37], Bitmap_Instruccion[36], Bitmap_Instruccion[35], Bitmap_Instruccion[34], Bitmap_Instruccion[33], Bitmap_Instruccion[32], Bitmap_Instruccion[31], Bitmap_Instruccion[30], Bitmap_Instruccion[27], Bitmap_Instruccion[26], Bitmap_Instruccion[25], Bitmap_Instruccion[24], Bitmap_Instruccion[23], Bitmap_Instruccion[22], Bitmap_Instruccion[21], Bitmap_Instruccion[20], Bitmap_Instruccion[19], Bitmap_Instruccion[18], Bitmap_Instruccion[17], Bitmap_Instruccion[16], Bitmap_Instruccion[15], Bitmap_Instruccion[14], Bitmap_Instruccion[13], Bitmap_Instruccion[11], Bitmap_Instruccion[8], Bitmap_Instruccion[7], Bitmap_Instruccion[6], Bitmap_Instruccion[5], Bitmap_Instruccion[4]);
  Priority_Encoder #(.select(1)) priority_encoder_3 (
    .in0(Bitmap_Instruccion[0]), .in1(or_5_out), .out(priority_encoder_3_out),
    .en_out(priority_encoder_3_en_out), .en_in(1'b1));  // open: gs
  not not_3 (not_3_out, priority_encoder_3_en_out);
  Multiplexer #(.enable("true"), .width(5)) multiplexer_3 (
    .in0({5{1'b0}}), .in1(Instruccion[25:21]), .out(Registro_Fuente), .sel(priority_encoder_3_out),
    .en(not_3_out));
  or or_6 (or_6_out, Bitmap_Instruccion[17], Bitmap_Instruccion[16], Bitmap_Instruccion[15], Bitmap_Instruccion[14], Bitmap_Instruccion[11]);
  or or_7 (or_7_out, Bitmap_Instruccion[17], Bitmap_Instruccion[16], Bitmap_Instruccion[15], Bitmap_Instruccion[14], Bitmap_Instruccion[13]);
  Priority_Encoder #(.select(1)) priority_encoder_4 (
    .in0(Bitmap_Instruccion[0]), .in1(or_6_out), .out(priority_encoder_4_out),
    .en_out(priority_encoder_4_en_out), .en_in(1'b1));  // open: gs
  not not_4 (not_4_out, priority_encoder_4_en_out);
  Multiplexer #(.enable("true")) multiplexer_4 (
    .in0(1'b0), .in1(1'b1), .out(Escribir_LOHI[1]), .sel(priority_encoder_4_out), .en(not_4_out));
  Priority_Encoder #(.select(1)) priority_encoder_5 (
    .in0(Bitmap_Instruccion[0]), .in1(or_7_out), .out(priority_encoder_5_out),
    .en_out(priority_encoder_5_en_out), .en_in(1'b1));  // open: gs
  not not_5 (not_5_out, priority_encoder_5_en_out);
  Multiplexer #(.enable("true")) multiplexer_5 (
    .in0(1'b0), .in1(1'b1), .out(Escribir_LOHI[0]), .sel(priority_encoder_5_out), .en(not_5_out));
  Priority_Encoder #(.select(1)) priority_encoder_6 (
    .in0(Bitmap_Instruccion[0]), .in1(Bitmap_Instruccion[10]), .out(priority_encoder_6_out),
    .en_out(priority_encoder_6_en_out), .en_in(1'b1));  // open: gs
  not not_6 (not_6_out, priority_encoder_6_en_out);
  Multiplexer #(.enable("true")) multiplexer_6 (
    .in0(1'b0), .in1(1'b1), .out(Leer_LOHI[1]), .sel(priority_encoder_6_out), .en(not_6_out));
  Priority_Encoder #(.select(1)) priority_encoder_7 (
    .in0(Bitmap_Instruccion[0]), .in1(Bitmap_Instruccion[12]), .out(priority_encoder_7_out),
    .en_out(priority_encoder_7_en_out), .en_in(1'b1));  // open: gs
  not not_7 (not_7_out, priority_encoder_7_en_out);
  Multiplexer #(.enable("true")) multiplexer_7 (
    .in0(1'b0), .in1(1'b1), .out(Leer_LOHI[0]), .sel(priority_encoder_7_out), .en(not_7_out));

  assign Bitmap_Instruccion[49:42] = Bitmap_Acceso_Memoria;
  assign Cantidad_Corrimiento = Instruccion[11:7];
  assign Direccion_Inmediata = Instruccion[25:0];
  assign Valor_Inmediato = Instruccion[15:0];

  // Other names for the same wires on the sheet: I_LB = Bitmap_Acceso_Memoria[0]; I_LH = Bitmap_Acceso_Memoria[1];
  //   I_LW = Bitmap_Acceso_Memoria[2]; I_LB_U = Bitmap_Acceso_Memoria[3]; I_LH_U = Bitmap_Acceso_Memoria[4];
  //   I_SB = Bitmap_Acceso_Memoria[5]; I_SH = Bitmap_Acceso_Memoria[6]; I_SW = Bitmap_Acceso_Memoria[7];
  //   Instruccion_Desconocida = Bitmap_Instruccion[0]; R_SLL = Bitmap_Instruccion[1]; R_SRL = Bitmap_Instruccion[2];
  //   R_SRA = Bitmap_Instruccion[3]; R_SLLV = Bitmap_Instruccion[4]; R_SRLV = Bitmap_Instruccion[5];
  //   R_SRAV = Bitmap_Instruccion[6]; R_JR = Bitmap_Instruccion[7]; R_JALR = Bitmap_Instruccion[8];
  //   R_SYS = Bitmap_Instruccion[9]; R_MFHI = Bitmap_Instruccion[10]; R_MTHI = Bitmap_Instruccion[11];
  //   R_MFLO = Bitmap_Instruccion[12]; R_MTLO = Bitmap_Instruccion[13]; R_MULT = Bitmap_Instruccion[14];
  //   R_MULT_U = Bitmap_Instruccion[15]; R_DIV = Bitmap_Instruccion[16]; R_DIV_U = Bitmap_Instruccion[17];
  //   R_ADD = Bitmap_Instruccion[18]; R_ADD_U = Bitmap_Instruccion[19]; R_SUB = Bitmap_Instruccion[20];
  //   R_SUB_U = Bitmap_Instruccion[21]; R_AND = Bitmap_Instruccion[22]; R_OR = Bitmap_Instruccion[23];
  //   R_XOR = Bitmap_Instruccion[24]; R_NOR = Bitmap_Instruccion[25]; R_SLT = Bitmap_Instruccion[26];
  //   R_SLT_U = Bitmap_Instruccion[27]; J_J = Bitmap_Instruccion[28]; J_JAL = Bitmap_Instruccion[29];
  //   I_BEQ = Bitmap_Instruccion[30]; I_BNE = Bitmap_Instruccion[31]; I_BLEZ = Bitmap_Instruccion[32];
  //   I_BGTZ = Bitmap_Instruccion[33]; I_ADD = Bitmap_Instruccion[34]; I_ADD_U = Bitmap_Instruccion[35];
  //   I_SLT = Bitmap_Instruccion[36]; I_SLT_U = Bitmap_Instruccion[37]; I_AND = Bitmap_Instruccion[38];
  //   I_OR = Bitmap_Instruccion[39]; I_XOR = Bitmap_Instruccion[40]; I_LUI = Bitmap_Instruccion[41];
  //   Candidato_Registro_Destino[4:0] = Instruccion[16:12]; Candidato_Registro_Objetivo[4:0] = Instruccion[20:16];
  //   Candidato_Registro_Fuente[4:0] = Instruccion[25:21]; Escribir_LO = Escribir_LOHI[0];
  //   Escribir_HI = Escribir_LOHI[1]; Funcion_Aritmetica[6:0] = Instruccion[6:0]; Leer_LO = Leer_LOHI[0];
  //   Leer_HI = Leer_LOHI[1]; Tipo_Operacion[5:0] = Instruccion[31:26]
endmodule

module MIPS_ALU (
  input  [49:0] Bitmap_Instruccion,
  input  [4:0] Cantidad_Corrimiento,
  input  [31:0] Contenido_Registro_Fuente,
  input  [31:0] Contenido_Registro_Objetivo,
  input  [31:0] Contenido_Previo_HI,
  input  [31:0] Contenido_Previo_LO,
  input  [15:0] Valor_Inmediato,
  input  [25:0] Direccion_Inmediata,
  input  [31:0] Indice_PC,
  output [31:0] Salida_HI,
  output [31:0] Salida_LO,
  output [31:0] Salida_Calculo,
  output [31:0] Direccion_Memoria,
  output Overflow,
  output Tomar_Salto,
  output Alineamiento_Memoria
);

  wire adder_4_cout, adder_5_cout, Alineamiento_Memoria_Halfword, Alineamiento_Memoria_Word, and_4_out,
       bit_extender_8_out, comparator_1_gt, comparator_1_lt, comparator_2_gt, comparator_2_lt,
       comparator_3_eq, comparator_3_gt, comparator_4_eq, comparator_4_lt, comparator_5_eq, comparator_5_gt,
       comparator_7_eq, multiplexer_3_out, not_2_out, not_3_out, not_4_out, not_5_out, not_6_out, not_7_out,
       not_8_out, not_9_out, or_4_out, or_5_out, or_6_out, or_7_out, or_8_out, or_10_out, or_11_out,
       or_12_out, or_13_out, or_14_out, or_15_out, or_16_out, or_18_out, or_19_out, or_20_out, or_21_out,
       or_22_out, or_23_out, or_25_out, or_26_out, Origen_Es_Igual, Origen_Es_Mayor, Origen_Es_Mayor_Cero,
       Origen_Es_Mayor_U, Origen_Es_Menor, Origen_Es_Menor_I, Origen_Es_Menor_I_U,
       Origen_Es_Menor_Igual_Cero, Origen_Es_Menor_U, Overflow_Acceso_Memoria, Overflow_ADD, Overflow_ADD_I,
       Overflow_Direccion_Previo_Salto_JAL_JALR, Overflow_Salto_Condicional, Overflow_Salto_J_JAL,
       Overflow_SUB, priority_encoder_1_en_out, priority_encoder_2_en_out, priority_encoder_3_en_out,
       priority_encoder_4_en_out, priority_encoder_5_en_out, priority_encoder_6_en_out,
       priority_encoder_7_en_out;
  wire [1:0] bit_extender_9_out, priority_encoder_1_out, priority_encoder_4_out, priority_encoder_5_out,
       priority_encoder_6_out;
  wire [2:0] priority_encoder_2_out, priority_encoder_3_out;
  wire [4:0] bit_extender_2_out, bit_extender_4_out, bit_extender_5_out, priority_encoder_7_out;
  wire [15:0] multiplier_3_cout, multiplier_3_out;
  wire [27:0] bit_extender_1_out, shifter_2_out;
  wire [31:0] adder_1_out, adder_4_out, and_1_out, bit_extender_3_out, bit_extender_10_out,
       bit_extender_11_out, bit_extender_12_out, bit_extender_13_out, Cociente_DIV, Cociente_DIV_U,
       Direccion_Acceso_Memoria, Direccion_Previo_Salto_JAL_JALR, Direccion_Salto_Condicional,
       Direccion_Salto_J_JAL, Inmediato_Extendido, Inmediato_Extendido_U, Parte_Inferior_MULT,
       Parte_Inferior_MULT_U, Parte_Superior_MULT, Parte_Superior_MULT_U, Residuo_DIV, Residuo_DIV_U,
       Resultado_ADD, Resultado_ADD_I, Resultado_AND, Resultado_AND_I, Resultado_LUI, Resultado_NOR,
       Resultado_OR, Resultado_OR_I, Resultado_SLL, Resultado_SLLV, Resultado_SRA, Resultado_SRAV,
       Resultado_SRL, Resultado_SRLV, Resultado_SUB, Resultado_XOR, Resultado_XOR_I;

  assign bit_extender_1_out = {{2{1'b0}}, Direccion_Inmediata};  // Bit_Extender bit_extender_1
  Bit_Extender #(.in_width(32), .out_width(5), .\type ("zero")) bit_extender_2 (
    .in(Contenido_Registro_Fuente), .out(bit_extender_2_out));
  Shifter #(.width(32)) shifter_1 (.in(Inmediato_Extendido_U), .\dist (5'b10000), .out(Resultado_LUI));
  Shifter #(.width(28)) shifter_2 (.in(bit_extender_1_out), .\dist (5'b00010), .out(shifter_2_out));
  assign and_1_out = 32'hf0000000 & adder_1_out;  // AND_Gate and_1, 32 bits wide
  Adder #(.width(32)) adder_1 (.a(32'h4), .b(Indice_PC), .out(adder_1_out), .cin(1'b0), .cout(Overflow_Salto_J_JAL));
  assign Resultado_AND = Contenido_Registro_Fuente & Contenido_Registro_Objetivo;  // AND_Gate and_2, 32 bits wide
  assign Resultado_XOR = Contenido_Registro_Fuente ^ Contenido_Registro_Objetivo;  // XOR_Gate xor_1, 32 bits wide
  Shifter #(.width(32)) shifter_3 (
    .in(Contenido_Registro_Objetivo), .\dist (Cantidad_Corrimiento), .out(Resultado_SLL));
  Shifter #(.width(32)) shifter_4 (.in(Contenido_Registro_Objetivo), .\dist (bit_extender_2_out), .out(Resultado_SLLV));
  Shifter #(.shift("ar"), .width(32)) shifter_5 (
    .in(Contenido_Registro_Objetivo), .\dist (Cantidad_Corrimiento), .out(Resultado_SRA));
  assign Resultado_AND_I = Contenido_Registro_Fuente & Inmediato_Extendido_U;  // AND_Gate and_3, 32 bits wide
  assign Resultado_XOR_I = Contenido_Registro_Fuente ^ Inmediato_Extendido_U;  // XOR_Gate xor_2, 32 bits wide
  assign bit_extender_3_out = {{4{1'b0}}, shifter_2_out};  // Bit_Extender bit_extender_3
  assign Direccion_Salto_J_JAL = bit_extender_3_out | and_1_out;  // OR_Gate or_1, 32 bits wide
  Bit_Extender #(.in_width(32), .out_width(5), .\type ("zero")) bit_extender_4 (
    .in(Contenido_Registro_Fuente), .out(bit_extender_4_out));
  Bit_Extender #(.in_width(32), .out_width(5), .\type ("zero")) bit_extender_5 (
    .in(Contenido_Registro_Fuente), .out(bit_extender_5_out));
  assign Resultado_OR = Contenido_Registro_Fuente | Contenido_Registro_Objetivo;  // OR_Gate or_2, 32 bits wide
  assign Resultado_NOR = ~Resultado_OR;  // NOT_Gate not_1, 32 bits wide
  Shifter #(.shift("lr"), .width(32)) shifter_6 (
    .in(Contenido_Registro_Objetivo), .\dist (Cantidad_Corrimiento), .out(Resultado_SRL));
  Shifter #(.shift("ar"), .width(32)) shifter_7 (
    .in(Contenido_Registro_Objetivo), .\dist (bit_extender_5_out), .out(Resultado_SRAV));
  Shifter #(.shift("lr"), .width(32)) shifter_8 (
    .in(Contenido_Registro_Objetivo), .\dist (bit_extender_4_out), .out(Resultado_SRLV));
  assign Resultado_OR_I = Contenido_Registro_Fuente | Inmediato_Extendido_U;  // OR_Gate or_3, 32 bits wide
  assign Inmediato_Extendido = {{16{Valor_Inmediato[15]}}, Valor_Inmediato};  // Bit_Extender bit_extender_6
  assign Inmediato_Extendido_U = {{16{1'b0}}, Valor_Inmediato};  // Bit_Extender bit_extender_7
  or or_4 (or_4_out, Bitmap_Instruccion[49], Bitmap_Instruccion[48], Bitmap_Instruccion[47], Bitmap_Instruccion[46], Bitmap_Instruccion[45], Bitmap_Instruccion[44], Bitmap_Instruccion[43], Bitmap_Instruccion[42]);
  or or_5 (or_5_out, Bitmap_Instruccion[33], Bitmap_Instruccion[32], Bitmap_Instruccion[31], Bitmap_Instruccion[30]);
  or or_6 (or_6_out, Bitmap_Instruccion[8], Bitmap_Instruccion[7]);
  Bit_Extender #(.in_width(32), .out_width(1), .\type ("zero")) bit_extender_8 (
    .in(Direccion_Memoria), .out(bit_extender_8_out));
  Bit_Extender #(.in_width(32), .out_width(2), .\type ("zero")) bit_extender_9 (
    .in(Direccion_Memoria), .out(bit_extender_9_out));
  // NoConnect on comparator_1_gt
  Comparator #(.width(1)) comparator_1 (
    .a(bit_extender_8_out), .b(1'b0), .gt(comparator_1_gt), .eq(Alineamiento_Memoria_Halfword),
    .lt(comparator_1_lt));
  // NoConnect on comparator_1_lt
  // NoConnect on comparator_2_gt
  Comparator #(.width(2)) comparator_2 (
    .a(bit_extender_9_out), .b(2'b00), .gt(comparator_2_gt), .eq(Alineamiento_Memoria_Word),
    .lt(comparator_2_lt));
  // NoConnect on comparator_2_lt
  or or_7 (or_7_out, Bitmap_Instruccion[29], Bitmap_Instruccion[28]);
  Priority_Encoder #(.select(2)) priority_encoder_1 (
    .in0(or_7_out), .in1(or_6_out), .in2(or_5_out), .in3(or_4_out), .out(priority_encoder_1_out),
    .en_out(priority_encoder_1_en_out), .en_in(1'b1));  // open: gs
  Adder #(.width(32)) adder_2 (
    .a(Contenido_Registro_Fuente), .b(Contenido_Registro_Objetivo), .out(Resultado_ADD), .cin(1'b0),
    .cout(Overflow_ADD));
  Multiplier #(.mode("twosComplement"), .width(32)) multiplier_1 (
    .a(Contenido_Registro_Fuente), .b(Contenido_Registro_Objetivo), .out(Parte_Inferior_MULT),
    .cin({32{1'b0}}), .cout(Parte_Superior_MULT));
  Adder #(.width(32)) adder_3 (
    .a(Contenido_Registro_Fuente), .b(Inmediato_Extendido), .out(Resultado_ADD_I), .cin(1'b0),
    .cout(Overflow_ADD_I));
  not not_2 (not_2_out, priority_encoder_1_en_out);
  Multiplexer #(.enable("true"), .select(2), .width(32)) multiplexer_1 (
    .in0(Direccion_Salto_J_JAL), .in1(Contenido_Registro_Fuente), .in2(Direccion_Salto_Condicional),
    .in3(Direccion_Acceso_Memoria), .out(Direccion_Memoria), .sel(priority_encoder_1_out), .en(not_2_out));
  Divider #(.mode("twosComplement"), .width(32)) divider_1 (
    .a(Contenido_Registro_Fuente), .b(Contenido_Registro_Objetivo), .out(Cociente_DIV), .upper({32{1'b0}}),
    .rem(Residuo_DIV));
  or or_8 (or_8_out, Bitmap_Instruccion[33], Bitmap_Instruccion[32], Bitmap_Instruccion[31], Bitmap_Instruccion[30], Bitmap_Instruccion[8], Bitmap_Instruccion[29], Bitmap_Instruccion[7], Bitmap_Instruccion[28]);
  Subtractor #(.width(32)) subtractor_1 (
    .a(Contenido_Registro_Fuente), .b(Contenido_Registro_Objetivo), .out(Resultado_SUB), .bin(1'b0),
    .bout(Overflow_SUB));
  Multiplier #(.width(32)) multiplier_2 (
    .a(Contenido_Registro_Fuente), .b(Contenido_Registro_Objetivo), .out(Parte_Inferior_MULT_U),
    .cin({32{1'b0}}), .cout(Parte_Superior_MULT_U));
  // NoConnect on comparator_3_gt
  // NoConnect on comparator_3_eq
  Comparator #(.width(32)) comparator_3 (
    .a(Contenido_Registro_Fuente), .b(Inmediato_Extendido), .gt(comparator_3_gt), .eq(comparator_3_eq),
    .lt(Origen_Es_Menor_I));
  not not_3 (not_3_out, Origen_Es_Igual);
  Divider #(.mode("twosComplement"), .width(32)) divider_2 (
    .a(Contenido_Registro_Fuente), .b(Contenido_Registro_Objetivo), .out(Cociente_DIV_U), .upper({32{1'b0}}),
    .rem(Residuo_DIV_U));
  Comparator #(.width(32)) comparator_4 (
    .a(Contenido_Registro_Fuente), .b({32{1'b0}}), .gt(Origen_Es_Mayor_Cero), .eq(comparator_4_eq),
    .lt(comparator_4_lt));
  or or_9 (Origen_Es_Menor_Igual_Cero, comparator_4_lt, comparator_4_eq);
  or or_10 (or_10_out, Bitmap_Instruccion[29], Bitmap_Instruccion[28], Bitmap_Instruccion[8], Bitmap_Instruccion[7]);
  or or_11 (or_11_out, Bitmap_Instruccion[33], Bitmap_Instruccion[32], Bitmap_Instruccion[31], Bitmap_Instruccion[30]);
  or or_12 (or_12_out, Bitmap_Instruccion[45], Bitmap_Instruccion[42], Bitmap_Instruccion[47]);
  not not_4 (not_4_out, priority_encoder_2_en_out);
  Priority_Encoder priority_encoder_2 (
    .in0(or_10_out), .in1(Bitmap_Instruccion[30]), .in2(Bitmap_Instruccion[31]),
    .in3(Bitmap_Instruccion[32]), .in4(Bitmap_Instruccion[33]), .in5(1'b0), .in6(1'b0), .in7(1'b0),
    .out(priority_encoder_2_out), .en_in(1'b1), .en_out(priority_encoder_2_en_out));  // open: gs
  Multiplexer #(.enable("true"), .select(3)) multiplexer_2 (
    .in0(1'b1), .in1(Origen_Es_Igual), .in2(not_3_out), .in3(Origen_Es_Menor_Igual_Cero),
    .in4(Origen_Es_Mayor_Cero), .in5(1'b0), .in6(1'b0), .in7(1'b0), .out(Tomar_Salto),
    .sel(priority_encoder_2_out), .en(not_4_out));
  or or_13 (or_13_out, Bitmap_Instruccion[8], Bitmap_Instruccion[29]);
  or or_14 (or_14_out, Bitmap_Instruccion[46], Bitmap_Instruccion[43], Bitmap_Instruccion[48]);
  or or_15 (or_15_out, Bitmap_Instruccion[49], Bitmap_Instruccion[48], Bitmap_Instruccion[47], Bitmap_Instruccion[46], Bitmap_Instruccion[45], Bitmap_Instruccion[44], Bitmap_Instruccion[43], Bitmap_Instruccion[42]);
  or or_16 (or_16_out, Bitmap_Instruccion[49], Bitmap_Instruccion[44]);
  and and_4 (and_4_out, Alineamiento_Memoria_Word, Tomar_Salto);
  not not_5 (not_5_out, priority_encoder_3_en_out);
  Priority_Encoder priority_encoder_3 (
    .in0(or_15_out), .in1(or_13_out), .in2(or_11_out), .in3(Bitmap_Instruccion[34]),
    .in4(Bitmap_Instruccion[20]), .in5(Bitmap_Instruccion[18]), .in6(Bitmap_Instruccion[16]), .in7(1'b0),
    .out(priority_encoder_3_out), .en_in(1'b1), .en_out(priority_encoder_3_en_out));  // open: gs
  not not_6 (not_6_out, priority_encoder_4_en_out);
  Priority_Encoder #(.select(2)) priority_encoder_4 (
    .in0(or_16_out), .in1(or_14_out), .in2(or_12_out), .in3(or_8_out), .out(priority_encoder_4_out),
    .en_out(priority_encoder_4_en_out), .en_in(1'b1));  // open: gs
  Multiplexer #(.enable("true"), .select(2)) multiplexer_3 (
    .in0(Alineamiento_Memoria_Word), .in1(Alineamiento_Memoria_Halfword), .in2(1'b1), .in3(and_4_out),
    .out(multiplexer_3_out), .sel(priority_encoder_4_out), .en(not_6_out));
  // NoConnect on comparator_5_gt
  // NoConnect on comparator_5_eq
  Comparator #(.mode("unsigned"), .width(32)) comparator_5 (
    .a(Contenido_Registro_Fuente), .b(Inmediato_Extendido), .gt(comparator_5_gt), .eq(comparator_5_eq),
    .lt(Origen_Es_Menor_I_U));
  Multiplexer #(.enable("true"), .select(3)) multiplexer_4 (
    .in0(Overflow_Acceso_Memoria), .in1(Overflow_Direccion_Previo_Salto_JAL_JALR),
    .in2(Overflow_Salto_Condicional), .in3(Overflow_ADD_I), .in4(Overflow_SUB), .in5(Overflow_ADD),
    .in6(1'b0), .in7(1'b0), .out(Overflow), .sel(priority_encoder_3_out), .en(not_5_out));
  or or_17 (Alineamiento_Memoria, priority_encoder_4_en_out, multiplexer_3_out);
  Comparator #(.width(32)) comparator_6 (
    .a(Contenido_Registro_Fuente), .b(Contenido_Registro_Objetivo), .gt(Origen_Es_Mayor),
    .eq(Origen_Es_Igual), .lt(Origen_Es_Menor));
  // NoConnect on comparator_7_eq
  Comparator #(.mode("unsigned"), .width(32)) comparator_7 (
    .a(Contenido_Registro_Fuente), .b(Contenido_Registro_Objetivo), .gt(Origen_Es_Mayor_U),
    .eq(comparator_7_eq), .lt(Origen_Es_Menor_U));
  or or_18 (or_18_out, Bitmap_Instruccion[8], Bitmap_Instruccion[29]);
  or or_19 (or_19_out, Bitmap_Instruccion[15], Bitmap_Instruccion[14]);
  or or_20 (or_20_out, Bitmap_Instruccion[19], Bitmap_Instruccion[18]);
  or or_21 (or_21_out, Bitmap_Instruccion[17], Bitmap_Instruccion[16]);
  or or_22 (or_22_out, Bitmap_Instruccion[35], Bitmap_Instruccion[34]);
  Multiplier #(.mode("twosComplement"), .width(16)) multiplier_3 (
    .a(Valor_Inmediato), .b(16'h4), .out(multiplier_3_out), .cin({16{1'b0}}), .cout(multiplier_3_cout));
  not not_7 (not_7_out, priority_encoder_5_en_out);
  Priority_Encoder #(.select(2)) priority_encoder_5 (
    .in0(or_21_out), .in1(or_19_out), .in2(Bitmap_Instruccion[11]), .in3(1'b0), .out(priority_encoder_5_out),
    .en_out(priority_encoder_5_en_out), .en_in(1'b1));  // open: gs
  Multiplexer #(.enable("true"), .select(2), .width(32)) multiplexer_5 (
    .in0(Cociente_DIV), .in1(Parte_Superior_MULT), .in2(Contenido_Registro_Fuente), .in3({32{1'b0}}),
    .out(Salida_HI), .sel(priority_encoder_5_out), .en(not_7_out));
  or or_23 (or_23_out, Bitmap_Instruccion[21], Bitmap_Instruccion[20]);
  Adder #(.width(32)) adder_4 (
    .a({multiplier_3_cout, multiplier_3_out}), .b(Indice_PC), .out(adder_4_out), .cin(1'b0),
    .cout(adder_4_cout));
  Adder #(.width(32)) adder_5 (
    .a(32'h4), .b(adder_4_out), .out(Direccion_Salto_Condicional), .cin(1'b0), .cout(adder_5_cout));
  or or_24 (Overflow_Salto_Condicional, adder_5_cout, adder_4_cout);
  assign bit_extender_10_out = {{31{1'b0}}, Origen_Es_Menor};  // Bit_Extender bit_extender_10
  or or_25 (or_25_out, Bitmap_Instruccion[15], Bitmap_Instruccion[14]);
  assign bit_extender_11_out = {{31{1'b0}}, Origen_Es_Menor_U};  // Bit_Extender bit_extender_11
  or or_26 (or_26_out, Bitmap_Instruccion[17], Bitmap_Instruccion[16]);
  assign bit_extender_12_out = {{31{1'b0}}, Origen_Es_Menor_I};  // Bit_Extender bit_extender_12
  Priority_Encoder #(.select(2)) priority_encoder_6 (
    .in0(or_26_out), .in1(or_25_out), .in2(Bitmap_Instruccion[13]), .in3(1'b0), .out(priority_encoder_6_out),
    .en_out(priority_encoder_6_en_out), .en_in(1'b1));  // open: gs
  assign bit_extender_13_out = {{31{1'b0}}, Origen_Es_Menor_I_U};  // Bit_Extender bit_extender_13
  Adder #(.width(32)) adder_6 (
    .a(Inmediato_Extendido), .b(Contenido_Registro_Fuente), .out(Direccion_Acceso_Memoria), .cin(1'b0),
    .cout(Overflow_Acceso_Memoria));
  not not_8 (not_8_out, priority_encoder_6_en_out);
  Multiplexer #(.enable("true"), .select(2), .width(32)) multiplexer_6 (
    .in0(Residuo_DIV), .in1(Parte_Inferior_MULT), .in2(Contenido_Registro_Fuente), .in3({32{1'b0}}),
    .out(Salida_LO), .sel(priority_encoder_6_out), .en(not_8_out));
  Adder #(.width(32)) adder_7 (
    .a(Indice_PC), .b(32'h8), .out(Direccion_Previo_Salto_JAL_JALR), .cin(1'b0),
    .cout(Overflow_Direccion_Previo_Salto_JAL_JALR));
  not not_9 (not_9_out, priority_encoder_7_en_out);
  Priority_Encoder #(.select(5)) priority_encoder_7 (
    .in0(Bitmap_Instruccion[41]), .in1(Bitmap_Instruccion[40]), .in2(Bitmap_Instruccion[39]),
    .in3(Bitmap_Instruccion[38]), .in4(Bitmap_Instruccion[37]), .in5(Bitmap_Instruccion[36]),
    .in6(Bitmap_Instruccion[27]), .in7(Bitmap_Instruccion[26]), .in8(Bitmap_Instruccion[25]),
    .in9(Bitmap_Instruccion[24]), .in10(Bitmap_Instruccion[23]), .in11(Bitmap_Instruccion[22]),
    .in12(Bitmap_Instruccion[6]), .in13(Bitmap_Instruccion[5]), .in14(Bitmap_Instruccion[4]),
    .in15(Bitmap_Instruccion[3]), .in16(Bitmap_Instruccion[2]), .in17(Bitmap_Instruccion[1]),
    .in18(Bitmap_Instruccion[12]), .in19(Bitmap_Instruccion[10]), .in20(or_23_out), .in21(or_22_out),
    .in22(or_20_out), .in23(or_18_out), .in24(1'b0), .in25(1'b0), .in26(1'b0), .in27(1'b0), .in28(1'b0),
    .in29(1'b0), .in30(1'b0), .in31(1'b0), .out(priority_encoder_7_out), .en_out(priority_encoder_7_en_out),
    .en_in(1'b1));  // open: gs
  Multiplexer #(.enable("true"), .select(5), .width(32)) multiplexer_7 (
    .in0(Resultado_LUI), .in1(Resultado_XOR_I), .in2(Resultado_OR_I), .in3(Resultado_AND_I),
    .in4(bit_extender_13_out), .in5(bit_extender_12_out), .in6(bit_extender_11_out),
    .in7(bit_extender_10_out), .in8(Resultado_NOR), .in9(Resultado_XOR), .in10(Resultado_OR),
    .in11(Resultado_AND), .in12(Resultado_SRAV), .in13(Resultado_SRLV), .in14(Resultado_SLLV),
    .in15(Resultado_SRA), .in16(Resultado_SRL), .in17(Resultado_SLL), .in18(Contenido_Previo_LO),
    .in19(Contenido_Previo_HI), .in20(Resultado_SUB), .in21(Resultado_ADD_I), .in22(Resultado_ADD),
    .in23(Direccion_Previo_Salto_JAL_JALR), .in24({32{1'b0}}), .in25({32{1'b0}}), .in26({32{1'b0}}),
    .in27({32{1'b0}}), .in28({32{1'b0}}), .in29({32{1'b0}}), .in30({32{1'b0}}), .in31({32{1'b0}}),
    .out(Salida_Calculo), .sel(priority_encoder_7_out), .en(not_9_out));

  // Other names for the same wires on the sheet: Instruccion_Desconocida = Bitmap_Instruccion[0];
  //   R_SLL = Bitmap_Instruccion[1]; R_SRL = Bitmap_Instruccion[2]; R_SRA = Bitmap_Instruccion[3];
  //   R_SLLV = Bitmap_Instruccion[4]; R_SRLV = Bitmap_Instruccion[5]; R_SRAV = Bitmap_Instruccion[6];
  //   R_JR = Bitmap_Instruccion[7]; R_JALR = Bitmap_Instruccion[8]; R_SYS = Bitmap_Instruccion[9];
  //   R_MFHI = Bitmap_Instruccion[10]; R_MTHI = Bitmap_Instruccion[11]; R_MFLO = Bitmap_Instruccion[12];
  //   R_MTLO = Bitmap_Instruccion[13]; R_MULT = Bitmap_Instruccion[14]; R_MULT_U = Bitmap_Instruccion[15];
  //   R_DIV = Bitmap_Instruccion[16]; R_DIV_U = Bitmap_Instruccion[17]; R_ADD = Bitmap_Instruccion[18];
  //   R_ADD_U = Bitmap_Instruccion[19]; R_SUB = Bitmap_Instruccion[20]; R_SUB_U = Bitmap_Instruccion[21];
  //   R_AND = Bitmap_Instruccion[22]; R_OR = Bitmap_Instruccion[23]; R_XOR = Bitmap_Instruccion[24];
  //   R_NOR = Bitmap_Instruccion[25]; R_SLT = Bitmap_Instruccion[26]; R_SLT_U = Bitmap_Instruccion[27];
  //   J_J = Bitmap_Instruccion[28]; J_JAL = Bitmap_Instruccion[29]; I_BEQ = Bitmap_Instruccion[30];
  //   I_BNE = Bitmap_Instruccion[31]; I_BLEZ = Bitmap_Instruccion[32]; I_BGTZ = Bitmap_Instruccion[33];
  //   I_ADD = Bitmap_Instruccion[34]; I_ADD_U = Bitmap_Instruccion[35]; I_SLT = Bitmap_Instruccion[36];
  //   I_SLT_U = Bitmap_Instruccion[37]; I_AND = Bitmap_Instruccion[38]; I_OR = Bitmap_Instruccion[39];
  //   I_XOR = Bitmap_Instruccion[40]; I_LUI = Bitmap_Instruccion[41]; I_LB = Bitmap_Instruccion[42];
  //   I_LH = Bitmap_Instruccion[43]; I_LW = Bitmap_Instruccion[44]; I_LB_U = Bitmap_Instruccion[45];
  //   I_LH_U = Bitmap_Instruccion[46]; I_SB = Bitmap_Instruccion[47]; I_SH = Bitmap_Instruccion[48];
  //   I_SW = Bitmap_Instruccion[49]; Direccion_Salto_JR_JALR[31:0] = Contenido_Registro_Fuente

  // Notes on the sheet:
  //   AND
  //   XOR
  //   SLL
  //   SLLV
  //   SRA
  //   AND_I
  //   XOR_I
  //   LUI
  //   J, JAL
  //   Aritmética de bits
  //   Aritmética de bits
  //   Conclusiones
  //   Entradas y salidas
  //   Cálculos de tipo R
  //   Cálculos de tipo I
  //   Cálculos de tipo J
  //   Direcciones de Memoria
  //   Identidad de instrucción
  //   OR
  //   NOR
  //   SRL
  //   SRLV
  //   SRAV
  //   OR_I
  //   Extensiones
  //   Índice
  //   Alineamientos
  //   Dirección de memoria
  //   ADD (U)
  //   MULT
  //   DIV
  //   ADD I (U)
  //   Arimética de enteros
  //   Arimética de enteros
  //   DIV U
  //   SUB (U)
  //   MULT U
  //   LTI
  //   BLEZ, BGTZ
  //   Aserciones
  //   Overflow
  //   Comparación de enteros
  //   Predicción sobre salto tomado
  //   Alineamiento en memoria
  //   LTI U
  //   LT, GT, EQ
  //   LT U, GT U
  //   Comparación de enteros
  //   Salida para HI
  //   Salida para registros
  //   Salida para registro o celda de memoria externa
  //   BEQ, BNE, BLEZ, BGTZ
  //   Direcciones de Memoria
  //   JR, JALR
  //   Salida para LO
  //   Direcciones de Memoria
  //   JAL, JALR
  //   LB (U), LH (U), LW, SB, SH, SW
endmodule

module MIPS_Memory_Controller (
  input  [31:0] Entrada,
  input  [4:0] Registro_Destino,
  input  [4:0] Registro_Objetivo,
  input  [7:0] Bitmap_Acceso_Memoria,
  input  [31:0] Word_Lectura,
  input  [15:0] Nibble_Lectura,
  input  [7:0] Byte_Lectura,
  output [31:0] Salida,
  output [4:0] Registro_Destino_Efectivo,
  output Solicitar_Memoria,
  output Escribir_Memoria
);

  wire Intencion_Escribir, Intencion_Leer, Leer, Ningun_Acceso, not_1_out, not_2_out,
       priority_encoder_1_en_out, priority_encoder_2_en_out, priority_encoder_2_out;
  wire [2:0] priority_encoder_1_out;
  wire [31:0] Byte_Expandido_U, Byte_Expandindo, Nibble_Expandido_U, Nibble_Expandindo;

  Comparator comparator_1 (.a(Bitmap_Acceso_Memoria), .b({8{1'b0}}), .eq(Ningun_Acceso));  // open: gt, lt
  assign Nibble_Expandindo = {{16{Nibble_Lectura[15]}}, Nibble_Lectura};  // Bit_Extender bit_extender_1
  assign Nibble_Expandido_U = {{16{1'b0}}, Nibble_Lectura};  // Bit_Extender bit_extender_2
  assign Byte_Expandindo = {{24{Byte_Lectura[7]}}, Byte_Lectura};  // Bit_Extender bit_extender_3
  assign Byte_Expandido_U = {{24{1'b0}}, Byte_Lectura};  // Bit_Extender bit_extender_4
  Priority_Encoder priority_encoder_1 (
    .in0(Ningun_Acceso), .in1(Bitmap_Acceso_Memoria[2]), .in2(Bitmap_Acceso_Memoria[4]),
    .in3(Bitmap_Acceso_Memoria[1]), .in4(Bitmap_Acceso_Memoria[3]), .in5(Bitmap_Acceso_Memoria[0]),
    .in6(1'b0), .in7(1'b0), .out(priority_encoder_1_out), .en_in(1'b1), .en_out(priority_encoder_1_en_out));  // open: gs
  Priority_Encoder #(.select(1)) priority_encoder_2 (
    .in0(Intencion_Leer), .in1(Ningun_Acceso), .out(priority_encoder_2_out),
    .en_out(priority_encoder_2_en_out), .en_in(1'b1));  // open: gs
  or or_1 (Intencion_Leer, Bitmap_Acceso_Memoria[4], Bitmap_Acceso_Memoria[3], Bitmap_Acceso_Memoria[2], Bitmap_Acceso_Memoria[1], Bitmap_Acceso_Memoria[0]);
  not not_1 (not_1_out, priority_encoder_1_en_out);
  Multiplexer #(.enable("true"), .select(3), .width(32)) multiplexer_1 (
    .in0(Entrada), .in1(Word_Lectura), .in2(Nibble_Expandido_U), .in3(Nibble_Expandindo),
    .in4(Byte_Expandido_U), .in5(Byte_Expandindo), .in6({32{1'b0}}), .in7({32{1'b0}}), .out(Salida),
    .sel(priority_encoder_1_out), .en(not_1_out));
  not not_2 (not_2_out, priority_encoder_2_en_out);
  Multiplexer #(.enable("true"), .width(5)) multiplexer_2 (
    .in0(Registro_Objetivo), .in1(Registro_Destino), .out(Registro_Destino_Efectivo),
    .sel(priority_encoder_2_out), .en(not_2_out));
  or or_2 (Intencion_Escribir, Bitmap_Acceso_Memoria[7], Bitmap_Acceso_Memoria[6], Bitmap_Acceso_Memoria[5]);
  not not_3 (Escribir_Memoria, Leer);
  and and_1 (Leer, ~Intencion_Escribir, Intencion_Leer);  // AND_Gate
  or or_3 (Solicitar_Memoria, Intencion_Escribir, Intencion_Leer);

  // Other names for the same wires on the sheet: I_LB = Bitmap_Acceso_Memoria[0]; I_LH = Bitmap_Acceso_Memoria[1];
  //   I_LW = Bitmap_Acceso_Memoria[2]; I_LB_U = Bitmap_Acceso_Memoria[3]; I_LH_U = Bitmap_Acceso_Memoria[4];
  //   I_SB = Bitmap_Acceso_Memoria[5]; I_SH = Bitmap_Acceso_Memoria[6]; I_SW = Bitmap_Acceso_Memoria[7]
endmodule

module MIPS_Data_Hazard_Detector (
  input  [4:0] ID_Registro_Fuente,
  input  [4:0] ID_Registro_Objetivo,
  input  [4:0] EX_Registro_Destino,
  input  [4:0] MEM_Indice_Registro,
  input  [1:0] ID_Leer_LOHI,
  input  [1:0] EX_Escribir_LOHI,
  input  [1:0] MEM_Escribir_LOHI,
  input  [7:0] EX_Bitmap_Acceso_Memoria,
  output [7:0] Bitmap_Dependencias,
  output EX_Lectura_Memoria_Pendiente
);

  wire comparator_1_eq, comparator_2_eq, comparator_3_eq, comparator_4_eq, comparator_5_eq, comparator_6_eq,
       comparator_7_eq, comparator_8_eq, EX_Registro_Escrito, MEM_Registro_Escrito, or_1_out, or_2_out,
       Registro_Fuente_Leido, Registro_Objetivo_Leido;

  and and_1 (Bitmap_Dependencias[1], MEM_Escribir_LOHI[0], ID_Leer_LOHI[0]);
  and and_2 (Bitmap_Dependencias[0], EX_Escribir_LOHI[0], ID_Leer_LOHI[0], ~Bitmap_Dependencias[1]);  // AND_Gate
  and and_3 (Bitmap_Dependencias[3], MEM_Escribir_LOHI[1], ID_Leer_LOHI[1]);
  and and_4 (Bitmap_Dependencias[2], EX_Escribir_LOHI[1], ID_Leer_LOHI[1], ~Bitmap_Dependencias[3]);  // AND_Gate
  or or_1 (or_1_out, EX_Bitmap_Acceso_Memoria[4], EX_Bitmap_Acceso_Memoria[3], EX_Bitmap_Acceso_Memoria[2], EX_Bitmap_Acceso_Memoria[1], EX_Bitmap_Acceso_Memoria[0]);
  not not_1 (Registro_Fuente_Leido, comparator_1_eq);
  Comparator #(.width(5)) comparator_1 (.a(ID_Registro_Fuente), .b({5{1'b0}}), .eq(comparator_1_eq));  // open: gt, lt
  not not_2 (EX_Registro_Escrito, comparator_2_eq);
  Comparator #(.width(5)) comparator_2 (.a(EX_Registro_Destino), .b({5{1'b0}}), .eq(comparator_2_eq));  // open: gt, lt
  Comparator #(.width(5)) comparator_3 (
    .a(ID_Registro_Fuente), .b(MEM_Indice_Registro), .eq(comparator_3_eq));  // open: gt, lt
  Comparator #(.width(5)) comparator_4 (
    .a(ID_Registro_Objetivo), .b(MEM_Indice_Registro), .eq(comparator_4_eq));  // open: gt, lt
  and and_5 (Bitmap_Dependencias[5], comparator_3_eq, MEM_Registro_Escrito);
  and and_6 (Bitmap_Dependencias[7], comparator_4_eq, MEM_Registro_Escrito);
  Comparator #(.width(5)) comparator_5 (.a(ID_Registro_Objetivo), .b({5{1'b0}}), .eq(comparator_5_eq));  // open: gt, lt
  Comparator #(.width(5)) comparator_6 (.a(MEM_Indice_Registro), .b({5{1'b0}}), .eq(comparator_6_eq));  // open: gt, lt
  or or_2 (or_2_out, Bitmap_Dependencias[4], Bitmap_Dependencias[6]);
  and and_7 (EX_Lectura_Memoria_Pendiente, or_2_out, or_1_out);
  not not_3 (Registro_Objetivo_Leido, comparator_5_eq);
  not not_4 (MEM_Registro_Escrito, comparator_6_eq);
  Comparator #(.width(5)) comparator_7 (
    .a(ID_Registro_Fuente), .b(EX_Registro_Destino), .eq(comparator_7_eq));  // open: gt, lt
  Comparator #(.width(5)) comparator_8 (
    .a(ID_Registro_Objetivo), .b(EX_Registro_Destino), .eq(comparator_8_eq));  // open: gt, lt
  and and_8 (Bitmap_Dependencias[4], EX_Registro_Escrito, comparator_7_eq, ~Bitmap_Dependencias[5]);  // AND_Gate
  and and_9 (Bitmap_Dependencias[6], EX_Registro_Escrito, comparator_8_eq, ~Bitmap_Dependencias[7]);  // AND_Gate

  // Other names for the same wires on the sheet: Dependencia_LO_EX = Bitmap_Dependencias[0];
  //   Dependencia_LO_MEM = Bitmap_Dependencias[1]; Dependencia_HI_EX = Bitmap_Dependencias[2];
  //   Dependencia_HI_MEM = Bitmap_Dependencias[3]; Dependencia_Registro_Fuente_EX = Bitmap_Dependencias[4];
  //   Dependencia_Registro_Fuente_MEM = Bitmap_Dependencias[5];
  //   Dependencia_Registro_Objetivo_EX = Bitmap_Dependencias[6];
  //   Dependencia_Registro_Objetivo_MEM = Bitmap_Dependencias[7]; I_LB = EX_Bitmap_Acceso_Memoria[0];
  //   I_LH = EX_Bitmap_Acceso_Memoria[1]; I_LW = EX_Bitmap_Acceso_Memoria[2]; I_LB_U = EX_Bitmap_Acceso_Memoria[3];
  //   I_LH_U = EX_Bitmap_Acceso_Memoria[4]; I_SB = EX_Bitmap_Acceso_Memoria[5]; I_SH = EX_Bitmap_Acceso_Memoria[6];
  //   I_SW = EX_Bitmap_Acceso_Memoria[7]; EX_LO_Escrito = EX_Escribir_LOHI[0]; EX_HI_Escrito = EX_Escribir_LOHI[1];
  //   ID_LO_Leido = ID_Leer_LOHI[0]; ID_HI_Leido = ID_Leer_LOHI[1]; MEM_LO_Escrito = MEM_Escribir_LOHI[0];
  //   MEM_HI_Escrito = MEM_Escribir_LOHI[1]
endmodule

module MIPS_Data_Hazard_Solver (
  input  [7:0] Bitmap_Dependencias,
  input  [31:0] EX_LO,
  input  [31:0] MEM_LO,
  input  [31:0] WB_LO,
  input  [31:0] EX_HI,
  input  [31:0] MEM_HI,
  input  [31:0] WB_HI,
  input  [31:0] EX_Salida,
  input  [31:0] MEM_Salida,
  input  [31:0] WB_Fuente,
  input  [31:0] WB_Objetivo,
  output [31:0] EX_Entrada_LO,
  output [31:0] EX_Entrada_HI,
  output [31:0] EX_Entrada_Fuente,
  output [31:0] EX_Entrada_Objetivo
);

  wire [31:0] multiplexer_1_out, multiplexer_2_out, multiplexer_5_out, multiplexer_6_out;

  Multiplexer #(.width(32)) multiplexer_1 (
    .in0(WB_LO), .in1(EX_LO), .out(multiplexer_1_out), .sel(Bitmap_Dependencias[0]));
  Multiplexer #(.width(32)) multiplexer_2 (
    .in0(WB_HI), .in1(EX_HI), .out(multiplexer_2_out), .sel(Bitmap_Dependencias[2]));
  Multiplexer #(.width(32)) multiplexer_3 (
    .in0(multiplexer_1_out), .in1(MEM_LO), .out(EX_Entrada_LO), .sel(Bitmap_Dependencias[1]));
  Multiplexer #(.width(32)) multiplexer_4 (
    .in0(multiplexer_2_out), .in1(MEM_HI), .out(EX_Entrada_HI), .sel(Bitmap_Dependencias[3]));
  Multiplexer #(.width(32)) multiplexer_5 (
    .in0(EX_Salida), .in1(WB_Fuente), .out(multiplexer_5_out), .sel(Bitmap_Dependencias[4]));
  Multiplexer #(.width(32)) multiplexer_6 (
    .in0(EX_Salida), .in1(WB_Fuente), .out(multiplexer_6_out), .sel(Bitmap_Dependencias[6]));
  Multiplexer #(.width(32)) multiplexer_7 (
    .in0(multiplexer_5_out), .in1(MEM_Salida), .out(EX_Entrada_Fuente), .sel(Bitmap_Dependencias[5]));
  Multiplexer #(.width(32)) multiplexer_8 (
    .in0(multiplexer_6_out), .in1(MEM_Salida), .out(EX_Entrada_Objetivo), .sel(Bitmap_Dependencias[7]));

  // Other names for the same wires on the sheet: Dependencia_LO_EX = Bitmap_Dependencias[0];
  //   Dependencia_LO_MEM = Bitmap_Dependencias[1]; Dependencia_HI_EX = Bitmap_Dependencias[2];
  //   Dependencia_HI_MEM = Bitmap_Dependencias[3]; Dependencia_Registro_Fuente_EX = Bitmap_Dependencias[4];
  //   Dependencia_Registro_Fuente_MEM = Bitmap_Dependencias[5];
  //   Dependencia_Registro_Objetivo_EX = Bitmap_Dependencias[6];
  //   Dependencia_Registro_Objetivo_MEM = Bitmap_Dependencias[7]; EX_Salida_Calculo[31:0] = EX_Salida;
  //   EX_Salida_HI[31:0] = EX_HI; EX_Salida_LO[31:0] = EX_LO; MEM_Salida_HI[31:0] = MEM_HI;
  //   MEM_Salida_LO[31:0] = MEM_LO; MEM_Salida_Registro[31:0] = MEM_Salida; WB_Salida_HI[31:0] = WB_HI;
  //   WB_Salida_LO[31:0] = WB_LO; WB_Salida_Registro_Fuente[31:0] = WB_Fuente;
  //   WB_Salida_Registro_Objetivo[31:0] = WB_Objetivo
endmodule

module Four_GB_ROM_Controller (
  input  [31:0] Direccion_32_bits,
  input  Usar_Litte_Endian,
  output [63:0] Doubleword,
  output [31:0] Word,
  output [15:0] Nibble,
  output [7:0] Byte
);

  wire [2:0] subtractor_2_out;
  wire [31:0] multiplexer_1_out, subtractor_1_out;
  wire [63:0] multiplexer_2_out, multiplexer_3_out, ROM_1_data, ROM_2_data, ROM_3_data, ROM_4_data,
       ROM_5_data, ROM_6_data, ROM_7_data, ROM_8_data, ROM_9_data, ROM_10_data, ROM_11_data, ROM_12_data,
       ROM_13_data, ROM_14_data, ROM_15_data, ROM_16_data, ROM_17_data, ROM_18_data, ROM_19_data,
       ROM_20_data, ROM_21_data, ROM_22_data, ROM_23_data, ROM_24_data, ROM_25_data, ROM_26_data,
       ROM_27_data, ROM_28_data, ROM_29_data, ROM_30_data, ROM_31_data, ROM_32_data;

  Subtractor #(.width(32)) subtractor_1 (
    .a({32{1'b1}}), .b(Direccion_32_bits), .out(subtractor_1_out), .bin(1'b0));  // open: bout
  Multiplexer #(.width(32)) multiplexer_1 (
    .in0(Direccion_32_bits), .in1(subtractor_1_out), .out(multiplexer_1_out), .sel(Usar_Litte_Endian));
  Subtractor #(.width(3)) subtractor_2 (
    .a(3'b111), .b(multiplexer_1_out[2:0]), .out(subtractor_2_out), .bin(1'b0));  // open: bout
  ROM #(.addrWidth(24), .dataWidth(64)) ROM_1 (.addr(multiplexer_1_out[26:3]), .data(ROM_1_data));
  ROM #(.addrWidth(24), .dataWidth(64)) ROM_5 (.addr(multiplexer_1_out[26:3]), .data(ROM_5_data));
  ROM #(.addrWidth(24), .dataWidth(64)) ROM_9 (.addr(multiplexer_1_out[26:3]), .data(ROM_9_data));
  ROM #(.addrWidth(24), .dataWidth(64)) ROM_13 (.addr(multiplexer_1_out[26:3]), .data(ROM_13_data));
  ROM #(.addrWidth(24), .dataWidth(64)) ROM_17 (.addr(multiplexer_1_out[26:3]), .data(ROM_17_data));
  ROM #(.addrWidth(24), .dataWidth(64)) ROM_21 (.addr(multiplexer_1_out[26:3]), .data(ROM_21_data));
  ROM #(.addrWidth(24), .dataWidth(64)) ROM_25 (.addr(multiplexer_1_out[26:3]), .data(ROM_25_data));
  ROM #(.addrWidth(24), .dataWidth(64)) ROM_29 (.addr(multiplexer_1_out[26:3]), .data(ROM_29_data));
  ROM #(.addrWidth(24), .dataWidth(64)) ROM_2 (.addr(multiplexer_1_out[26:3]), .data(ROM_2_data));
  ROM #(.addrWidth(24), .dataWidth(64)) ROM_6 (.addr(multiplexer_1_out[26:3]), .data(ROM_6_data));
  ROM #(.addrWidth(24), .dataWidth(64)) ROM_10 (.addr(multiplexer_1_out[26:3]), .data(ROM_10_data));
  ROM #(.addrWidth(24), .dataWidth(64)) ROM_14 (.addr(multiplexer_1_out[26:3]), .data(ROM_14_data));
  ROM #(.addrWidth(24), .dataWidth(64)) ROM_18 (.addr(multiplexer_1_out[26:3]), .data(ROM_18_data));
  ROM #(.addrWidth(24), .dataWidth(64)) ROM_22 (.addr(multiplexer_1_out[26:3]), .data(ROM_22_data));
  ROM #(.addrWidth(24), .dataWidth(64)) ROM_26 (.addr(multiplexer_1_out[26:3]), .data(ROM_26_data));
  ROM #(.addrWidth(24), .dataWidth(64)) ROM_30 (.addr(multiplexer_1_out[26:3]), .data(ROM_30_data));
  ROM #(.addrWidth(24), .dataWidth(64)) ROM_3 (.addr(multiplexer_1_out[26:3]), .data(ROM_3_data));
  ROM #(.addrWidth(24), .dataWidth(64)) ROM_7 (.addr(multiplexer_1_out[26:3]), .data(ROM_7_data));
  ROM #(.addrWidth(24), .dataWidth(64)) ROM_11 (.addr(multiplexer_1_out[26:3]), .data(ROM_11_data));
  ROM #(.addrWidth(24), .dataWidth(64)) ROM_15 (.addr(multiplexer_1_out[26:3]), .data(ROM_15_data));
  ROM #(.addrWidth(24), .dataWidth(64)) ROM_19 (.addr(multiplexer_1_out[26:3]), .data(ROM_19_data));
  ROM #(.addrWidth(24), .dataWidth(64)) ROM_23 (.addr(multiplexer_1_out[26:3]), .data(ROM_23_data));
  ROM #(.addrWidth(24), .dataWidth(64)) ROM_27 (.addr(multiplexer_1_out[26:3]), .data(ROM_27_data));
  ROM #(.addrWidth(24), .dataWidth(64)) ROM_31 (.addr(multiplexer_1_out[26:3]), .data(ROM_31_data));
  ROM #(.addrWidth(24), .dataWidth(64)) ROM_4 (.addr(multiplexer_1_out[26:3]), .data(ROM_4_data));
  ROM #(.addrWidth(24), .dataWidth(64)) ROM_8 (.addr(multiplexer_1_out[26:3]), .data(ROM_8_data));
  ROM #(.addrWidth(24), .dataWidth(64)) ROM_12 (.addr(multiplexer_1_out[26:3]), .data(ROM_12_data));
  ROM #(.addrWidth(24), .dataWidth(64)) ROM_16 (.addr(multiplexer_1_out[26:3]), .data(ROM_16_data));
  ROM #(.addrWidth(24), .dataWidth(64)) ROM_20 (.addr(multiplexer_1_out[26:3]), .data(ROM_20_data));
  ROM #(.addrWidth(24), .dataWidth(64)) ROM_24 (.addr(multiplexer_1_out[26:3]), .data(ROM_24_data));
  ROM #(.addrWidth(24), .dataWidth(64)) ROM_28 (.addr(multiplexer_1_out[26:3]), .data(ROM_28_data));
  ROM #(.addrWidth(24), .dataWidth(64)) ROM_32 (.addr(multiplexer_1_out[26:3]), .data(ROM_32_data));
  Multiplexer #(.select(4), .width(64)) multiplexer_2 (
    .in0(ROM_1_data), .in1(ROM_5_data), .in2(ROM_9_data), .in3(ROM_13_data), .in4(ROM_2_data),
    .in5(ROM_6_data), .in6(ROM_10_data), .in7(ROM_14_data), .in8(ROM_3_data), .in9(ROM_7_data),
    .in10(ROM_11_data), .in11(ROM_15_data), .in12(ROM_4_data), .in13(ROM_8_data), .in14(ROM_12_data),
    .in15(ROM_16_data), .out(multiplexer_2_out), .sel(multiplexer_1_out[30:27]));
  Multiplexer #(.select(4), .width(64)) multiplexer_3 (
    .in0(ROM_17_data), .in1(ROM_21_data), .in2(ROM_25_data), .in3(ROM_29_data), .in4(ROM_18_data),
    .in5(ROM_22_data), .in6(ROM_26_data), .in7(ROM_30_data), .in8(ROM_19_data), .in9(ROM_23_data),
    .in10(ROM_27_data), .in11(ROM_31_data), .in12(ROM_20_data), .in13(ROM_24_data), .in14(ROM_28_data),
    .in15(ROM_32_data), .out(multiplexer_3_out), .sel(multiplexer_1_out[30:27]));
  Multiplexer #(.width(64)) multiplexer_4 (
    .in0(multiplexer_2_out), .in1(multiplexer_3_out), .out(Doubleword), .sel(multiplexer_1_out[31]));
  Multiplexer #(.width(32)) multiplexer_5 (
    .in0(Doubleword[31:0]), .in1(Doubleword[63:32]), .out(Word), .sel(subtractor_2_out[2]));
  Multiplexer #(.width(16)) multiplexer_6 (
    .in0(Word[15:0]), .in1(Word[31:16]), .out(Nibble), .sel(subtractor_2_out[1]));
  Multiplexer #(.width(8)) multiplexer_7 (.in0(Nibble[7:0]), .in1(Nibble[15:8]), .out(Byte), .sel(subtractor_2_out[0]));

  // Notes on the sheet:
  //   Tamaño de memoria accesible
  //   Longitud de byte
  //   contents of ROM_1 (hex, n*v repeats v):
  //   3c01000a00000000
  //   4 Gigabit
  //   4 Gigabit
  //   4 Gigabit
  //   4 Gigabit
  //   4 Gigabytes
  //   4 Giganibbles
  //   4 Giganibbles
  //   4 Gigabit
  //   4 Gigabit
  //   contents of ROM_32 (hex, n*v repeats v):
  //   16777215*0 123456789abcdef
  //   4 Gigabit
  //   4 Gigabit
endmodule
module Four_GB_RAM_Controller (
  input  Reloj,
  input  Limpiar,
  input  Bloquear,
  input  Escribir,
  input  [31:0] Direccion_32_bits,
  input  Usar_Litte_Endian,
  input  [31:0] Entrada,
  output [63:0] Doubleword,
  output [31:0] Word,
  output [15:0] Nibble,
  output [7:0] Byte
);

  wire and_1_out, and_2_out, and_3_out, and_4_out, and_5_out, and_6_out, and_7_out, and_8_out, and_9_out,
       and_10_out, and_11_out, and_12_out, and_13_out, and_14_out, and_15_out, and_16_out, and_17_out,
       and_18_out, and_19_out, and_20_out, and_21_out, and_22_out, and_23_out, and_24_out, and_25_out,
       and_26_out, and_27_out, and_28_out, and_30_out, and_31_out, and_32_out, and_33_out, and_34_out,
       and_35_out, and_36_out, and_37_out, and_38_out, and_39_out, and_40_out, and_41_out, and_42_out,
       and_43_out, and_44_out, and_45_out, and_46_out, and_47_out, and_48_out, and_49_out, and_50_out,
       and_51_out, and_52_out, and_53_out, and_54_out, and_55_out, and_56_out, and_57_out, and_58_out,
       and_59_out, and_60_out, and_61_out, and_62_out, and_63_out, and_64_out, and_65_out, and_66_out,
       and_67_out, and_68_out, and_69_out, and_70_out, and_71_out, and_72_out, and_73_out, and_74_out,
       and_75_out, and_76_out, and_77_out, and_78_out, and_79_out, and_80_out, and_81_out, and_82_out,
       and_83_out, and_84_out, and_85_out, and_86_out, and_87_out, and_88_out, and_89_out, and_90_out,
       and_91_out, and_92_out, and_93_out, and_94_out, and_95_out, and_96_out, and_97_out, and_98_out,
       and_99_out, and_100_out, and_101_out, and_102_out, and_103_out, decoder_1_out0, decoder_1_out1,
       decoder_2_out0, decoder_2_out1, decoder_2_out2, decoder_2_out3, decoder_3_out0, decoder_3_out1,
       decoder_3_out2, decoder_3_out3, decoder_4_out0, decoder_4_out1, decoder_4_out2, decoder_4_out3,
       decoder_5_out0, decoder_5_out1, decoder_5_out2, decoder_5_out3, not_1_out;
  wire [1:0] multiplexer_1_out_3, multiplexer_1_out_4;
  wire [2:0] subtractor_2_out;
  wire [23:0] multiplexer_1_out_2;
  wire [31:0] multiplexer_1_out, subtractor_1_out;
  wire [63:0] and_29_out, bit_extender_1_out, bit_extender_2_out, controlled_buffer_1_out,
       controlled_buffer_18_out, multiplexer_5_out, or_1_out, ram_1_dout, ram_2_dout, ram_3_dout, ram_4_dout,
       ram_5_dout, ram_6_dout, ram_7_dout, ram_8_dout, ram_9_dout, ram_10_dout, ram_11_dout, ram_12_dout,
       ram_13_dout, ram_14_dout, ram_15_dout, ram_16_dout, ram_17_dout, ram_18_dout, ram_19_dout,
       ram_20_dout, ram_21_dout, ram_22_dout, ram_23_dout, ram_24_dout, ram_25_dout, ram_26_dout,
       ram_27_dout, ram_28_dout, ram_29_dout, ram_30_dout, ram_31_dout, ram_32_dout, shifter_1_out, xor_1_out;

  Subtractor #(.width(32)) subtractor_1 (
    .a({32{1'b1}}), .b(Direccion_32_bits), .out(subtractor_1_out), .bin(1'b0));  // open: bout
  Multiplexer #(.width(32)) multiplexer_1 (
    .in0(Direccion_32_bits), .in1(subtractor_1_out),
    .out({multiplexer_1_out[31], multiplexer_1_out_4, multiplexer_1_out_3, multiplexer_1_out_2, multiplexer_1_out[2:0]}),
    .sel(Usar_Litte_Endian));
  Subtractor #(.width(3)) subtractor_2 (
    .a(3'b111), .b(multiplexer_1_out[2:0]), .out(subtractor_2_out), .bin(1'b0));  // open: bout
  // Probe on subtractor_2_out
  and and_1 (and_1_out, ~Escribir, ~Bloquear);  // AND_Gate
  and and_2 (and_2_out, Escribir, ~Bloquear);  // AND_Gate
  Decoder #(.enable("false")) decoder_1 (.out0(decoder_1_out0), .out1(decoder_1_out1), .sel(multiplexer_1_out[31]));
  // Probe on multiplexer_1_out_2
  // Probe on multiplexer_1_out_4
  // Probe on multiplexer_1_out_3
  and and_3 (and_3_out, decoder_1_out0, and_2_out);
  and and_4 (and_4_out, decoder_1_out0, and_1_out);
  // Probe on {multiplexer_1_out_4, multiplexer_1_out_3, multiplexer_1_out_2}
  Decoder #(.enable("false"), .select(2)) decoder_2 (
    .out0(decoder_2_out0), .out1(decoder_2_out1), .out2(decoder_2_out2), .out3(decoder_2_out3),
    .sel(multiplexer_1_out_4));
  Decoder #(.enable("false"), .select(2)) decoder_3 (
    .out0(decoder_3_out0), .out1(decoder_3_out1), .out2(decoder_3_out2), .out3(decoder_3_out3),
    .sel(multiplexer_1_out_3));
  and and_5 (and_5_out, decoder_3_out0, decoder_2_out0);
  and and_6 (and_6_out, and_5_out, and_3_out);
  and and_7 (and_7_out, and_5_out, and_4_out);
  and and_8 (and_8_out, decoder_3_out0, decoder_2_out1);
  and and_9 (and_9_out, and_8_out, and_3_out);
  and and_10 (and_10_out, and_8_out, and_4_out);
  and and_11 (and_11_out, decoder_3_out0, decoder_2_out2);
  and and_12 (and_12_out, and_11_out, and_3_out);
  and and_13 (and_13_out, and_11_out, and_4_out);
  and and_14 (and_14_out, decoder_3_out0, decoder_2_out3);
  and and_15 (and_15_out, and_14_out, and_3_out);
  and and_16 (and_16_out, and_14_out, and_4_out);
  RAM #(.addrWidth(24), .asyncread("true"), .clearpin("true"), .dataWidth(64)) ram_1 (
    .addr(multiplexer_1_out_2), .we(and_6_out), .oe(and_7_out), .clk(Reloj), .din(or_1_out),
    .dout(ram_1_dout), .clr(Limpiar));
  RAM #(.addrWidth(24), .asyncread("true"), .clearpin("true"), .dataWidth(64)) ram_2 (
    .addr(multiplexer_1_out_2), .we(and_9_out), .oe(and_10_out), .clk(Reloj), .din(or_1_out),
    .dout(ram_2_dout), .clr(Limpiar));
  RAM #(.addrWidth(24), .asyncread("true"), .clearpin("true"), .dataWidth(64)) ram_3 (
    .addr(multiplexer_1_out_2), .we(and_12_out), .oe(and_13_out), .clk(Reloj), .din(or_1_out),
    .dout(ram_3_dout), .clr(Limpiar));
  RAM #(.addrWidth(24), .asyncread("true"), .clearpin("true"), .dataWidth(64)) ram_4 (
    .addr(multiplexer_1_out_2), .we(and_15_out), .oe(and_16_out), .clk(Reloj), .din(or_1_out),
    .dout(ram_4_dout), .clr(Limpiar));
  assign controlled_buffer_1_out = and_5_out ? ram_1_dout : 64'bz;  // Controlled_Buffer controlled_buffer_1
  assign controlled_buffer_1_out = and_8_out ? ram_2_dout : 64'bz;  // Controlled_Buffer controlled_buffer_2
  assign controlled_buffer_1_out = and_11_out ? ram_3_dout : 64'bz;  // Controlled_Buffer controlled_buffer_3
  assign controlled_buffer_1_out = and_14_out ? ram_4_dout : 64'bz;  // Controlled_Buffer controlled_buffer_4
  assign Doubleword = decoder_1_out0 ? controlled_buffer_1_out : 64'bz;  // Controlled_Buffer controlled_buffer_5
  and and_17 (and_17_out, decoder_3_out1, decoder_2_out0);
  and and_18 (and_18_out, decoder_3_out1, decoder_2_out1);
  and and_19 (and_19_out, decoder_3_out1, decoder_2_out2);
  and and_20 (and_20_out, decoder_3_out1, decoder_2_out3);
  Multiplexer #(.width(32)) multiplexer_2 (
    .in0(Doubleword[31:0]), .in1(Doubleword[63:32]), .out(Word), .sel(subtractor_2_out[2]));
  not not_1 (not_1_out, subtractor_2_out[2]);
  and and_21 (and_21_out, and_17_out, and_3_out);
  and and_22 (and_22_out, and_17_out, and_4_out);
  and and_23 (and_23_out, and_18_out, and_3_out);
  and and_24 (and_24_out, and_18_out, and_4_out);
  and and_25 (and_25_out, and_19_out, and_3_out);
  and and_26 (and_26_out, and_19_out, and_4_out);
  and and_27 (and_27_out, and_20_out, and_3_out);
  and and_28 (and_28_out, and_20_out, and_4_out);
  Multiplexer #(.width(16)) multiplexer_3 (
    .in0(Word[15:0]), .in1(Word[31:16]), .out(Nibble), .sel(subtractor_2_out[1]));
  Multiplexer #(.width(8)) multiplexer_4 (.in0(Nibble[7:0]), .in1(Nibble[15:8]), .out(Byte), .sel(subtractor_2_out[0]));
  assign bit_extender_1_out = {{63{not_1_out}}, not_1_out};  // Bit_Extender bit_extender_1
  assign bit_extender_2_out = {{32{1'b0}}, Entrada};  // Bit_Extender bit_extender_2
  RAM #(.addrWidth(24), .asyncread("true"), .clearpin("true"), .dataWidth(64)) ram_5 (
    .addr(multiplexer_1_out_2), .we(and_21_out), .oe(and_22_out), .clk(Reloj), .din(or_1_out),
    .dout(ram_5_dout), .clr(Limpiar));
  RAM #(.addrWidth(24), .asyncread("true"), .clearpin("true"), .dataWidth(64)) ram_6 (
    .addr(multiplexer_1_out_2), .we(and_23_out), .oe(and_24_out), .clk(Reloj), .din(or_1_out),
    .dout(ram_6_dout), .clr(Limpiar));
  RAM #(.addrWidth(24), .asyncread("true"), .clearpin("true"), .dataWidth(64)) ram_7 (
    .addr(multiplexer_1_out_2), .we(and_25_out), .oe(and_26_out), .clk(Reloj), .din(or_1_out),
    .dout(ram_7_dout), .clr(Limpiar));
  RAM #(.addrWidth(24), .asyncread("true"), .clearpin("true"), .dataWidth(64)) ram_8 (
    .addr(multiplexer_1_out_2), .we(and_27_out), .oe(and_28_out), .clk(Reloj), .din(or_1_out),
    .dout(ram_8_dout), .clr(Limpiar));
  assign xor_1_out = 64'hffffffff ^ bit_extender_1_out;  // XOR_Gate xor_1, 64 bits wide
  Multiplexer #(.width(64)) multiplexer_5 (
    .in0(bit_extender_2_out), .in1(shifter_1_out), .out(multiplexer_5_out), .sel(subtractor_2_out[2]));
  Shifter #(.width(64)) shifter_1 (.in(bit_extender_2_out), .\dist (6'b100000), .out(shifter_1_out));
  assign and_29_out = Doubleword & xor_1_out;  // AND_Gate and_29, 64 bits wide
  assign or_1_out = and_29_out | multiplexer_5_out;  // OR_Gate or_1, 64 bits wide
  assign controlled_buffer_1_out = and_17_out ? ram_5_dout : 64'bz;  // Controlled_Buffer controlled_buffer_6
  assign controlled_buffer_1_out = and_18_out ? ram_6_dout : 64'bz;  // Controlled_Buffer controlled_buffer_7
  assign controlled_buffer_1_out = and_19_out ? ram_7_dout : 64'bz;  // Controlled_Buffer controlled_buffer_8
  assign controlled_buffer_1_out = and_20_out ? ram_8_dout : 64'bz;  // Controlled_Buffer controlled_buffer_9
  // Probe on or_1_out
  and and_30 (and_30_out, decoder_3_out2, decoder_2_out0);
  and and_31 (and_31_out, decoder_3_out2, decoder_2_out1);
  and and_32 (and_32_out, decoder_3_out2, decoder_2_out2);
  and and_33 (and_33_out, decoder_3_out2, decoder_2_out3);
  RAM #(.addrWidth(24), .asyncread("true"), .clearpin("true"), .dataWidth(64)) ram_9 (
    .addr(multiplexer_1_out_2), .we(and_34_out), .oe(and_35_out), .clk(Reloj), .din(or_1_out),
    .dout(ram_9_dout), .clr(Limpiar));
  and and_34 (and_34_out, and_30_out, and_3_out);
  and and_35 (and_35_out, and_30_out, and_4_out);
  RAM #(.addrWidth(24), .asyncread("true"), .clearpin("true"), .dataWidth(64)) ram_10 (
    .addr(multiplexer_1_out_2), .we(and_36_out), .oe(and_37_out), .clk(Reloj), .din(or_1_out),
    .dout(ram_10_dout), .clr(Limpiar));
  and and_36 (and_36_out, and_31_out, and_3_out);
  and and_37 (and_37_out, and_31_out, and_4_out);
  RAM #(.addrWidth(24), .asyncread("true"), .clearpin("true"), .dataWidth(64)) ram_11 (
    .addr(multiplexer_1_out_2), .we(and_38_out), .oe(and_39_out), .clk(Reloj), .din(or_1_out),
    .dout(ram_11_dout), .clr(Limpiar));
  and and_38 (and_38_out, and_32_out, and_3_out);
  and and_39 (and_39_out, and_32_out, and_4_out);
  RAM #(.addrWidth(24), .asyncread("true"), .clearpin("true"), .dataWidth(64)) ram_12 (
    .addr(multiplexer_1_out_2), .we(and_40_out), .oe(and_41_out), .clk(Reloj), .din(or_1_out),
    .dout(ram_12_dout), .clr(Limpiar));
  and and_40 (and_40_out, and_33_out, and_3_out);
  and and_41 (and_41_out, and_33_out, and_4_out);
  and and_42 (and_42_out, decoder_3_out3, decoder_2_out0);
  assign controlled_buffer_1_out = and_30_out ? ram_9_dout : 64'bz;  // Controlled_Buffer controlled_buffer_10
  and and_43 (and_43_out, decoder_3_out3, decoder_2_out1);
  assign controlled_buffer_1_out = and_31_out ? ram_10_dout : 64'bz;  // Controlled_Buffer controlled_buffer_11
  and and_44 (and_44_out, decoder_3_out3, decoder_2_out2);
  assign controlled_buffer_1_out = and_32_out ? ram_11_dout : 64'bz;  // Controlled_Buffer controlled_buffer_12
  and and_45 (and_45_out, decoder_3_out3, decoder_2_out3);
  assign controlled_buffer_1_out = and_33_out ? ram_12_dout : 64'bz;  // Controlled_Buffer controlled_buffer_13
  and and_46 (and_46_out, and_42_out, and_3_out);
  and and_47 (and_47_out, and_42_out, and_4_out);
  and and_48 (and_48_out, and_43_out, and_3_out);
  and and_49 (and_49_out, and_43_out, and_4_out);
  and and_50 (and_50_out, and_44_out, and_3_out);
  and and_51 (and_51_out, and_44_out, and_4_out);
  and and_52 (and_52_out, and_45_out, and_3_out);
  and and_53 (and_53_out, and_45_out, and_4_out);
  RAM #(.addrWidth(24), .asyncread("true"), .clearpin("true"), .dataWidth(64)) ram_13 (
    .addr(multiplexer_1_out_2), .we(and_46_out), .oe(and_47_out), .clk(Reloj), .din(or_1_out),
    .dout(ram_13_dout), .clr(Limpiar));
  RAM #(.addrWidth(24), .asyncread("true"), .clearpin("true"), .dataWidth(64)) ram_14 (
    .addr(multiplexer_1_out_2), .we(and_48_out), .oe(and_49_out), .clk(Reloj), .din(or_1_out),
    .dout(ram_14_dout), .clr(Limpiar));
  RAM #(.addrWidth(24), .asyncread("true"), .clearpin("true"), .dataWidth(64)) ram_15 (
    .addr(multiplexer_1_out_2), .we(and_50_out), .oe(and_51_out), .clk(Reloj), .din(or_1_out),
    .dout(ram_15_dout), .clr(Limpiar));
  RAM #(.addrWidth(24), .asyncread("true"), .clearpin("true"), .dataWidth(64)) ram_16 (
    .addr(multiplexer_1_out_2), .we(and_52_out), .oe(and_53_out), .clk(Reloj), .din(or_1_out),
    .dout(ram_16_dout), .clr(Limpiar));
  assign controlled_buffer_1_out = and_42_out ? ram_13_dout : 64'bz;  // Controlled_Buffer controlled_buffer_14
  assign controlled_buffer_1_out = and_43_out ? ram_14_dout : 64'bz;  // Controlled_Buffer controlled_buffer_15
  assign controlled_buffer_1_out = and_44_out ? ram_15_dout : 64'bz;  // Controlled_Buffer controlled_buffer_16
  assign controlled_buffer_1_out = and_45_out ? ram_16_dout : 64'bz;  // Controlled_Buffer controlled_buffer_17
  and and_54 (and_54_out, decoder_1_out1, and_2_out);
  and and_55 (and_55_out, decoder_1_out1, and_1_out);
  Decoder #(.enable("false"), .select(2)) decoder_4 (
    .out0(decoder_4_out0), .out1(decoder_4_out1), .out2(decoder_4_out2), .out3(decoder_4_out3),
    .sel(multiplexer_1_out_4));
  Decoder #(.enable("false"), .select(2)) decoder_5 (
    .out0(decoder_5_out0), .out1(decoder_5_out1), .out2(decoder_5_out2), .out3(decoder_5_out3),
    .sel(multiplexer_1_out_3));
  and and_56 (and_56_out, decoder_5_out0, decoder_4_out0);
  and and_57 (and_57_out, and_56_out, and_54_out);
  and and_58 (and_58_out, and_56_out, and_55_out);
  and and_59 (and_59_out, decoder_5_out0, decoder_4_out1);
  and and_60 (and_60_out, and_59_out, and_54_out);
  and and_61 (and_61_out, and_59_out, and_55_out);
  and and_62 (and_62_out, decoder_5_out0, decoder_4_out2);
  and and_63 (and_63_out, and_62_out, and_54_out);
  and and_64 (and_64_out, and_62_out, and_55_out);
  and and_65 (and_65_out, decoder_5_out0, decoder_4_out3);
  and and_66 (and_66_out, and_65_out, and_54_out);
  and and_67 (and_67_out, and_65_out, and_55_out);
  RAM #(.addrWidth(24), .asyncread("true"), .clearpin("true"), .dataWidth(64)) ram_17 (
    .addr(multiplexer_1_out_2), .we(and_57_out), .oe(and_58_out), .clk(Reloj), .din(or_1_out),
    .dout(ram_17_dout), .clr(Limpiar));
  RAM #(.addrWidth(24), .asyncread("true"), .clearpin("true"), .dataWidth(64)) ram_18 (
    .addr(multiplexer_1_out_2), .we(and_60_out), .oe(and_61_out), .clk(Reloj), .din(or_1_out),
    .dout(ram_18_dout), .clr(Limpiar));
  RAM #(.addrWidth(24), .asyncread("true"), .clearpin("true"), .dataWidth(64)) ram_19 (
    .addr(multiplexer_1_out_2), .we(and_63_out), .oe(and_64_out), .clk(Reloj), .din(or_1_out),
    .dout(ram_19_dout), .clr(Limpiar));
  RAM #(.addrWidth(24), .asyncread("true"), .clearpin("true"), .dataWidth(64)) ram_20 (
    .addr(multiplexer_1_out_2), .we(and_66_out), .oe(and_67_out), .clk(Reloj), .din(or_1_out),
    .dout(ram_20_dout), .clr(Limpiar));
  assign controlled_buffer_18_out = and_56_out ? ram_17_dout : 64'bz;  // Controlled_Buffer controlled_buffer_18
  assign controlled_buffer_18_out = and_59_out ? ram_18_dout : 64'bz;  // Controlled_Buffer controlled_buffer_19
  assign controlled_buffer_18_out = and_62_out ? ram_19_dout : 64'bz;  // Controlled_Buffer controlled_buffer_20
  assign controlled_buffer_18_out = and_65_out ? ram_20_dout : 64'bz;  // Controlled_Buffer controlled_buffer_21
  assign Doubleword = decoder_1_out1 ? controlled_buffer_18_out : 64'bz;  // Controlled_Buffer controlled_buffer_22
  and and_68 (and_68_out, decoder_5_out1, decoder_4_out0);
  and and_69 (and_69_out, decoder_5_out1, decoder_4_out1);
  and and_70 (and_70_out, decoder_5_out1, decoder_4_out2);
  and and_71 (and_71_out, decoder_5_out1, decoder_4_out3);
  and and_72 (and_72_out, and_68_out, and_54_out);
  and and_73 (and_73_out, and_68_out, and_55_out);
  and and_74 (and_74_out, and_69_out, and_54_out);
  and and_75 (and_75_out, and_69_out, and_55_out);
  and and_76 (and_76_out, and_70_out, and_54_out);
  and and_77 (and_77_out, and_70_out, and_55_out);
  and and_78 (and_78_out, and_71_out, and_54_out);
  and and_79 (and_79_out, and_71_out, and_55_out);
  RAM #(.addrWidth(24), .asyncread("true"), .clearpin("true"), .dataWidth(64)) ram_21 (
    .addr(multiplexer_1_out_2), .we(and_72_out), .oe(and_73_out), .clk(Reloj), .din(or_1_out),
    .dout(ram_21_dout), .clr(Limpiar));
  RAM #(.addrWidth(24), .asyncread("true"), .clearpin("true"), .dataWidth(64)) ram_22 (
    .addr(multiplexer_1_out_2), .we(and_74_out), .oe(and_75_out), .clk(Reloj), .din(or_1_out),
    .dout(ram_22_dout), .clr(Limpiar));
  RAM #(.addrWidth(24), .asyncread("true"), .clearpin("true"), .dataWidth(64)) ram_23 (
    .addr(multiplexer_1_out_2), .we(and_76_out), .oe(and_77_out), .clk(Reloj), .din(or_1_out),
    .dout(ram_23_dout), .clr(Limpiar));
  RAM #(.addrWidth(24), .asyncread("true"), .clearpin("true"), .dataWidth(64)) ram_24 (
    .addr(multiplexer_1_out_2), .we(and_78_out), .oe(and_79_out), .clk(Reloj), .din(or_1_out),
    .dout(ram_24_dout), .clr(Limpiar));
  assign controlled_buffer_18_out = and_68_out ? ram_21_dout : 64'bz;  // Controlled_Buffer controlled_buffer_23
  assign controlled_buffer_18_out = and_69_out ? ram_22_dout : 64'bz;  // Controlled_Buffer controlled_buffer_24
  assign controlled_buffer_18_out = and_70_out ? ram_23_dout : 64'bz;  // Controlled_Buffer controlled_buffer_25
  assign controlled_buffer_18_out = and_71_out ? ram_24_dout : 64'bz;  // Controlled_Buffer controlled_buffer_26
  and and_80 (and_80_out, decoder_5_out2, decoder_4_out0);
  and and_81 (and_81_out, decoder_5_out2, decoder_4_out1);
  and and_82 (and_82_out, decoder_5_out2, decoder_4_out2);
  and and_83 (and_83_out, decoder_5_out2, decoder_4_out3);
  RAM #(.addrWidth(24), .asyncread("true"), .clearpin("true"), .dataWidth(64)) ram_25 (
    .addr(multiplexer_1_out_2), .we(and_84_out), .oe(and_85_out), .clk(Reloj), .din(or_1_out),
    .dout(ram_25_dout), .clr(Limpiar));
  and and_84 (and_84_out, and_80_out, and_54_out);
  and and_85 (and_85_out, and_80_out, and_55_out);
  RAM #(.addrWidth(24), .asyncread("true"), .clearpin("true"), .dataWidth(64)) ram_26 (
    .addr(multiplexer_1_out_2), .we(and_86_out), .oe(and_87_out), .clk(Reloj), .din(or_1_out),
    .dout(ram_26_dout), .clr(Limpiar));
  and and_86 (and_86_out, and_81_out, and_54_out);
  and and_87 (and_87_out, and_81_out, and_55_out);
  RAM #(.addrWidth(24), .asyncread("true"), .clearpin("true"), .dataWidth(64)) ram_27 (
    .addr(multiplexer_1_out_2), .we(and_88_out), .oe(and_89_out), .clk(Reloj), .din(or_1_out),
    .dout(ram_27_dout), .clr(Limpiar));
  and and_88 (and_88_out, and_82_out, and_54_out);
  and and_89 (and_89_out, and_82_out, and_55_out);
  RAM #(.addrWidth(24), .asyncread("true"), .clearpin("true"), .dataWidth(64)) ram_28 (
    .addr(multiplexer_1_out_2), .we(and_90_out), .oe(and_91_out), .clk(Reloj), .din(or_1_out),
    .dout(ram_28_dout), .clr(Limpiar));
  and and_90 (and_90_out, and_83_out, and_54_out);
  and and_91 (and_91_out, and_83_out, and_55_out);
  and and_92 (and_92_out, decoder_5_out3, decoder_4_out0);
  assign controlled_buffer_18_out = and_80_out ? ram_25_dout : 64'bz;  // Controlled_Buffer controlled_buffer_27
  and and_93 (and_93_out, decoder_5_out3, decoder_4_out1);
  assign controlled_buffer_18_out = and_81_out ? ram_26_dout : 64'bz;  // Controlled_Buffer controlled_buffer_28
  and and_94 (and_94_out, decoder_5_out3, decoder_4_out2);
  assign controlled_buffer_18_out = and_82_out ? ram_27_dout : 64'bz;  // Controlled_Buffer controlled_buffer_29
  and and_95 (and_95_out, decoder_5_out3, decoder_4_out3);
  assign controlled_buffer_18_out = and_83_out ? ram_28_dout : 64'bz;  // Controlled_Buffer controlled_buffer_30
  and and_96 (and_96_out, and_92_out, and_54_out);
  and and_97 (and_97_out, and_92_out, and_55_out);
  and and_98 (and_98_out, and_93_out, and_54_out);
  and and_99 (and_99_out, and_93_out, and_55_out);
  and and_100 (and_100_out, and_94_out, and_54_out);
  and and_101 (and_101_out, and_94_out, and_55_out);
  and and_102 (and_102_out, and_95_out, and_54_out);
  and and_103 (and_103_out, and_95_out, and_55_out);
  RAM #(.addrWidth(24), .asyncread("true"), .clearpin("true"), .dataWidth(64)) ram_29 (
    .addr(multiplexer_1_out_2), .we(and_96_out), .oe(and_97_out), .clk(Reloj), .din(or_1_out),
    .dout(ram_29_dout), .clr(Limpiar));
  RAM #(.addrWidth(24), .asyncread("true"), .clearpin("true"), .dataWidth(64)) ram_30 (
    .addr(multiplexer_1_out_2), .we(and_98_out), .oe(and_99_out), .clk(Reloj), .din(or_1_out),
    .dout(ram_30_dout), .clr(Limpiar));
  RAM #(.addrWidth(24), .asyncread("true"), .clearpin("true"), .dataWidth(64)) ram_31 (
    .addr(multiplexer_1_out_2), .we(and_100_out), .oe(and_101_out), .clk(Reloj), .din(or_1_out),
    .dout(ram_31_dout), .clr(Limpiar));
  RAM #(.addrWidth(24), .asyncread("true"), .clearpin("true"), .dataWidth(64)) ram_32 (
    .addr(multiplexer_1_out_2), .we(and_102_out), .oe(and_103_out), .clk(Reloj), .din(or_1_out),
    .dout(ram_32_dout), .clr(Limpiar));
  assign controlled_buffer_18_out = and_92_out ? ram_29_dout : 64'bz;  // Controlled_Buffer controlled_buffer_31
  assign controlled_buffer_18_out = and_93_out ? ram_30_dout : 64'bz;  // Controlled_Buffer controlled_buffer_32
  assign controlled_buffer_18_out = and_94_out ? ram_31_dout : 64'bz;  // Controlled_Buffer controlled_buffer_33
  assign controlled_buffer_18_out = and_95_out ? ram_32_dout : 64'bz;  // Controlled_Buffer controlled_buffer_34

  // Notes on the sheet:
  //   Tamaño de memoria accesible
  //   Longitud de byte
  //   (Little Endian)
  //   (Big Endian)
  //   2 Gigabytes
  //   2 Gigabytes
endmodule

module Thirty_Two_Bit_RAM_Contender (
  input  Reiniciar,
  input  Reloj,
  input  Solicitar_A,
  input  Escribir_A,
  input  [31:0] Direccion_A,
  input  [31:0] Entrada_A,
  input  Solicitar_B,
  input  Escribir_B,
  input  [31:0] Direccion_B,
  input  [31:0] Entrada_B,
  output Atendiendo_B,
  output Escribir,
  output [31:0] Direccion,
  output [31:0] Entrada
);

  wire random_1_out;
  wire [1:0] bit_extender_1_out, bit_extender_2_out, Solicitantes;

  assign bit_extender_1_out = {{1{1'b0}}, Solicitar_A};  // Bit_Extender bit_extender_1
  assign bit_extender_2_out = {{1{1'b0}}, Solicitar_B};  // Bit_Extender bit_extender_2
  Random #(.width(1)) random_1 (.clr(Reiniciar), .next(1'b1), .clk(Reloj), .out(random_1_out));
  Adder #(.width(2)) adder_1 (.a(bit_extender_1_out), .b(bit_extender_2_out), .out(Solicitantes));  // open: cin, cout
  Multiplexer multiplexer_1 (.in0(Escribir_A), .in1(Escribir_B), .out(Escribir), .sel(Atendiendo_B));
  Multiplexer #(.width(32)) multiplexer_2 (.in0(Direccion_A), .in1(Direccion_B), .out(Direccion), .sel(Atendiendo_B));
  Multiplexer #(.width(32)) multiplexer_3 (.in0(Entrada_A), .in1(Entrada_B), .out(Entrada), .sel(Atendiendo_B));
  Multiplexer #(.select(2)) multiplexer_4 (
    .in0(random_1_out), .in1(Solicitar_B), .in2(random_1_out), .in3(random_1_out), .out(Atendiendo_B),
    .sel(Solicitantes));

  // Other names for the same wires on the sheet: Solicitante_Atendido = Atendiendo_B
endmodule

module Thirty_Two_Bit_Divisor (
  input  [31:0] Dividendo,
  input  [31:0] Divisor,
  input  Con_Signo,
  output Overflow,
  output [31:0] Cociente,
  output [31:0] Residuo
);

  wire adder_3_cout, bitselector_1_out, bitselector_2_out, C00, C01, C02, C03, C04, C05, C06, C07, C08, C09,
       C10, C11, C12, C13, C14, C15, C16, C17, C18, C19, C20, C21, C22, C23, C24, C25, C26, C27, C28, C29,
       C30, C31, Cociente_No_Representable, comparator_1_lt, comparator_2_lt, comparator_3_lt,
       comparator_4_lt, comparator_5_lt, comparator_6_lt, comparator_7_lt, comparator_8_lt, comparator_9_lt,
       comparator_10_lt, comparator_11_lt, comparator_12_lt, comparator_13_lt, comparator_14_lt,
       comparator_15_lt, comparator_16_lt, comparator_17_lt, comparator_18_lt, comparator_19_lt,
       comparator_20_lt, comparator_21_lt, comparator_22_lt, comparator_23_lt, comparator_24_lt,
       comparator_25_lt, comparator_26_lt, comparator_27_lt, comparator_28_lt, comparator_29_lt,
       comparator_30_lt, comparator_31_lt, comparator_32_lt, comparator_33_eq, Dividendo_Negativo,
       Divisor_Negativo, Overflow_Cociente, xor_1_out;
  wire [31:0] adder_1_out, adder_2_out, adder_3_out, adder_4_out, not_1_out, not_2_out, not_35_out,
       not_36_out, Valor_Absoluto_Dividendo, Valor_Absoluto_Divisor, Valor_Absoluto_Residuo;
  wire [62:0] P01, P02, P03, P04, P05, P06, P07, P08, P09, P10, P11, P12, P13, P14, P15, P16, P17, P18, P19,
       P20, P21, P22, P23, P24, P25, P26, P27, P28, P29, P30, P31, P32, R00, R01, R02, R03, R04, R05, R06,
       R07, R08, R09, R10, R11, R12, R13, R14, R15, R16, R17, R18, R19, R20, R21, R22, R23, R24, R25, R26,
       R27, R28, R29, R30, R31, R32, subtractor_1_out, subtractor_2_out, subtractor_3_out, subtractor_4_out,
       subtractor_5_out, subtractor_6_out, subtractor_7_out, subtractor_8_out, subtractor_9_out,
       subtractor_10_out, subtractor_11_out, subtractor_12_out, subtractor_13_out, subtractor_14_out,
       subtractor_15_out, subtractor_16_out, subtractor_17_out, subtractor_18_out, subtractor_19_out,
       subtractor_20_out, subtractor_21_out, subtractor_22_out, subtractor_23_out, subtractor_24_out,
       subtractor_25_out, subtractor_26_out, subtractor_27_out, subtractor_28_out, subtractor_29_out,
       subtractor_30_out, subtractor_31_out, subtractor_32_out;

  assign not_1_out = ~Dividendo;  // NOT_Gate not_1, 32 bits wide
  assign not_2_out = ~Divisor;  // NOT_Gate not_2, 32 bits wide
  Comparator #(.mode("unsigned"), .width(63)) comparator_1 (.a(R32), .b(P32), .lt(comparator_1_lt));  // open: gt, eq
  Subtractor #(.width(63)) subtractor_1 (.a(R32), .b(P32), .out(subtractor_1_out), .bin(1'b0));  // open: bout
  Comparator #(.mode("unsigned"), .width(63)) comparator_2 (.a(R31), .b(P31), .lt(comparator_2_lt));  // open: gt, eq
  Subtractor #(.width(63)) subtractor_2 (.a(R31), .b(P31), .out(subtractor_2_out), .bin(1'b0));  // open: bout
  Comparator #(.mode("unsigned"), .width(63)) comparator_3 (.a(R30), .b(P30), .lt(comparator_3_lt));  // open: gt, eq
  Subtractor #(.width(63)) subtractor_3 (.a(R30), .b(P30), .out(subtractor_3_out), .bin(1'b0));  // open: bout
  Comparator #(.mode("unsigned"), .width(63)) comparator_4 (.a(R29), .b(P29), .lt(comparator_4_lt));  // open: gt, eq
  Subtractor #(.width(63)) subtractor_4 (.a(R29), .b(P29), .out(subtractor_4_out), .bin(1'b0));  // open: bout
  Comparator #(.mode("unsigned"), .width(63)) comparator_5 (.a(R28), .b(P28), .lt(comparator_5_lt));  // open: gt, eq
  Subtractor #(.width(63)) subtractor_5 (.a(R28), .b(P28), .out(subtractor_5_out), .bin(1'b0));  // open: bout
  Comparator #(.mode("unsigned"), .width(63)) comparator_6 (.a(R27), .b(P27), .lt(comparator_6_lt));  // open: gt, eq
  Subtractor #(.width(63)) subtractor_6 (.a(R27), .b(P27), .out(subtractor_6_out), .bin(1'b0));  // open: bout
  Comparator #(.mode("unsigned"), .width(63)) comparator_7 (.a(R26), .b(P26), .lt(comparator_7_lt));  // open: gt, eq
  Subtractor #(.width(63)) subtractor_7 (.a(R26), .b(P26), .out(subtractor_7_out), .bin(1'b0));  // open: bout
  Comparator #(.mode("unsigned"), .width(63)) comparator_8 (.a(R25), .b(P25), .lt(comparator_8_lt));  // open: gt, eq
  Subtractor #(.width(63)) subtractor_8 (.a(R25), .b(P25), .out(subtractor_8_out), .bin(1'b0));  // open: bout
  Comparator #(.mode("unsigned"), .width(63)) comparator_9 (.a(R24), .b(P24), .lt(comparator_9_lt));  // open: gt, eq
  Subtractor #(.width(63)) subtractor_9 (.a(R24), .b(P24), .out(subtractor_9_out), .bin(1'b0));  // open: bout
  Comparator #(.mode("unsigned"), .width(63)) comparator_10 (.a(R23), .b(P23), .lt(comparator_10_lt));  // open: gt, eq
  Subtractor #(.width(63)) subtractor_10 (.a(R23), .b(P23), .out(subtractor_10_out), .bin(1'b0));  // open: bout
  Comparator #(.mode("unsigned"), .width(63)) comparator_11 (.a(R22), .b(P22), .lt(comparator_11_lt));  // open: gt, eq
  Subtractor #(.width(63)) subtractor_11 (.a(R22), .b(P22), .out(subtractor_11_out), .bin(1'b0));  // open: bout
  Comparator #(.mode("unsigned"), .width(63)) comparator_12 (.a(R21), .b(P21), .lt(comparator_12_lt));  // open: gt, eq
  Subtractor #(.width(63)) subtractor_12 (.a(R21), .b(P21), .out(subtractor_12_out), .bin(1'b0));  // open: bout
  Comparator #(.mode("unsigned"), .width(63)) comparator_13 (.a(R20), .b(P20), .lt(comparator_13_lt));  // open: gt, eq
  Subtractor #(.width(63)) subtractor_13 (.a(R20), .b(P20), .out(subtractor_13_out), .bin(1'b0));  // open: bout
  Comparator #(.mode("unsigned"), .width(63)) comparator_14 (.a(R19), .b(P19), .lt(comparator_14_lt));  // open: gt, eq
  Subtractor #(.width(63)) subtractor_14 (.a(R19), .b(P19), .out(subtractor_14_out), .bin(1'b0));  // open: bout
  Comparator #(.mode("unsigned"), .width(63)) comparator_15 (.a(R18), .b(P18), .lt(comparator_15_lt));  // open: gt, eq
  Subtractor #(.width(63)) subtractor_15 (.a(R18), .b(P18), .out(subtractor_15_out), .bin(1'b0));  // open: bout
  Comparator #(.mode("unsigned"), .width(63)) comparator_16 (.a(R17), .b(P17), .lt(comparator_16_lt));  // open: gt, eq
  Subtractor #(.width(63)) subtractor_16 (.a(R17), .b(P17), .out(subtractor_16_out), .bin(1'b0));  // open: bout
  Comparator #(.mode("unsigned"), .width(63)) comparator_17 (.a(R16), .b(P16), .lt(comparator_17_lt));  // open: gt, eq
  Subtractor #(.width(63)) subtractor_17 (.a(R16), .b(P16), .out(subtractor_17_out), .bin(1'b0));  // open: bout
  Comparator #(.mode("unsigned"), .width(63)) comparator_18 (.a(R15), .b(P15), .lt(comparator_18_lt));  // open: gt, eq
  Subtractor #(.width(63)) subtractor_18 (.a(R15), .b(P15), .out(subtractor_18_out), .bin(1'b0));  // open: bout
  Comparator #(.mode("unsigned"), .width(63)) comparator_19 (.a(R14), .b(P14), .lt(comparator_19_lt));  // open: gt, eq
  Subtractor #(.width(63)) subtractor_19 (.a(R14), .b(P14), .out(subtractor_19_out), .bin(1'b0));  // open: bout
  Comparator #(.mode("unsigned"), .width(63)) comparator_20 (.a(R13), .b(P13), .lt(comparator_20_lt));  // open: gt, eq
  Subtractor #(.width(63)) subtractor_20 (.a(R13), .b(P13), .out(subtractor_20_out), .bin(1'b0));  // open: bout
  Comparator #(.mode("unsigned"), .width(63)) comparator_21 (.a(R12), .b(P12), .lt(comparator_21_lt));  // open: gt, eq
  Subtractor #(.width(63)) subtractor_21 (.a(R12), .b(P12), .out(subtractor_21_out), .bin(1'b0));  // open: bout
  Comparator #(.mode("unsigned"), .width(63)) comparator_22 (.a(R11), .b(P11), .lt(comparator_22_lt));  // open: gt, eq
  Subtractor #(.width(63)) subtractor_22 (.a(R11), .b(P11), .out(subtractor_22_out), .bin(1'b0));  // open: bout
  Comparator #(.mode("unsigned"), .width(63)) comparator_23 (.a(R10), .b(P10), .lt(comparator_23_lt));  // open: gt, eq
  Subtractor #(.width(63)) subtractor_23 (.a(R10), .b(P10), .out(subtractor_23_out), .bin(1'b0));  // open: bout
  Comparator #(.mode("unsigned"), .width(63)) comparator_24 (.a(R09), .b(P09), .lt(comparator_24_lt));  // open: gt, eq
  Subtractor #(.width(63)) subtractor_24 (.a(R09), .b(P09), .out(subtractor_24_out), .bin(1'b0));  // open: bout
  Comparator #(.mode("unsigned"), .width(63)) comparator_25 (.a(R08), .b(P08), .lt(comparator_25_lt));  // open: gt, eq
  Subtractor #(.width(63)) subtractor_25 (.a(R08), .b(P08), .out(subtractor_25_out), .bin(1'b0));  // open: bout
  Comparator #(.mode("unsigned"), .width(63)) comparator_26 (.a(R07), .b(P07), .lt(comparator_26_lt));  // open: gt, eq
  Subtractor #(.width(63)) subtractor_26 (.a(R07), .b(P07), .out(subtractor_26_out), .bin(1'b0));  // open: bout
  Comparator #(.mode("unsigned"), .width(63)) comparator_27 (.a(R06), .b(P06), .lt(comparator_27_lt));  // open: gt, eq
  Subtractor #(.width(63)) subtractor_27 (.a(R06), .b(P06), .out(subtractor_27_out), .bin(1'b0));  // open: bout
  Comparator #(.mode("unsigned"), .width(63)) comparator_28 (.a(R05), .b(P05), .lt(comparator_28_lt));  // open: gt, eq
  Subtractor #(.width(63)) subtractor_28 (.a(R05), .b(P05), .out(subtractor_28_out), .bin(1'b0));  // open: bout
  Comparator #(.mode("unsigned"), .width(63)) comparator_29 (.a(R04), .b(P04), .lt(comparator_29_lt));  // open: gt, eq
  Subtractor #(.width(63)) subtractor_29 (.a(R04), .b(P04), .out(subtractor_29_out), .bin(1'b0));  // open: bout
  Comparator #(.mode("unsigned"), .width(63)) comparator_30 (.a(R03), .b(P03), .lt(comparator_30_lt));  // open: gt, eq
  Subtractor #(.width(63)) subtractor_30 (.a(R03), .b(P03), .out(subtractor_30_out), .bin(1'b0));  // open: bout
  Comparator #(.mode("unsigned"), .width(63)) comparator_31 (.a(R02), .b(P02), .lt(comparator_31_lt));  // open: gt, eq
  Subtractor #(.width(63)) subtractor_31 (.a(R02), .b(P02), .out(subtractor_31_out), .bin(1'b0));  // open: bout
  Comparator #(.mode("unsigned"), .width(63)) comparator_32 (.a(R01), .b(P01), .lt(comparator_32_lt));  // open: gt, eq
  Subtractor #(.width(63)) subtractor_32 (.a(R01), .b(P01), .out(subtractor_32_out), .bin(1'b0));  // open: bout
  BitSelector #(.width(32)) bitselector_1 (.in(Dividendo), .out(bitselector_1_out), .sel({5{1'b1}}));
  BitSelector #(.width(32)) bitselector_2 (.in(Divisor), .out(bitselector_2_out), .sel({5{1'b1}}));
  Adder #(.width(32)) adder_1 (.a(not_1_out), .b(32'h1), .out(adder_1_out), .cin(1'b0));  // open: cout
  Adder #(.width(32)) adder_2 (.a(not_2_out), .b(32'h1), .out(adder_2_out), .cin(1'b0));  // open: cout
  and and_1 (Overflow_Cociente, adder_3_cout, Con_Signo);
  not not_3 (C31, comparator_1_lt);
  Multiplexer #(.width(63)) multiplexer_1 (.in0(subtractor_1_out), .in1(R32), .out(R31), .sel(comparator_1_lt));
  not not_4 (C30, comparator_2_lt);
  Multiplexer #(.width(63)) multiplexer_2 (.in0(subtractor_2_out), .in1(R31), .out(R30), .sel(comparator_2_lt));
  not not_5 (C29, comparator_3_lt);
  Multiplexer #(.width(63)) multiplexer_3 (.in0(subtractor_3_out), .in1(R30), .out(R29), .sel(comparator_3_lt));
  not not_6 (C28, comparator_4_lt);
  Multiplexer #(.width(63)) multiplexer_4 (.in0(subtractor_4_out), .in1(R29), .out(R28), .sel(comparator_4_lt));
  not not_7 (C27, comparator_5_lt);
  Multiplexer #(.width(63)) multiplexer_5 (.in0(subtractor_5_out), .in1(R28), .out(R27), .sel(comparator_5_lt));
  not not_8 (C26, comparator_6_lt);
  Multiplexer #(.width(63)) multiplexer_6 (.in0(subtractor_6_out), .in1(R27), .out(R26), .sel(comparator_6_lt));
  not not_9 (C25, comparator_7_lt);
  Multiplexer #(.width(63)) multiplexer_7 (.in0(subtractor_7_out), .in1(R26), .out(R25), .sel(comparator_7_lt));
  not not_10 (C24, comparator_8_lt);
  Multiplexer #(.width(63)) multiplexer_8 (.in0(subtractor_8_out), .in1(R25), .out(R24), .sel(comparator_8_lt));
  not not_11 (C23, comparator_9_lt);
  Multiplexer #(.width(63)) multiplexer_9 (.in0(subtractor_9_out), .in1(R24), .out(R23), .sel(comparator_9_lt));
  not not_12 (C22, comparator_10_lt);
  Multiplexer #(.width(63)) multiplexer_10 (.in0(subtractor_10_out), .in1(R23), .out(R22), .sel(comparator_10_lt));
  not not_13 (C21, comparator_11_lt);
  Multiplexer #(.width(63)) multiplexer_11 (.in0(subtractor_11_out), .in1(R22), .out(R21), .sel(comparator_11_lt));
  not not_14 (C20, comparator_12_lt);
  Multiplexer #(.width(63)) multiplexer_12 (.in0(subtractor_12_out), .in1(R21), .out(R20), .sel(comparator_12_lt));
  not not_15 (C19, comparator_13_lt);
  Multiplexer #(.width(63)) multiplexer_13 (.in0(subtractor_13_out), .in1(R20), .out(R19), .sel(comparator_13_lt));
  not not_16 (C18, comparator_14_lt);
  Multiplexer #(.width(63)) multiplexer_14 (.in0(subtractor_14_out), .in1(R19), .out(R18), .sel(comparator_14_lt));
  not not_17 (C17, comparator_15_lt);
  Multiplexer #(.width(63)) multiplexer_15 (.in0(subtractor_15_out), .in1(R18), .out(R17), .sel(comparator_15_lt));
  not not_18 (C16, comparator_16_lt);
  Multiplexer #(.width(63)) multiplexer_16 (.in0(subtractor_16_out), .in1(R17), .out(R16), .sel(comparator_16_lt));
  not not_19 (C15, comparator_17_lt);
  Multiplexer #(.width(63)) multiplexer_17 (.in0(subtractor_17_out), .in1(R16), .out(R15), .sel(comparator_17_lt));
  not not_20 (C14, comparator_18_lt);
  Multiplexer #(.width(63)) multiplexer_18 (.in0(subtractor_18_out), .in1(R15), .out(R14), .sel(comparator_18_lt));
  not not_21 (C13, comparator_19_lt);
  Multiplexer #(.width(63)) multiplexer_19 (.in0(subtractor_19_out), .in1(R14), .out(R13), .sel(comparator_19_lt));
  not not_22 (C12, comparator_20_lt);
  Multiplexer #(.width(63)) multiplexer_20 (.in0(subtractor_20_out), .in1(R13), .out(R12), .sel(comparator_20_lt));
  not not_23 (C11, comparator_21_lt);
  Multiplexer #(.width(63)) multiplexer_21 (.in0(subtractor_21_out), .in1(R12), .out(R11), .sel(comparator_21_lt));
  not not_24 (C10, comparator_22_lt);
  Multiplexer #(.width(63)) multiplexer_22 (.in0(subtractor_22_out), .in1(R11), .out(R10), .sel(comparator_22_lt));
  not not_25 (C09, comparator_23_lt);
  Multiplexer #(.width(63)) multiplexer_23 (.in0(subtractor_23_out), .in1(R10), .out(R09), .sel(comparator_23_lt));
  not not_26 (C08, comparator_24_lt);
  Multiplexer #(.width(63)) multiplexer_24 (.in0(subtractor_24_out), .in1(R09), .out(R08), .sel(comparator_24_lt));
  not not_27 (C07, comparator_25_lt);
  Multiplexer #(.width(63)) multiplexer_25 (.in0(subtractor_25_out), .in1(R08), .out(R07), .sel(comparator_25_lt));
  not not_28 (C06, comparator_26_lt);
  Multiplexer #(.width(63)) multiplexer_26 (.in0(subtractor_26_out), .in1(R07), .out(R06), .sel(comparator_26_lt));
  not not_29 (C05, comparator_27_lt);
  Multiplexer #(.width(63)) multiplexer_27 (.in0(subtractor_27_out), .in1(R06), .out(R05), .sel(comparator_27_lt));
  not not_30 (C04, comparator_28_lt);
  Multiplexer #(.width(63)) multiplexer_28 (.in0(subtractor_28_out), .in1(R05), .out(R04), .sel(comparator_28_lt));
  not not_31 (C03, comparator_29_lt);
  Multiplexer #(.width(63)) multiplexer_29 (.in0(subtractor_29_out), .in1(R04), .out(R03), .sel(comparator_29_lt));
  not not_32 (C02, comparator_30_lt);
  Multiplexer #(.width(63)) multiplexer_30 (.in0(subtractor_30_out), .in1(R03), .out(R02), .sel(comparator_30_lt));
  not not_33 (C01, comparator_31_lt);
  Multiplexer #(.width(63)) multiplexer_31 (.in0(subtractor_31_out), .in1(R02), .out(R01), .sel(comparator_31_lt));
  not not_34 (C00, comparator_32_lt);
  Multiplexer #(.width(63)) multiplexer_32 (.in0(subtractor_32_out), .in1(R01), .out(R00), .sel(comparator_32_lt));
  and and_2 (Dividendo_Negativo, Con_Signo, bitselector_1_out);
  and and_3 (Divisor_Negativo, Con_Signo, bitselector_2_out);
  Multiplexer #(.width(32)) multiplexer_33 (
    .in0(Dividendo), .in1(adder_1_out), .out(Valor_Absoluto_Dividendo), .sel(Dividendo_Negativo));
  Multiplexer #(.width(32)) multiplexer_34 (
    .in0(Divisor), .in1(adder_2_out), .out(Valor_Absoluto_Divisor), .sel(Divisor_Negativo));
  assign not_35_out = ~{C31, C30, C29, C28, C27, C26, C25, C24, C23, C22, C21, C20, C19, C18, C17, C16, C15, C14, C13, C12, C11, C10, C09, C08, C07, C06, C05, C04, C03, C02, C01, C00};  // NOT_Gate not_35, 32 bits wide
  assign not_36_out = ~Valor_Absoluto_Residuo;  // NOT_Gate not_36, 32 bits wide
  Adder #(.width(32)) adder_3 (.a(not_35_out), .b(32'h1), .out(adder_3_out), .cin(1'b0), .cout(adder_3_cout));
  xor xor_1 (xor_1_out, Divisor_Negativo, Dividendo_Negativo);
  Adder #(.width(32)) adder_4 (.a(not_36_out), .b(32'h1), .out(adder_4_out), .cin(1'b0));  // open: cout
  assign P01 = {{31{1'b0}}, Valor_Absoluto_Divisor};  // Bit_Extender bit_extender_1
  Multiplexer #(.width(32)) multiplexer_35 (
    .in0({C31, C30, C29, C28, C27, C26, C25, C24, C23, C22, C21, C20, C19, C18, C17, C16, C15, C14, C13, C12, C11, C10, C09, C08, C07, C06, C05, C04, C03, C02, C01, C00}),
    .in1(adder_3_out), .out(Cociente), .sel(xor_1_out));
  Multiplexer #(.width(32)) multiplexer_36 (
    .in0(Valor_Absoluto_Residuo), .in1(adder_4_out), .out(Residuo), .sel(Dividendo_Negativo));
  Shifter #(.width(63)) shifter_1 (.in(P01), .\dist (6'b011111), .out(P32));
  Shifter #(.width(63)) shifter_2 (.in(P01), .\dist (6'b011110), .out(P31));
  Shifter #(.width(63)) shifter_3 (.in(P01), .\dist (6'b011101), .out(P30));
  Shifter #(.width(63)) shifter_4 (.in(P01), .\dist (6'b011100), .out(P29));
  Shifter #(.width(63)) shifter_5 (.in(P01), .\dist (6'b011011), .out(P28));
  Shifter #(.width(63)) shifter_6 (.in(P01), .\dist (6'b011010), .out(P27));
  Shifter #(.width(63)) shifter_7 (.in(P01), .\dist (6'b011001), .out(P26));
  Shifter #(.width(63)) shifter_8 (.in(P01), .\dist (6'b011000), .out(P25));
  Shifter #(.width(63)) shifter_9 (.in(P01), .\dist (6'b010111), .out(P24));
  Shifter #(.width(63)) shifter_10 (.in(P01), .\dist (6'b010110), .out(P23));
  Shifter #(.width(63)) shifter_11 (.in(P01), .\dist (6'b010101), .out(P22));
  Shifter #(.width(63)) shifter_12 (.in(P01), .\dist (6'b010100), .out(P21));
  Shifter #(.width(63)) shifter_13 (.in(P01), .\dist (6'b010011), .out(P20));
  Shifter #(.width(63)) shifter_14 (.in(P01), .\dist (6'b010010), .out(P19));
  Shifter #(.width(63)) shifter_15 (.in(P01), .\dist (6'b010001), .out(P18));
  Shifter #(.width(63)) shifter_16 (.in(P01), .\dist (6'b010000), .out(P17));
  Shifter #(.width(63)) shifter_17 (.in(P01), .\dist (6'b001111), .out(P16));
  Shifter #(.width(63)) shifter_18 (.in(P01), .\dist (6'b001110), .out(P15));
  Shifter #(.width(63)) shifter_19 (.in(P01), .\dist (6'b001101), .out(P14));
  Shifter #(.width(63)) shifter_20 (.in(P01), .\dist (6'b001100), .out(P13));
  Shifter #(.width(63)) shifter_21 (.in(P01), .\dist (6'b001011), .out(P12));
  Shifter #(.width(63)) shifter_22 (.in(P01), .\dist (6'b001010), .out(P11));
  Shifter #(.width(63)) shifter_23 (.in(P01), .\dist (6'b001001), .out(P10));
  Shifter #(.width(63)) shifter_24 (.in(P01), .\dist (6'b001000), .out(P09));
  Shifter #(.width(63)) shifter_25 (.in(P01), .\dist (6'b000111), .out(P08));
  Shifter #(.width(63)) shifter_26 (.in(P01), .\dist (6'b000110), .out(P07));
  Shifter #(.width(63)) shifter_27 (.in(P01), .\dist (6'b000101), .out(P06));
  Shifter #(.width(63)) shifter_28 (.in(P01), .\dist (6'b000100), .out(P05));
  Shifter #(.width(63)) shifter_29 (.in(P01), .\dist (6'b000011), .out(P04));
  Shifter #(.width(63)) shifter_30 (.in(P01), .\dist (6'b000010), .out(P03));
  Shifter #(.width(63)) shifter_31 (.in(P01), .\dist (6'b000001), .out(P02));
  Comparator #(.mode("unsigned"), .width(32)) comparator_33 (
    .a(Cociente), .b(32'h80000000), .eq(comparator_33_eq));  // open: gt, lt
  and and_4 (Cociente_No_Representable, Divisor_Negativo, comparator_33_eq);
  Bit_Extender #(.in_width(63), .out_width(32)) bit_extender_2 (.in(R00), .out(Valor_Absoluto_Residuo));
  or or_1 (Overflow, Cociente_No_Representable, Overflow_Cociente);
  assign R32 = {{31{1'b0}}, Valor_Absoluto_Dividendo};  // Bit_Extender bit_extender_3

  // Other names for the same wires on the sheet: Valor_Absoluto_Cociente[31:0] = {C31, C30, C29, C28, C27, C26, C25, C24, C23, C22, C21, C20, C19, C18, C17, C16, C15, C14, C13, C12, C11, C10, C09, C08, C07, C06, C05, C04, C03, C02, C01, C00}

  // Notes on the sheet:
  //   División entera
  //   Entradas y Salidas
  //   Banderas de Estado
  //   Conversiones de signo
endmodule

// VHDL entity MIPS_Control_Hazard_Solver, as the project stores it:
LIBRARY ieee;
USE ieee.std_logic_1164.all;

ENTITY MIPS_Control_Hazard_Solver IS
  	PORT (
------------------------------------------------------------------------------
-- Entradas
	Reloj               : IN  std_logic; -- Reloj interno del procesador
	Lectura_Pendiente   : IN  std_logic; -- Si hay una lectura pendiente de MEM desde EX
	EX_Salto_Pendiente  : IN  std_logic; -- Si hay un salto pendiente de WB desde EX
	MEM_Salto_Pendiente : IN  std_logic; -- (...) WB desde MEM
	   
------------------------------------------------------------------------------
-- Salidas
	IF_Dormir           : OUT std_logic; -- Si se pausa la ejecución de IF
	ID_Dormir           : OUT std_logic; -- (...) de ID
	EX_Dormir           : OUT std_logic; -- (...) de EX
	MEM_Dormir          : OUT std_logic; -- (...) de MEM
	WB_Dormir           : OUT std_logic; -- (...) de WB
	
	IF_Reiniciar        : OUT std_logic; -- Si se reinicia el caché de la instrucción en IF (asincrónicamente)
	ID_Reiniciar        : OUT std_logic; -- (...) en ID
	EX_Reiniciar        : OUT std_logic; -- (...) en EX
	MEM_Reiniciar       : OUT std_logic; -- (...) en MEM
	WB_Reiniciar        : OUT std_logic -- (...) en WB
	);
END MIPS_Control_Hazard_Solver;

--------------------------------------------------------------------------------
-- Implementación
--------------------------------------------------------------------------------

ARCHITECTURE Solver_Implementation OF MIPS_Control_Hazard_Solver IS
BEGIN
	process(MEM_Salto_Pendiente, EX_Salto_Pendiente, Lectura_Pendiente, Reloj)
	begin
		-- Si hay un salto pendiente en MEM para WB, invalidar
		-- las instrucciones previas (pero dejar IF hábil)
		if (MEM_Salto_Pendiente = '1') then
			report "MEM Salto Pendiente";
			if rising_edge(Reloj) then
				-- Fijar ID, EX y MEM
				IF_Dormir <= '0';
				ID_Dormir <= '1';
				EX_Dormir <= '1';
				MEM_Dormir <= '1';
				WB_Dormir <= '0';
				-- Conservando sus valores
				IF_Reiniciar <= '0';
				ID_Reiniciar <= '0';
				EX_Reiniciar <= '0';
				MEM_Reiniciar <= '0';
				WB_Reiniciar <= '0';
	
			elsif falling_edge(Reloj) then
				-- Liberar todas las fases
				IF_Dormir <= '0';
				ID_Dormir <= '0';
				EX_Dormir <= '0';
				MEM_Dormir <= '0';
				WB_Dormir <= '0';
				-- Anulando ID, EX y MEM
				IF_Reiniciar <= '0';
				ID_Reiniciar <= '1';
				EX_Reiniciar <= '1';
				MEM_Reiniciar <= '1';
				WB_Reiniciar <= '0';
			end if;
	
		-- Sino, si hay un salto pendiente en EX para WB,
		-- invalidar las instrucciones previas
		elsif (EX_Salto_Pendiente = '1') then
			report "EX Salto Pendiente";
			if rising_edge(Reloj) then
				-- Fijar IF, ID y EX
				IF_Dormir <= '1';
				ID_Dormir <= '1';
				EX_Dormir <= '1';
				MEM_Dormir <= '0';
				WB_Dormir <= '0';
				-- Conservando sus valores
				IF_Reiniciar <= '0';
				ID_Reiniciar <= '0';
				EX_Reiniciar <= '0';
				MEM_Reiniciar <= '0';
				WB_Reiniciar <= '0';
	
			elsif falling_edge(Reloj) then
				-- Liberar todas las fases
				IF_Dormir <= '0';
				ID_Dormir <= '0';
				EX_Dormir <= '0';
				MEM_Dormir <= '0';
				WB_Dormir <= '0';
				-- Anulando IF, ID y EX
				IF_Reiniciar <= '1';
				ID_Reiniciar <= '1';
				EX_Reiniciar <= '1';
				MEM_Reiniciar <= '0';
				WB_Reiniciar <= '0';
			end if;
	
		-- Sino, si hay una lectura pendiente en EX para MEM,
		--  insertar una burbuja en EX
		elsif (Lectura_Pendiente = '1') then
			report "Lectura pendiente";
			if rising_edge(Reloj) then
				-- Fijar IF, ID y EX
				IF_Dormir <= '1';
				ID_Dormir <= '1';
				EX_Dormir <= '1';
				MEM_Dormir <= '0';
				WB_Dormir <= '0';
				-- Anular ninguna
				IF_Reiniciar <= '0';
				ID_Reiniciar <= '0';
				EX_Reiniciar <= '0';
				MEM_Reiniciar <= '0';
				WB_Reiniciar <= '0';
	
			elsif falling_edge(Reloj) then
				-- Liberar todas las fases
				IF_Dormir <= '0';
				ID_Dormir <= '0';
				EX_Dormir <= '0';
				MEM_Dormir <= '0';
				WB_Dormir <= '0';
				-- Anular únicamente la duplicada en EX
				IF_Reiniciar <= '0';
				ID_Reiniciar <= '0';
				EX_Reiniciar <= '1';
				MEM_Reiniciar <= '0';
				WB_Reiniciar <= '0';
			end if;
		-- Sino, no bloquear ni anular ninguna instrucción
		else
			report "Búcle normal";
			-- Fijar ninguna
			IF_Dormir <= '0';
			ID_Dormir <= '0';
			EX_Dormir <= '0';
			MEM_Dormir <= '0';
			WB_Dormir <= '0';
			-- Anular ninguna
			IF_Reiniciar <= '0';
			ID_Reiniciar <= '0';
			EX_Reiniciar <= '0';
			MEM_Reiniciar <= '0';
			WB_Reiniciar <= '0';
		end if;
	end process;
END Solver_Implementation;
